// Logisim project PotenciaBinaria.circ as structural Verilog: 42 circuits, main circuit mainPotencia
module mainPotencia (
  input  EXPONENTE,
  input  E2,
  input  E3,
  input  BASE,
  input  B2,
  input  B3,
  input  BITS_DE_CONTROL,
  input  in_8
);

  wire display_3_entradas_1_a, display_3_entradas_1_b, display_3_entradas_1_c, display_3_entradas_1_d,
       display_3_entradas_1_e, display_3_entradas_1_f, display_3_entradas_1_g, display_3_entradas_2_a,
       display_3_entradas_2_b, display_3_entradas_2_c, display_3_entradas_2_d, display_3_entradas_2_e,
       display_3_entradas_2_f, display_3_entradas_2_g, nucleo_de_la_potencia_1_out_8,
       nucleo_de_la_potencia_1_out_9, nucleo_de_la_potencia_1_out_10, nucleo_de_la_potencia_1_out_11,
       nucleo_de_la_potencia_1_out_12, nucleo_de_la_potencia_1_out_13, nucleo_de_la_potencia_1_out_14,
       nucleo_de_la_potencia_1_out_15, nucleo_de_la_potencia_1_out_16, nucleo_de_la_potencia_1_out_17,
       nucleo_de_la_potencia_1_out_18, nucleo_de_la_potencia_1_out_19, nucleo_de_la_potencia_1_out_20,
       nucleo_de_la_potencia_1_out_21, nucleo_de_la_potencia_1_out_22, nucleo_de_la_potencia_1_out_23,
       nucleo_de_la_potencia_1_out_24, nucleo_de_la_potencia_1_out_25, nucleo_de_la_potencia_1_out_26,
       nucleo_de_la_potencia_1_t, nucleo_de_los_displays_1_out_23, nucleo_de_los_displays_1_out_24,
       nucleo_de_los_displays_1_out_25, nucleo_de_los_displays_1_out_26, nucleo_de_los_displays_1_out_27,
       nucleo_de_los_displays_1_out_28, nucleo_de_los_displays_1_out_29, nucleo_de_los_displays_1_out_30,
       nucleo_de_los_displays_1_out_31, nucleo_de_los_displays_1_out_32, nucleo_de_los_displays_1_out_33,
       nucleo_de_los_displays_1_out_34, nucleo_de_los_displays_1_out_35, nucleo_de_los_displays_1_out_36,
       nucleo_de_los_displays_1_out_37, nucleo_de_los_displays_1_out_38, nucleo_de_los_displays_1_out_39,
       nucleo_de_los_displays_1_out_40, nucleo_de_los_displays_1_out_41, nucleo_de_los_displays_1_out_42,
       nucleo_de_los_displays_1_out_43, nucleo_de_los_displays_1_out_44, nucleo_de_los_displays_1_out_45,
       nucleo_de_los_displays_1_out_46, nucleo_de_los_displays_1_out_47, nucleo_de_los_displays_1_out_48,
       nucleo_de_los_displays_1_out_49, nucleo_de_los_displays_1_out_50, nucleo_de_los_displays_1_out_51,
       nucleo_de_los_displays_1_out_52, nucleo_de_los_displays_1_out_53, nucleo_de_los_displays_1_out_54,
       nucleo_de_los_displays_1_out_55, nucleo_de_los_displays_1_out_56, nucleo_de_los_displays_1_out_57,
       nucleo_de_los_displays_1_out_58, nucleo_de_los_displays_1_out_59, nucleo_de_los_displays_1_out_60,
       nucleo_de_los_displays_1_out_61, nucleo_de_los_displays_1_out_62, nucleo_de_los_displays_1_out_63,
       nucleo_de_los_displays_1_out_64, nucleo_de_los_displays_1_out_65, nucleo_de_los_displays_1_out_66,
       nucleo_de_los_displays_1_out_67, nucleo_de_los_displays_1_out_68, nucleo_de_los_displays_1_out_69,
       nucleo_de_los_displays_1_out_70, nucleo_de_los_displays_1_out_71;

  _7_Segment_Display u_7_segment_display_1 (
    .g(display_3_entradas_1_g), .f(display_3_entradas_1_f), .a(display_3_entradas_1_a),
    .b(display_3_entradas_1_b), .e(display_3_entradas_1_e), .d(display_3_entradas_1_d),
    .c(display_3_entradas_1_c));  // open: dp
  Display_3_Entradas display_3_entradas_1 (
    .E1(BASE), .E2(B2), .E3(B3), .a(display_3_entradas_1_a), .b(display_3_entradas_1_b),
    .c(display_3_entradas_1_c), .d(display_3_entradas_1_d), .e(display_3_entradas_1_e),
    .f(display_3_entradas_1_f), .g(display_3_entradas_1_g));
  Display_3_Entradas display_3_entradas_2 (
    .E1(EXPONENTE), .E2(E2), .E3(E3), .a(display_3_entradas_2_a), .b(display_3_entradas_2_b),
    .c(display_3_entradas_2_c), .d(display_3_entradas_2_d), .e(display_3_entradas_2_e),
    .f(display_3_entradas_2_f), .g(display_3_entradas_2_g));
  Nucleo_de_la_Potencia nucleo_de_la_potencia_1 (
    .EXPONENTE(EXPONENTE), .E2(E2), .E3(E3), .BASE(BASE), .B2(B2), .B3(B3), .T(nucleo_de_la_potencia_1_t),
    .out_8(nucleo_de_la_potencia_1_out_8), .out_19(nucleo_de_la_potencia_1_out_19),
    .out_23(nucleo_de_la_potencia_1_out_23), .out_9(nucleo_de_la_potencia_1_out_9),
    .out_10(nucleo_de_la_potencia_1_out_10), .out_11(nucleo_de_la_potencia_1_out_11),
    .out_12(nucleo_de_la_potencia_1_out_12), .out_13(nucleo_de_la_potencia_1_out_13),
    .out_14(nucleo_de_la_potencia_1_out_14), .out_15(nucleo_de_la_potencia_1_out_15),
    .out_16(nucleo_de_la_potencia_1_out_16), .out_17(nucleo_de_la_potencia_1_out_17),
    .out_18(nucleo_de_la_potencia_1_out_18), .out_20(nucleo_de_la_potencia_1_out_20),
    .out_21(nucleo_de_la_potencia_1_out_21), .out_22(nucleo_de_la_potencia_1_out_22),
    .out_24(nucleo_de_la_potencia_1_out_24), .out_25(nucleo_de_la_potencia_1_out_25),
    .out_26(nucleo_de_la_potencia_1_out_26));
  _7_Segment_Display u_7_segment_display_2 (
    .g(display_3_entradas_2_g), .f(display_3_entradas_2_f), .a(display_3_entradas_2_a),
    .b(display_3_entradas_2_b), .e(display_3_entradas_2_e), .d(display_3_entradas_2_d),
    .c(display_3_entradas_2_c));  // open: dp
  Nucleo_de_los_Displays nucleo_de_los_displays_1 (
    .in_1(nucleo_de_la_potencia_1_t), .in_2(nucleo_de_la_potencia_1_out_19),
    .in_3(nucleo_de_la_potencia_1_out_23), .in_4(nucleo_de_la_potencia_1_out_8),
    .in_5(nucleo_de_la_potencia_1_out_9), .in_6(nucleo_de_la_potencia_1_out_10),
    .in_7(nucleo_de_la_potencia_1_out_11), .in_8(nucleo_de_la_potencia_1_out_12),
    .in_9(nucleo_de_la_potencia_1_out_13), .in_10(nucleo_de_la_potencia_1_out_14),
    .in_11(nucleo_de_la_potencia_1_out_15), .in_12(nucleo_de_la_potencia_1_out_16),
    .in_13(nucleo_de_la_potencia_1_out_17), .in_14(nucleo_de_la_potencia_1_out_18),
    .in_15(nucleo_de_la_potencia_1_out_20), .in_16(nucleo_de_la_potencia_1_out_21),
    .in_17(nucleo_de_la_potencia_1_out_22), .in_18(nucleo_de_la_potencia_1_out_24),
    .in_19(nucleo_de_la_potencia_1_out_25), .in_20(nucleo_de_la_potencia_1_out_26), .in_21(BITS_DE_CONTROL),
    .out_23(nucleo_de_los_displays_1_out_23), .out_24(nucleo_de_los_displays_1_out_24),
    .out_25(nucleo_de_los_displays_1_out_25), .out_26(nucleo_de_los_displays_1_out_26),
    .out_27(nucleo_de_los_displays_1_out_27), .out_28(nucleo_de_los_displays_1_out_28),
    .out_29(nucleo_de_los_displays_1_out_29), .out_30(nucleo_de_los_displays_1_out_30),
    .out_31(nucleo_de_los_displays_1_out_31), .out_32(nucleo_de_los_displays_1_out_32),
    .out_33(nucleo_de_los_displays_1_out_33), .out_34(nucleo_de_los_displays_1_out_34),
    .out_35(nucleo_de_los_displays_1_out_35), .out_36(nucleo_de_los_displays_1_out_36),
    .out_37(nucleo_de_los_displays_1_out_37), .out_38(nucleo_de_los_displays_1_out_38),
    .out_39(nucleo_de_los_displays_1_out_39), .out_40(nucleo_de_los_displays_1_out_40),
    .out_41(nucleo_de_los_displays_1_out_41), .out_42(nucleo_de_los_displays_1_out_42),
    .out_43(nucleo_de_los_displays_1_out_43), .out_44(nucleo_de_los_displays_1_out_44),
    .out_45(nucleo_de_los_displays_1_out_45), .out_46(nucleo_de_los_displays_1_out_46),
    .out_47(nucleo_de_los_displays_1_out_47), .out_48(nucleo_de_los_displays_1_out_48),
    .out_49(nucleo_de_los_displays_1_out_49), .out_50(nucleo_de_los_displays_1_out_50),
    .out_51(nucleo_de_los_displays_1_out_51), .out_52(nucleo_de_los_displays_1_out_52),
    .out_53(nucleo_de_los_displays_1_out_53), .out_54(nucleo_de_los_displays_1_out_54),
    .out_55(nucleo_de_los_displays_1_out_55), .out_56(nucleo_de_los_displays_1_out_56),
    .out_57(nucleo_de_los_displays_1_out_57), .out_71(nucleo_de_los_displays_1_out_71),
    .out_70(nucleo_de_los_displays_1_out_70), .out_69(nucleo_de_los_displays_1_out_69),
    .out_68(nucleo_de_los_displays_1_out_68), .out_67(nucleo_de_los_displays_1_out_67),
    .out_66(nucleo_de_los_displays_1_out_66), .out_65(nucleo_de_los_displays_1_out_65),
    .out_64(nucleo_de_los_displays_1_out_64), .out_63(nucleo_de_los_displays_1_out_63),
    .out_62(nucleo_de_los_displays_1_out_62), .out_61(nucleo_de_los_displays_1_out_61),
    .out_60(nucleo_de_los_displays_1_out_60), .out_59(nucleo_de_los_displays_1_out_59),
    .out_58(nucleo_de_los_displays_1_out_58), .in_22(in_8));
  _7_Segment_Display u_7_segment_display_3 (
    .g(nucleo_de_los_displays_1_out_65), .f(nucleo_de_los_displays_1_out_66),
    .a(nucleo_de_los_displays_1_out_71), .b(nucleo_de_los_displays_1_out_70),
    .e(nucleo_de_los_displays_1_out_67), .d(nucleo_de_los_displays_1_out_68),
    .c(nucleo_de_los_displays_1_out_69));  // open: dp
  _7_Segment_Display u_7_segment_display_4 (
    .g(nucleo_de_los_displays_1_out_58), .f(nucleo_de_los_displays_1_out_59),
    .a(nucleo_de_los_displays_1_out_64), .b(nucleo_de_los_displays_1_out_63),
    .e(nucleo_de_los_displays_1_out_60), .d(nucleo_de_los_displays_1_out_61),
    .c(nucleo_de_los_displays_1_out_62));  // open: dp
  _7_Segment_Display u_7_segment_display_5 (
    .g(nucleo_de_los_displays_1_out_51), .f(nucleo_de_los_displays_1_out_52),
    .a(nucleo_de_los_displays_1_out_57), .b(nucleo_de_los_displays_1_out_56),
    .e(nucleo_de_los_displays_1_out_53), .d(nucleo_de_los_displays_1_out_54),
    .c(nucleo_de_los_displays_1_out_55));  // open: dp
  _7_Segment_Display u_7_segment_display_6 (
    .g(nucleo_de_los_displays_1_out_44), .f(nucleo_de_los_displays_1_out_45),
    .a(nucleo_de_los_displays_1_out_50), .b(nucleo_de_los_displays_1_out_49),
    .e(nucleo_de_los_displays_1_out_46), .d(nucleo_de_los_displays_1_out_47),
    .c(nucleo_de_los_displays_1_out_48));  // open: dp
  _7_Segment_Display u_7_segment_display_7 (
    .g(nucleo_de_los_displays_1_out_37), .f(nucleo_de_los_displays_1_out_38),
    .a(nucleo_de_los_displays_1_out_43), .b(nucleo_de_los_displays_1_out_42),
    .e(nucleo_de_los_displays_1_out_39), .d(nucleo_de_los_displays_1_out_40),
    .c(nucleo_de_los_displays_1_out_41));  // open: dp
  _7_Segment_Display u_7_segment_display_8 (
    .g(nucleo_de_los_displays_1_out_30), .f(nucleo_de_los_displays_1_out_31),
    .a(nucleo_de_los_displays_1_out_36), .b(nucleo_de_los_displays_1_out_35),
    .e(nucleo_de_los_displays_1_out_32), .d(nucleo_de_los_displays_1_out_33),
    .c(nucleo_de_los_displays_1_out_34));  // open: dp
  _7_Segment_Display u_7_segment_display_9 (
    .g(nucleo_de_los_displays_1_out_23), .f(nucleo_de_los_displays_1_out_24),
    .a(nucleo_de_los_displays_1_out_29), .b(nucleo_de_los_displays_1_out_28),
    .e(nucleo_de_los_displays_1_out_25), .d(nucleo_de_los_displays_1_out_26),
    .c(nucleo_de_los_displays_1_out_27));  // open: dp

  // Notes on the sheet:
  //   E1
  //   B1
  //   ^
  //   =
endmodule

module Nucleo_de_la_Potencia (
  input  EXPONENTE,
  input  E2,
  input  E3,
  input  BASE,
  input  B2,
  input  B3,
  output T,
  output out_8,
  output out_9,
  output out_10,
  output out_11,
  output out_12,
  output out_13,
  output out_14,
  output out_15,
  output out_16,
  output out_17,
  output out_18,
  output out_19,
  output out_20,
  output out_21,
  output out_22,
  output out_23,
  output out_24,
  output out_25,
  output out_26
);

  wire \elección_potencia_p_0_1_out_7 , \elección_potencia_p_0_1_out_8 , \elección_potencia_p_0_1_out_9 ,
       \elección_potencia_p_1_1_out_7 , \elección_potencia_p_1_1_out_8 , \elección_potencia_p_1_1_out_9 ,
       \elección_potencia_p_2_1_out_7 , \elección_potencia_p_2_1_out_8 , \elección_potencia_p_2_1_out_9 ,
       \elección_potencia_p_2_1_out_10 , \elección_potencia_p_2_1_out_11 , \elección_potencia_p_2_1_out_12 ,
       \elección_potencia_p_3_1_out_7 , \elección_potencia_p_3_1_out_8 , \elección_potencia_p_3_1_out_9 ,
       \elección_potencia_p_3_1_out_10 , \elección_potencia_p_3_1_out_11 , \elección_potencia_p_3_1_out_12 ,
       \elección_potencia_p_3_1_out_13 , \elección_potencia_p_3_1_out_14 , \elección_potencia_p_3_1_out_15 ,
       \elección_potencia_p_4_1_out_7 , \elección_potencia_p_4_1_out_8 , \elección_potencia_p_4_1_out_9 ,
       \elección_potencia_p_4_1_out_10 , \elección_potencia_p_4_1_out_11 , \elección_potencia_p_4_1_out_12 ,
       \elección_potencia_p_4_1_out_13 , \elección_potencia_p_4_1_out_14 , \elección_potencia_p_4_1_out_15 ,
       \elección_potencia_p_4_1_out_16 , \elección_potencia_p_4_1_out_17 , \elección_potencia_p_4_1_out_18 ,
       \elección_potencia_p_5_1_out_7 , \elección_potencia_p_5_1_out_8 , \elección_potencia_p_5_1_out_9 ,
       \elección_potencia_p_5_1_out_10 , \elección_potencia_p_5_1_out_11 , \elección_potencia_p_5_1_out_12 ,
       \elección_potencia_p_5_1_out_13 , \elección_potencia_p_5_1_out_14 , \elección_potencia_p_5_1_out_15 ,
       \elección_potencia_p_5_1_out_16 , \elección_potencia_p_5_1_out_17 , \elección_potencia_p_5_1_out_18 ,
       \elección_potencia_p_5_1_out_19 , \elección_potencia_p_5_1_out_20 , \elección_potencia_p_5_1_out_21 ,
       \elección_potencia_p_6_1_out_7 , \elección_potencia_p_6_1_out_8 , \elección_potencia_p_6_1_out_9 ,
       \elección_potencia_p_6_1_out_10 , \elección_potencia_p_6_1_out_11 , \elección_potencia_p_6_1_out_12 ,
       \elección_potencia_p_6_1_out_13 , \elección_potencia_p_6_1_out_14 , \elección_potencia_p_6_1_out_15 ,
       \elección_potencia_p_6_1_out_16 , \elección_potencia_p_6_1_out_17 , \elección_potencia_p_6_1_out_18 ,
       \elección_potencia_p_6_1_out_19 , \elección_potencia_p_6_1_out_20 , \elección_potencia_p_6_1_out_21 ,
       \elección_potencia_p_6_1_out_22 , \elección_potencia_p_6_1_out_23 , \elección_potencia_p_7_1_out_10 ,
       \elección_potencia_p_7_1_out_11 , \elección_potencia_p_7_1_out_12 , \elección_potencia_p_7_1_out_13 ,
       \elección_potencia_p_7_1_out_14 , \elección_potencia_p_7_1_out_15 , \elección_potencia_p_7_1_out_16 ,
       \elección_potencia_p_7_1_out_17 , \elección_potencia_p_7_1_out_18 , \elección_potencia_p_7_1_out_19 ,
       \elección_potencia_p_7_1_out_20 , \elección_potencia_p_7_1_out_21 , \elección_potencia_p_7_1_out_22 ,
       \elección_potencia_p_7_1_out_23 , \elección_potencia_p_7_1_out_24 , \elección_potencia_p_7_1_out_25 ,
       \elección_potencia_p_7_1_out_26 ;

  \Elección_Potencia_p___0  \elección_potencia_p_0_1  (
    .EXPONENTE(EXPONENTE), .E2(E2), .E3(E3), .BASE(BASE), .B2(B2), .B3(B3),
    .out_7(\elección_potencia_p_0_1_out_7 ), .out_8(\elección_potencia_p_0_1_out_8 ),
    .out_9(\elección_potencia_p_0_1_out_9 ));
  \Elección_Potencia_p___1  \elección_potencia_p_1_1  (
    .EXPONENTE(EXPONENTE), .E2(E2), .E3(E3), .BASE(BASE), .B2(B2), .B3(B3),
    .out_8(\elección_potencia_p_1_1_out_8 ), .out_7(\elección_potencia_p_1_1_out_7 ),
    .out_9(\elección_potencia_p_1_1_out_9 ));
  \Elección_Potencia_p___2  \elección_potencia_p_2_1  (
    .E1(EXPONENTE), .E2(E2), .E3(E3), .out_12(\elección_potencia_p_2_1_out_12 ),
    .out_11(\elección_potencia_p_2_1_out_11 ), .out_10(\elección_potencia_p_2_1_out_10 ),
    .out_9(\elección_potencia_p_2_1_out_9 ), .out_8(\elección_potencia_p_2_1_out_8 ),
    .out_7(\elección_potencia_p_2_1_out_7 ), .BASE(BASE), .B2(B2), .B3(B3));
  \Elección_Potencia_p___3  \elección_potencia_p_3_1  (
    .E1(EXPONENTE), .E2(E2), .E3(E3), .BASE(BASE), .B2(B2), .B3(B3), .out_7(\elección_potencia_p_3_1_out_7 ),
    .out_8(\elección_potencia_p_3_1_out_8 ), .out_9(\elección_potencia_p_3_1_out_9 ),
    .out_10(\elección_potencia_p_3_1_out_10 ), .out_11(\elección_potencia_p_3_1_out_11 ),
    .out_12(\elección_potencia_p_3_1_out_12 ), .out_13(\elección_potencia_p_3_1_out_13 ),
    .out_14(\elección_potencia_p_3_1_out_14 ), .out_15(\elección_potencia_p_3_1_out_15 ));
  \Elección_Potencia_p___4  \elección_potencia_p_4_1  (
    .E1(EXPONENTE), .E2(E2), .E3(E3), .BASE(BASE), .B2(B2), .B3(B3), .out_7(\elección_potencia_p_4_1_out_7 ),
    .out_8(\elección_potencia_p_4_1_out_8 ), .out_9(\elección_potencia_p_4_1_out_9 ),
    .out_10(\elección_potencia_p_4_1_out_10 ), .out_11(\elección_potencia_p_4_1_out_11 ),
    .out_12(\elección_potencia_p_4_1_out_12 ), .out_13(\elección_potencia_p_4_1_out_13 ),
    .out_14(\elección_potencia_p_4_1_out_14 ), .out_15(\elección_potencia_p_4_1_out_15 ),
    .out_16(\elección_potencia_p_4_1_out_16 ), .out_17(\elección_potencia_p_4_1_out_17 ),
    .out_18(\elección_potencia_p_4_1_out_18 ));
  \Elección_Potencia_p___5  \elección_potencia_p_5_1  (
    .E1(EXPONENTE), .E2(E2), .E3(E3), .BASE(BASE), .B2(B2), .B3(B3), .out_7(\elección_potencia_p_5_1_out_7 ),
    .out_8(\elección_potencia_p_5_1_out_8 ), .out_9(\elección_potencia_p_5_1_out_9 ),
    .out_10(\elección_potencia_p_5_1_out_10 ), .out_11(\elección_potencia_p_5_1_out_11 ),
    .out_12(\elección_potencia_p_5_1_out_12 ), .out_13(\elección_potencia_p_5_1_out_13 ),
    .out_14(\elección_potencia_p_5_1_out_14 ), .out_15(\elección_potencia_p_5_1_out_15 ),
    .out_16(\elección_potencia_p_5_1_out_16 ), .out_17(\elección_potencia_p_5_1_out_17 ),
    .out_18(\elección_potencia_p_5_1_out_18 ), .out_19(\elección_potencia_p_5_1_out_19 ),
    .out_20(\elección_potencia_p_5_1_out_20 ), .out_21(\elección_potencia_p_5_1_out_21 ));
  \Elección_Potencia_p___6  \elección_potencia_p_6_1  (
    .E1(EXPONENTE), .E2(E2), .E3(E3), .BASE(BASE), .B2(B2), .B3(B3), .out_7(\elección_potencia_p_6_1_out_7 ),
    .out_8(\elección_potencia_p_6_1_out_8 ), .out_9(\elección_potencia_p_6_1_out_9 ),
    .out_10(\elección_potencia_p_6_1_out_10 ), .out_11(\elección_potencia_p_6_1_out_11 ),
    .out_12(\elección_potencia_p_6_1_out_12 ), .out_13(\elección_potencia_p_6_1_out_13 ),
    .out_14(\elección_potencia_p_6_1_out_14 ), .out_15(\elección_potencia_p_6_1_out_15 ),
    .out_16(\elección_potencia_p_6_1_out_16 ), .out_17(\elección_potencia_p_6_1_out_17 ),
    .out_18(\elección_potencia_p_6_1_out_18 ), .out_19(\elección_potencia_p_6_1_out_19 ),
    .out_20(\elección_potencia_p_6_1_out_20 ), .out_21(\elección_potencia_p_6_1_out_21 ),
    .out_22(\elección_potencia_p_6_1_out_22 ), .out_23(\elección_potencia_p_6_1_out_23 ));
  \Elección_Potencia_p___7  \elección_potencia_p_7_1  (
    .E1(EXPONENTE), .E2(E2), .E3(E3), .B1(BASE), .B2(B2), .B3(B3), .out_7(T), .out_8(out_19), .out_9(out_23),
    .out_10(\elección_potencia_p_7_1_out_10 ), .out_11(\elección_potencia_p_7_1_out_11 ),
    .out_12(\elección_potencia_p_7_1_out_12 ), .out_13(\elección_potencia_p_7_1_out_13 ),
    .out_14(\elección_potencia_p_7_1_out_14 ), .out_15(\elección_potencia_p_7_1_out_15 ),
    .out_16(\elección_potencia_p_7_1_out_16 ), .out_17(\elección_potencia_p_7_1_out_17 ),
    .out_18(\elección_potencia_p_7_1_out_18 ), .out_19(\elección_potencia_p_7_1_out_19 ),
    .out_20(\elección_potencia_p_7_1_out_20 ), .out_21(\elección_potencia_p_7_1_out_21 ),
    .out_22(\elección_potencia_p_7_1_out_22 ), .out_23(\elección_potencia_p_7_1_out_23 ),
    .out_24(\elección_potencia_p_7_1_out_24 ), .out_25(\elección_potencia_p_7_1_out_25 ),
    .out_26(\elección_potencia_p_7_1_out_26 ));
  or or_1 (out_8, \elección_potencia_p_6_1_out_7 , \elección_potencia_p_7_1_out_10 );
  or or_2 (out_9, \elección_potencia_p_6_1_out_8 , \elección_potencia_p_7_1_out_11 );
  or or_3 (out_10, \elección_potencia_p_5_1_out_7 , \elección_potencia_p_6_1_out_9 , \elección_potencia_p_7_1_out_12 );
  or or_4 (out_11, \elección_potencia_p_5_1_out_8 , \elección_potencia_p_6_1_out_10 , \elección_potencia_p_7_1_out_13 );
  or or_5 (out_12, \elección_potencia_p_5_1_out_9 , \elección_potencia_p_6_1_out_11 , \elección_potencia_p_7_1_out_14 );
  or or_6 (out_13, \elección_potencia_p_4_1_out_7 , \elección_potencia_p_5_1_out_10 , \elección_potencia_p_6_1_out_12 , \elección_potencia_p_7_1_out_15 );
  or or_7 (out_14, \elección_potencia_p_4_1_out_8 , \elección_potencia_p_5_1_out_11 , \elección_potencia_p_6_1_out_13 , \elección_potencia_p_7_1_out_16 );
  or or_8 (out_15, \elección_potencia_p_4_1_out_9 , \elección_potencia_p_5_1_out_12 , \elección_potencia_p_6_1_out_14 , \elección_potencia_p_7_1_out_17 );
  or or_9 (out_16, \elección_potencia_p_3_1_out_7 , \elección_potencia_p_4_1_out_10 , \elección_potencia_p_5_1_out_13 , \elección_potencia_p_6_1_out_15 , \elección_potencia_p_7_1_out_18 );
  or or_10 (out_17, \elección_potencia_p_3_1_out_8 , \elección_potencia_p_4_1_out_11 , \elección_potencia_p_5_1_out_14 , \elección_potencia_p_6_1_out_16 , \elección_potencia_p_7_1_out_19 );
  or or_11 (out_18, \elección_potencia_p_3_1_out_9 , \elección_potencia_p_4_1_out_12 , \elección_potencia_p_5_1_out_15 , \elección_potencia_p_6_1_out_17 , \elección_potencia_p_7_1_out_20 );
  or or_12 (out_20, \elección_potencia_p_2_1_out_7 , \elección_potencia_p_3_1_out_10 , \elección_potencia_p_4_1_out_13 , \elección_potencia_p_5_1_out_16 , \elección_potencia_p_6_1_out_18 , \elección_potencia_p_7_1_out_21 );
  or or_13 (out_21, \elección_potencia_p_2_1_out_8 , \elección_potencia_p_3_1_out_11 , \elección_potencia_p_4_1_out_14 , \elección_potencia_p_5_1_out_17 , \elección_potencia_p_6_1_out_19 , \elección_potencia_p_7_1_out_22 );
  or or_14 (out_22, \elección_potencia_p_2_1_out_9 , \elección_potencia_p_3_1_out_12 , \elección_potencia_p_4_1_out_15 , \elección_potencia_p_5_1_out_18 , \elección_potencia_p_6_1_out_20 , \elección_potencia_p_7_1_out_23 );
  or or_15 (out_24, \elección_potencia_p_0_1_out_9 , \elección_potencia_p_1_1_out_7 , \elección_potencia_p_2_1_out_10 , \elección_potencia_p_3_1_out_13 , \elección_potencia_p_4_1_out_16 , \elección_potencia_p_5_1_out_19 , \elección_potencia_p_6_1_out_21 , \elección_potencia_p_7_1_out_24 );
  or or_16 (out_25, \elección_potencia_p_0_1_out_8 , \elección_potencia_p_1_1_out_8 , \elección_potencia_p_2_1_out_11 , \elección_potencia_p_3_1_out_14 , \elección_potencia_p_4_1_out_17 , \elección_potencia_p_5_1_out_20 , \elección_potencia_p_6_1_out_22 , \elección_potencia_p_7_1_out_25 );
  or or_17 (out_26, \elección_potencia_p_0_1_out_7 , \elección_potencia_p_1_1_out_9 , \elección_potencia_p_2_1_out_12 , \elección_potencia_p_3_1_out_15 , \elección_potencia_p_4_1_out_18 , \elección_potencia_p_5_1_out_21 , \elección_potencia_p_6_1_out_23 , \elección_potencia_p_7_1_out_26 );

  // Notes on the sheet:
  //   E1
  //   B1
endmodule

module Nucleo_de_los_Displays (
  input  in_1,
  input  in_2,
  input  in_3,
  input  in_4,
  input  in_5,
  input  in_6,
  input  in_7,
  input  in_8,
  input  in_9,
  input  in_10,
  input  in_11,
  input  in_12,
  input  in_13,
  input  in_14,
  input  in_15,
  input  in_16,
  input  in_17,
  input  in_18,
  input  in_19,
  input  in_20,
  input  in_21,
  input  in_22,
  output out_23,
  output out_24,
  output out_25,
  output out_26,
  output out_27,
  output out_28,
  output out_29,
  output out_30,
  output out_31,
  output out_32,
  output out_33,
  output out_34,
  output out_35,
  output out_36,
  output out_37,
  output out_38,
  output out_39,
  output out_40,
  output out_41,
  output out_42,
  output out_43,
  output out_44,
  output out_45,
  output out_46,
  output out_47,
  output out_48,
  output out_49,
  output out_50,
  output out_51,
  output out_52,
  output out_53,
  output out_54,
  output out_55,
  output out_56,
  output out_57,
  output out_58,
  output out_59,
  output out_60,
  output out_61,
  output out_62,
  output out_63,
  output out_64,
  output out_65,
  output out_66,
  output out_67,
  output out_68,
  output out_69,
  output out_70,
  output out_71
);

  wire display_decimal_1_out_23, display_decimal_1_out_24, display_decimal_1_out_25,
       display_decimal_1_out_26, display_decimal_1_out_27, display_decimal_1_out_28,
       display_decimal_1_out_29, display_decimal_1_out_30, display_decimal_1_out_31,
       display_decimal_1_out_32, display_decimal_1_out_33, display_decimal_1_out_34,
       display_decimal_1_out_35, display_decimal_1_out_36, display_decimal_1_out_37,
       display_decimal_1_out_38, display_decimal_1_out_39, display_decimal_1_out_40,
       display_decimal_1_out_41, display_decimal_1_out_42, display_decimal_1_out_43,
       display_decimal_1_out_44, display_decimal_1_out_45, display_decimal_1_out_46,
       display_decimal_1_out_47, display_decimal_1_out_48, display_decimal_1_out_49,
       display_decimal_1_out_50, display_decimal_1_out_51, display_decimal_1_out_52,
       display_decimal_1_out_53, display_decimal_1_out_54, display_decimal_1_out_55,
       display_decimal_1_out_56, display_decimal_1_out_57, display_decimal_1_out_58,
       display_decimal_1_out_59, display_decimal_1_out_60, display_decimal_1_out_61,
       display_decimal_1_out_62, display_decimal_1_out_63, display_decimal_1_out_64,
       display_decimal_1_out_65, display_decimal_1_out_66, display_decimal_1_out_67,
       display_decimal_1_out_68, display_decimal_1_out_69, display_decimal_1_out_70,
       display_decimal_1_out_71, display_hexadecimal_1_out_23, display_hexadecimal_1_out_24,
       display_hexadecimal_1_out_25, display_hexadecimal_1_out_26, display_hexadecimal_1_out_27,
       display_hexadecimal_1_out_28, display_hexadecimal_1_out_29, display_hexadecimal_1_out_30,
       display_hexadecimal_1_out_31, display_hexadecimal_1_out_32, display_hexadecimal_1_out_33,
       display_hexadecimal_1_out_34, display_hexadecimal_1_out_35, display_hexadecimal_1_out_36,
       display_hexadecimal_1_out_37, display_hexadecimal_1_out_38, display_hexadecimal_1_out_39,
       display_hexadecimal_1_out_40, display_hexadecimal_1_out_41, display_hexadecimal_1_out_42,
       display_hexadecimal_1_out_43, display_hexadecimal_1_out_44, display_hexadecimal_1_out_45,
       display_hexadecimal_1_out_46, display_hexadecimal_1_out_47, display_hexadecimal_1_out_48,
       display_hexadecimal_1_out_49, display_hexadecimal_1_out_50, display_hexadecimal_1_out_51,
       display_hexadecimal_1_out_52, display_hexadecimal_1_out_53, display_hexadecimal_1_out_54,
       display_hexadecimal_1_out_55, display_hexadecimal_1_out_56, display_hexadecimal_1_out_57,
       display_hexadecimal_1_out_58, display_hexadecimal_1_out_59, display_hexadecimal_1_out_60,
       display_hexadecimal_1_out_61, display_hexadecimal_1_out_62, display_hexadecimal_1_out_63,
       display_hexadecimal_1_out_64, display_hexadecimal_1_out_65, display_hexadecimal_1_out_66,
       display_hexadecimal_1_out_67, display_hexadecimal_1_out_68, display_hexadecimal_1_out_69,
       display_hexadecimal_1_out_70, display_hexadecimal_1_out_71, display_octal_1_out_23,
       display_octal_1_out_24, display_octal_1_out_25, display_octal_1_out_26, display_octal_1_out_27,
       display_octal_1_out_28, display_octal_1_out_29, display_octal_1_out_30, display_octal_1_out_31,
       display_octal_1_out_32, display_octal_1_out_33, display_octal_1_out_34, display_octal_1_out_35,
       display_octal_1_out_36, display_octal_1_out_37, display_octal_1_out_38, display_octal_1_out_39,
       display_octal_1_out_40, display_octal_1_out_41, display_octal_1_out_42, display_octal_1_out_43,
       display_octal_1_out_44, display_octal_1_out_45, display_octal_1_out_46, display_octal_1_out_47,
       display_octal_1_out_48, display_octal_1_out_49, display_octal_1_out_50, display_octal_1_out_51,
       display_octal_1_out_52, display_octal_1_out_53, display_octal_1_out_54, display_octal_1_out_55,
       display_octal_1_out_56, display_octal_1_out_57, display_octal_1_out_58, display_octal_1_out_59,
       display_octal_1_out_60, display_octal_1_out_61, display_octal_1_out_62, display_octal_1_out_63,
       display_octal_1_out_64, display_octal_1_out_65, display_octal_1_out_66, display_octal_1_out_67,
       display_octal_1_out_68, display_octal_1_out_69, display_octal_1_out_70, display_octal_1_out_71;

  Display_Decimal display_decimal_1 (
    .in_1(in_1), .in_2(in_2), .in_3(in_3), .in_4(in_4), .in_5(in_5), .in_6(in_6), .in_7(in_7), .in_8(in_8),
    .in_9(in_9), .in_10(in_10), .in_11(in_11), .in_12(in_12), .in_13(in_13), .in_14(in_14), .in_15(in_15),
    .in_16(in_16), .in_17(in_17), .in_18(in_18), .in_19(in_19), .in_20(in_20), .in_21(in_21), .in_22(in_22),
    .out_23(display_decimal_1_out_23), .out_24(display_decimal_1_out_24), .out_25(display_decimal_1_out_25),
    .out_26(display_decimal_1_out_26), .out_27(display_decimal_1_out_27), .out_28(display_decimal_1_out_28),
    .out_29(display_decimal_1_out_29), .out_30(display_decimal_1_out_30), .out_31(display_decimal_1_out_31),
    .out_32(display_decimal_1_out_32), .out_33(display_decimal_1_out_33), .out_34(display_decimal_1_out_34),
    .out_35(display_decimal_1_out_35), .out_36(display_decimal_1_out_36), .out_37(display_decimal_1_out_37),
    .out_38(display_decimal_1_out_38), .out_39(display_decimal_1_out_39), .out_40(display_decimal_1_out_40),
    .out_41(display_decimal_1_out_41), .out_42(display_decimal_1_out_42), .out_43(display_decimal_1_out_43),
    .out_44(display_decimal_1_out_44), .out_45(display_decimal_1_out_45), .out_46(display_decimal_1_out_46),
    .out_47(display_decimal_1_out_47), .out_48(display_decimal_1_out_48), .out_49(display_decimal_1_out_49),
    .out_50(display_decimal_1_out_50), .out_51(display_decimal_1_out_51), .out_52(display_decimal_1_out_52),
    .out_53(display_decimal_1_out_53), .out_54(display_decimal_1_out_54), .out_55(display_decimal_1_out_55),
    .out_56(display_decimal_1_out_56), .out_57(display_decimal_1_out_57), .out_58(display_decimal_1_out_58),
    .out_59(display_decimal_1_out_59), .out_60(display_decimal_1_out_60), .out_61(display_decimal_1_out_61),
    .out_62(display_decimal_1_out_62), .out_63(display_decimal_1_out_63), .out_64(display_decimal_1_out_64),
    .out_65(display_decimal_1_out_65), .out_66(display_decimal_1_out_66), .out_67(display_decimal_1_out_67),
    .out_68(display_decimal_1_out_68), .out_69(display_decimal_1_out_69), .out_70(display_decimal_1_out_70),
    .out_71(display_decimal_1_out_71));
  Display_Octal display_octal_1 (
    .in_1(in_1), .in_2(in_2), .in_3(in_3), .in_4(in_4), .in_5(in_5), .in_6(in_6), .in_7(in_7), .in_8(in_8),
    .in_9(in_9), .in_10(in_10), .in_11(in_11), .in_12(in_12), .in_13(in_13), .in_14(in_14), .in_15(in_15),
    .in_16(in_16), .in_17(in_17), .in_18(in_18), .in_19(in_19), .in_20(in_20), .in_21(in_21),
    .out_23(display_octal_1_out_23), .out_24(display_octal_1_out_24), .out_25(display_octal_1_out_25),
    .out_26(display_octal_1_out_26), .out_27(display_octal_1_out_27), .out_28(display_octal_1_out_28),
    .out_29(display_octal_1_out_29), .out_30(display_octal_1_out_30), .out_31(display_octal_1_out_31),
    .out_32(display_octal_1_out_32), .out_33(display_octal_1_out_33), .out_34(display_octal_1_out_34),
    .out_35(display_octal_1_out_35), .out_36(display_octal_1_out_36), .out_37(display_octal_1_out_37),
    .out_38(display_octal_1_out_38), .out_39(display_octal_1_out_39), .out_40(display_octal_1_out_40),
    .out_41(display_octal_1_out_41), .out_42(display_octal_1_out_42), .out_43(display_octal_1_out_43),
    .out_44(display_octal_1_out_44), .out_45(display_octal_1_out_45), .out_46(display_octal_1_out_46),
    .out_47(display_octal_1_out_47), .out_48(display_octal_1_out_48), .out_49(display_octal_1_out_49),
    .out_50(display_octal_1_out_50), .out_51(display_octal_1_out_51), .out_52(display_octal_1_out_52),
    .out_53(display_octal_1_out_53), .out_54(display_octal_1_out_54), .out_55(display_octal_1_out_55),
    .out_56(display_octal_1_out_56), .out_57(display_octal_1_out_57), .out_58(display_octal_1_out_58),
    .out_59(display_octal_1_out_59), .out_60(display_octal_1_out_60), .out_61(display_octal_1_out_61),
    .out_62(display_octal_1_out_62), .out_63(display_octal_1_out_63), .out_64(display_octal_1_out_64),
    .out_65(display_octal_1_out_65), .out_66(display_octal_1_out_66), .out_67(display_octal_1_out_67),
    .out_68(display_octal_1_out_68), .out_69(display_octal_1_out_69), .out_70(display_octal_1_out_70),
    .out_71(display_octal_1_out_71), .in_22(in_22));
  Display_Hexadecimal display_hexadecimal_1 (
    .in_1(in_1), .in_2(in_2), .in_3(in_3), .in_4(in_4), .in_5(in_5), .in_6(in_6), .in_7(in_7), .in_8(in_8),
    .in_9(in_9), .in_10(in_10), .in_11(in_11), .in_12(in_12), .in_13(in_13), .in_14(in_14), .in_15(in_15),
    .in_16(in_16), .in_17(in_17), .in_18(in_18), .in_19(in_19), .in_20(in_20), .in_21(in_21),
    .out_23(display_hexadecimal_1_out_23), .out_24(display_hexadecimal_1_out_24),
    .out_25(display_hexadecimal_1_out_25), .out_26(display_hexadecimal_1_out_26),
    .out_27(display_hexadecimal_1_out_27), .out_28(display_hexadecimal_1_out_28),
    .out_29(display_hexadecimal_1_out_29), .out_30(display_hexadecimal_1_out_30),
    .out_31(display_hexadecimal_1_out_31), .out_32(display_hexadecimal_1_out_32),
    .out_33(display_hexadecimal_1_out_33), .out_34(display_hexadecimal_1_out_34),
    .out_35(display_hexadecimal_1_out_35), .out_36(display_hexadecimal_1_out_36),
    .out_37(display_hexadecimal_1_out_37), .out_38(display_hexadecimal_1_out_38),
    .out_39(display_hexadecimal_1_out_39), .out_40(display_hexadecimal_1_out_40),
    .out_41(display_hexadecimal_1_out_41), .out_42(display_hexadecimal_1_out_42),
    .out_43(display_hexadecimal_1_out_43), .out_44(display_hexadecimal_1_out_44),
    .out_45(display_hexadecimal_1_out_45), .out_46(display_hexadecimal_1_out_46),
    .out_47(display_hexadecimal_1_out_47), .out_48(display_hexadecimal_1_out_48),
    .out_49(display_hexadecimal_1_out_49), .out_50(display_hexadecimal_1_out_50),
    .out_51(display_hexadecimal_1_out_51), .out_52(display_hexadecimal_1_out_52),
    .out_53(display_hexadecimal_1_out_53), .out_54(display_hexadecimal_1_out_54),
    .out_55(display_hexadecimal_1_out_55), .out_56(display_hexadecimal_1_out_56),
    .out_57(display_hexadecimal_1_out_57), .out_58(display_hexadecimal_1_out_58),
    .out_59(display_hexadecimal_1_out_59), .out_60(display_hexadecimal_1_out_60),
    .out_61(display_hexadecimal_1_out_61), .out_62(display_hexadecimal_1_out_62),
    .out_63(display_hexadecimal_1_out_63), .out_64(display_hexadecimal_1_out_64),
    .out_65(display_hexadecimal_1_out_65), .out_66(display_hexadecimal_1_out_66),
    .out_67(display_hexadecimal_1_out_67), .out_68(display_hexadecimal_1_out_68),
    .out_69(display_hexadecimal_1_out_69), .out_70(display_hexadecimal_1_out_70),
    .out_71(display_hexadecimal_1_out_71), .in_22(in_22));
  or or_1 (out_23, display_octal_1_out_71, display_decimal_1_out_71, display_hexadecimal_1_out_71);
  or or_2 (out_24, display_octal_1_out_70, display_decimal_1_out_70, display_hexadecimal_1_out_70);
  or or_3 (out_25, display_octal_1_out_69, display_decimal_1_out_69, display_hexadecimal_1_out_69);
  or or_4 (out_26, display_octal_1_out_68, display_decimal_1_out_68, display_hexadecimal_1_out_68);
  or or_5 (out_27, display_octal_1_out_67, display_decimal_1_out_67, display_hexadecimal_1_out_67);
  or or_6 (out_28, display_octal_1_out_66, display_decimal_1_out_66, display_hexadecimal_1_out_66);
  or or_7 (out_29, display_octal_1_out_65, display_decimal_1_out_65, display_hexadecimal_1_out_65);
  or or_8 (out_30, display_octal_1_out_64, display_decimal_1_out_64, display_hexadecimal_1_out_64);
  or or_9 (out_31, display_octal_1_out_63, display_decimal_1_out_63, display_hexadecimal_1_out_63);
  or or_10 (out_32, display_octal_1_out_62, display_decimal_1_out_62, display_hexadecimal_1_out_62);
  or or_11 (out_33, display_octal_1_out_61, display_decimal_1_out_61, display_hexadecimal_1_out_61);
  or or_12 (out_34, display_octal_1_out_60, display_decimal_1_out_60, display_hexadecimal_1_out_60);
  or or_13 (out_35, display_octal_1_out_59, display_decimal_1_out_59, display_hexadecimal_1_out_59);
  or or_14 (out_36, display_octal_1_out_58, display_decimal_1_out_58, display_hexadecimal_1_out_58);
  or or_15 (out_37, display_octal_1_out_57, display_decimal_1_out_57, display_hexadecimal_1_out_57);
  or or_16 (out_38, display_octal_1_out_56, display_decimal_1_out_56, display_hexadecimal_1_out_56);
  or or_17 (out_39, display_octal_1_out_55, display_decimal_1_out_55, display_hexadecimal_1_out_55);
  or or_18 (out_40, display_octal_1_out_54, display_decimal_1_out_54, display_hexadecimal_1_out_54);
  or or_19 (out_41, display_octal_1_out_53, display_decimal_1_out_53, display_hexadecimal_1_out_53);
  or or_20 (out_42, display_octal_1_out_52, display_decimal_1_out_52, display_hexadecimal_1_out_52);
  or or_21 (out_43, display_octal_1_out_51, display_decimal_1_out_51, display_hexadecimal_1_out_51);
  or or_22 (out_44, display_octal_1_out_50, display_decimal_1_out_50, display_hexadecimal_1_out_50);
  or or_23 (out_45, display_octal_1_out_49, display_decimal_1_out_49, display_hexadecimal_1_out_49);
  or or_24 (out_46, display_octal_1_out_48, display_decimal_1_out_48, display_hexadecimal_1_out_48);
  or or_25 (out_47, display_octal_1_out_47, display_decimal_1_out_47, display_hexadecimal_1_out_47);
  or or_26 (out_48, display_octal_1_out_46, display_decimal_1_out_46, display_hexadecimal_1_out_46);
  or or_27 (out_49, display_octal_1_out_45, display_decimal_1_out_45, display_hexadecimal_1_out_45);
  or or_28 (out_50, display_octal_1_out_44, display_decimal_1_out_44, display_hexadecimal_1_out_44);
  or or_29 (out_51, display_octal_1_out_43, display_decimal_1_out_43, display_hexadecimal_1_out_43);
  or or_30 (out_52, display_octal_1_out_42, display_decimal_1_out_42, display_hexadecimal_1_out_42);
  or or_31 (out_53, display_octal_1_out_41, display_decimal_1_out_41, display_hexadecimal_1_out_41);
  or or_32 (out_54, display_octal_1_out_40, display_decimal_1_out_40, display_hexadecimal_1_out_40);
  or or_33 (out_55, display_octal_1_out_39, display_decimal_1_out_39, display_hexadecimal_1_out_39);
  or or_34 (out_56, display_octal_1_out_38, display_decimal_1_out_38, display_hexadecimal_1_out_38);
  or or_35 (out_57, display_octal_1_out_37, display_decimal_1_out_37, display_hexadecimal_1_out_37);
  or or_36 (out_58, display_octal_1_out_36, display_decimal_1_out_36, display_hexadecimal_1_out_36);
  or or_37 (out_59, display_octal_1_out_35, display_decimal_1_out_35, display_hexadecimal_1_out_35);
  or or_38 (out_60, display_octal_1_out_34, display_decimal_1_out_34, display_hexadecimal_1_out_34);
  or or_39 (out_61, display_octal_1_out_33, display_decimal_1_out_33, display_hexadecimal_1_out_33);
  or or_40 (out_62, display_octal_1_out_32, display_decimal_1_out_32, display_hexadecimal_1_out_32);
  or or_41 (out_63, display_octal_1_out_31, display_decimal_1_out_31, display_hexadecimal_1_out_31);
  or or_42 (out_64, display_octal_1_out_30, display_decimal_1_out_30, display_hexadecimal_1_out_30);
  or or_43 (out_65, display_octal_1_out_29, display_decimal_1_out_29, display_hexadecimal_1_out_29);
  or or_44 (out_66, display_octal_1_out_28, display_decimal_1_out_28, display_hexadecimal_1_out_28);
  or or_45 (out_67, display_octal_1_out_27, display_decimal_1_out_27, display_hexadecimal_1_out_27);
  or or_46 (out_68, display_octal_1_out_26, display_decimal_1_out_26, display_hexadecimal_1_out_26);
  or or_47 (out_69, display_octal_1_out_25, display_decimal_1_out_25, display_hexadecimal_1_out_25);
  or or_48 (out_70, display_octal_1_out_24, display_decimal_1_out_24, display_hexadecimal_1_out_24);
  or or_49 (out_71, display_octal_1_out_23, display_decimal_1_out_23, display_hexadecimal_1_out_23);
endmodule

module Suma_de_2_Entradas (
  input  E1,
  input  E2,
  output out_3,
  output ACARREO_1
);

  wire and_1_out, and_2_out, not_1_out, not_2_out;

  not not_1 (not_1_out, E1);
  not not_2 (not_2_out, E2);
  and and_1 (and_1_out, not_1_out, E2);
  and and_2 (and_2_out, E1, not_2_out);
  and and_3 (ACARREO_1, E1, E2);
  or or_1 (out_3, and_1_out, and_2_out);

  // Notes on the sheet:
  //   ENTRADAS
  //   RESULTADO DE LA SUMA
endmodule

module Suma_de_3_Entradas (
  input  E1,
  input  E2,
  input  E3,
  output out_4,
  output ACARREO_1
);

  wire and_1_out, and_2_out, and_3_out, and_4_out, and_5_out, and_6_out, and_7_out, not_1_out, not_2_out,
       not_3_out;

  not not_1 (not_1_out, E1);
  not not_2 (not_2_out, E2);
  not not_3 (not_3_out, E3);
  and and_1 (and_1_out, E1, not_2_out, not_3_out);
  and and_2 (and_2_out, E1, E2, E3);
  and and_3 (and_3_out, not_1_out, E2, not_3_out);
  and and_4 (and_4_out, not_1_out, not_2_out, E3);
  and and_5 (and_5_out, E1, E2);
  and and_6 (and_6_out, E1, E3);
  and and_7 (and_7_out, E2, E3);
  or or_1 (out_4, and_1_out, and_2_out, and_3_out, and_4_out);
  or or_2 (ACARREO_1, and_5_out, and_6_out, and_7_out);

  // Notes on the sheet:
  //   ENTRADAS
  //   RESULTADO DE LA SUMA
endmodule

module Suma_de_4_Entradas (
  input  E1,
  input  E2,
  input  E3,
  input  E4,
  output out_5,
  output ACARREO_1,
  output ACARREO_2
);

  wire and_1_out, and_2_out, and_3_out, and_4_out, and_5_out, and_6_out, and_7_out, and_8_out, not_1_out,
       not_2_out, not_3_out, not_4_out, or_1_out, or_2_out, or_3_out, or_4_out, or_5_out;

  not not_1 (not_1_out, E1);
  not not_2 (not_2_out, E2);
  not not_3 (not_3_out, E3);
  not not_4 (not_4_out, E4);
  and and_1 (and_1_out, not_1_out, not_2_out, not_3_out, E4);
  and and_2 (and_2_out, not_1_out, not_2_out, E3, not_4_out);
  and and_3 (and_3_out, not_1_out, E2, not_3_out, not_4_out);
  and and_4 (and_4_out, not_1_out, E2, E3, E4);
  and and_5 (and_5_out, E1, E2, not_3_out, E4);
  and and_6 (and_6_out, E1, E2, E3, not_4_out);
  and and_7 (and_7_out, E1, not_2_out, not_3_out, not_4_out);
  and and_8 (and_8_out, E1, not_2_out, E3, E4);
  or or_1 (or_1_out, E1, E3, E4);
  or or_2 (or_2_out, E1, E2, E3);
  or or_3 (or_3_out, E1, E2, E4);
  or or_4 (or_4_out, E2, E3, E4);
  or or_5 (or_5_out, not_1_out, not_2_out, not_3_out, not_4_out);
  and and_9 (ACARREO_2, E1, E2, E3, E4);
  or or_6 (out_5, and_1_out, and_2_out, and_3_out, and_4_out, and_5_out, and_6_out, and_7_out, and_8_out);
  and and_10 (ACARREO_1, or_1_out, or_2_out, or_3_out, or_4_out, or_5_out);

  // Notes on the sheet:
  //   ENTRADAS
  //   RESULTADO DE LA SUMA
endmodule

module Suma_de_5_Entradas (
  input  E1,
  input  E2,
  input  E3,
  input  E4,
  input  E5,
  output out_6,
  output ACARREO_1,
  output ACARREO_2
);

  wire and_1_out, and_2_out, and_3_out, and_4_out, and_5_out, and_6_out, and_7_out, and_8_out, and_9_out,
       and_10_out, and_11_out, and_12_out, and_13_out, and_14_out, and_15_out, and_16_out, and_17_out,
       and_18_out, and_19_out, and_20_out, and_21_out, not_1_out, not_2_out, not_3_out, not_4_out, not_5_out,
       or_1_out, or_2_out, or_3_out, or_4_out, or_5_out, or_6_out, or_7_out, or_8_out, or_9_out, or_10_out;

  not not_1 (not_1_out, E1);
  not not_2 (not_2_out, E2);
  not not_3 (not_3_out, E3);
  not not_4 (not_4_out, E4);
  not not_5 (not_5_out, E5);
  or or_1 (or_1_out, not_5_out, not_4_out, not_3_out, not_2_out);
  and and_1 (and_1_out, not_1_out, not_2_out, not_3_out, not_4_out, E5);
  and and_2 (and_2_out, not_1_out, not_2_out, not_3_out, E4, not_5_out);
  and and_3 (and_3_out, not_1_out, not_2_out, E3, not_4_out, not_5_out);
  and and_4 (and_4_out, not_1_out, not_2_out, E3, E4, E5);
  and and_5 (and_5_out, not_1_out, E2, E3, not_4_out, E5);
  and and_6 (and_6_out, not_1_out, E2, E3, E4, not_5_out);
  and and_7 (and_7_out, not_1_out, E2, not_3_out, not_4_out, not_5_out);
  and and_8 (and_8_out, not_1_out, E2, not_3_out, E4, E5);
  and and_9 (and_9_out, E1, not_2_out, not_3_out, not_4_out, not_5_out);
  and and_10 (and_10_out, E1, not_2_out, not_3_out, E4, E5);
  and and_11 (and_11_out, E1, not_2_out, E3, not_4_out, E5);
  and and_12 (and_12_out, E1, not_2_out, E3, E4, not_5_out);
  and and_13 (and_13_out, E1, E2, E3, not_4_out, not_5_out);
  and and_14 (and_14_out, E1, E2, E3, E4, E5);
  and and_15 (and_15_out, E1, E2, not_3_out, not_4_out, E5);
  and and_16 (and_16_out, E1, E2, not_3_out, E4, not_5_out);
  or or_2 (or_2_out, E1, E2, E3, E4);
  or or_3 (or_3_out, E1, E2, E4, E5);
  or or_4 (or_4_out, E1, E3, E4, E5);
  or or_5 (or_5_out, E2, E3, E4, E5);
  or or_6 (or_6_out, not_2_out, E3, not_1_out, not_4_out, not_5_out);
  or or_7 (or_7_out, E1, E2, E3, not_4_out, E5);
  or or_8 (or_8_out, not_1_out, not_4_out, not_3_out, not_5_out);
  or or_9 (or_9_out, not_1_out, not_3_out, not_2_out, not_5_out);
  or or_10 (or_10_out, not_1_out, not_4_out, not_3_out, not_2_out);
  and and_17 (and_17_out, E2, E3, E4, E5);
  and and_18 (and_18_out, E1, E3, E4, E5);
  and and_19 (and_19_out, E1, E2, E3, E5);
  and and_20 (and_20_out, E1, E2, E4, E5);
  and and_21 (and_21_out, E1, E2, E3, E4);
  or or_11 (ACARREO_2, and_17_out, and_18_out, and_19_out, and_20_out, and_21_out);
  or or_12 (out_6, and_1_out, and_2_out, and_3_out, and_4_out, and_5_out, and_6_out, and_7_out, and_8_out, and_9_out, and_10_out, and_11_out, and_12_out, and_13_out, and_14_out, and_15_out, and_16_out);
  and and_22 (ACARREO_1, or_1_out, or_2_out, or_3_out, or_4_out, or_5_out, or_6_out, or_7_out, or_8_out, or_9_out, or_10_out);

  // Notes on the sheet:
  //   ENTRADAS
  //   RESULTADO DE LA SUMA
endmodule

module \Multiplicación_de_3___1  (
  input  ENTRADAS,
  input  in_2,
  input  MULTIPLICANDO_3,
  input  MULTIPLICADOR,
  output RESULTADO_1,
  output RESULTADO_2,
  output RESULTADO_3
);

  and and_1 (RESULTADO_1, ENTRADAS, MULTIPLICADOR);
  and and_2 (RESULTADO_2, in_2, MULTIPLICADOR);
  and and_3 (RESULTADO_3, MULTIPLICANDO_3, MULTIPLICADOR);

  // Notes on the sheet:
  //   MULTIPLICANDO 1
  //   MULTIPLICANDO 2
endmodule

module \Multiplicación_de_6___1  (
  input  ENTRADAS,
  input  in_2,
  input  MULTIPLICANDO_3,
  input  MULTIPLICANDO_4,
  input  MULTIPLICANDO_5,
  input  in_6,
  input  MULTIPLICADOR,
  output RESULTADO_1,
  output RESULTADO_2,
  output RESULTADO_3,
  output RESULTADO_4,
  output RESULTADO_5,
  output RESULTADO_6
);

  and and_1 (RESULTADO_1, ENTRADAS, MULTIPLICADOR);
  and and_2 (RESULTADO_2, in_2, MULTIPLICADOR);
  and and_3 (RESULTADO_3, MULTIPLICANDO_3, MULTIPLICADOR);
  and and_4 (RESULTADO_4, MULTIPLICANDO_4, MULTIPLICADOR);
  and and_5 (RESULTADO_5, MULTIPLICANDO_5, MULTIPLICADOR);
  and and_6 (RESULTADO_6, in_6, MULTIPLICADOR);

  // Notes on the sheet:
  //   MULTIPLICANDO 1
  //   MULTIPLICANDO 2
  //   MULTIPLICANDO 6
endmodule

module \Multiplicación_de_9___1  (
  input  ENTRADAS,
  input  in_2,
  input  MULTIPLICANDO_3,
  input  MULTIPLICANDO_4,
  input  MULTIPLICANDO_5,
  input  in_6,
  input  MULTIPLICANDO_7,
  input  MULTIPLICANDO_8,
  input  in_9,
  input  MULTIPLICADOR,
  output RESULTADO_1,
  output RESULTADO_2,
  output RESULTADO_3,
  output RESULTADO_4,
  output RESULTADO_5,
  output RESULTADO_6,
  output RESULTADO_7,
  output RESULTADO_8,
  output RESULTADO_9
);

  and and_1 (RESULTADO_1, ENTRADAS, MULTIPLICADOR);
  and and_2 (RESULTADO_2, in_2, MULTIPLICADOR);
  and and_3 (RESULTADO_3, MULTIPLICANDO_3, MULTIPLICADOR);
  and and_4 (RESULTADO_4, MULTIPLICANDO_4, MULTIPLICADOR);
  and and_5 (RESULTADO_5, MULTIPLICANDO_5, MULTIPLICADOR);
  and and_6 (RESULTADO_6, in_6, MULTIPLICADOR);
  and and_7 (RESULTADO_7, MULTIPLICANDO_7, MULTIPLICADOR);
  and and_8 (RESULTADO_8, MULTIPLICANDO_8, MULTIPLICADOR);
  and and_9 (RESULTADO_9, in_9, MULTIPLICADOR);

  // Notes on the sheet:
  //   MULTIPLICANDO 1
  //   MULTIPLICANDO 2
  //   MULTIPLICANDO 6
  //   MULTIPLICANDO 9
endmodule

module \Multiplicación_de_12___1  (
  input  ENTRADAS,
  input  in_2,
  input  MULTIPLICANDO_3,
  input  MULTIPLICANDO_4,
  input  MULTIPLICANDO_5,
  input  in_6,
  input  MULTIPLICANDO_7,
  input  MULTIPLICANDO_8,
  input  in_9,
  input  MULTIPLICANDO_10,
  input  MULTIPLICANDO_11,
  input  in_12,
  input  MULTIPLICADOR,
  output RESULTADO_1,
  output RESULTADO_2,
  output RESULTADO_3,
  output RESULTADO_4,
  output RESULTADO_5,
  output RESULTADO_6,
  output RESULTADO_7,
  output RESULTADO_8,
  output RESULTADO_9,
  output RESULTADO_10,
  output RESULTADO_11,
  output RESULTADO_12
);

  and and_1 (RESULTADO_1, ENTRADAS, MULTIPLICADOR);
  and and_2 (RESULTADO_2, in_2, MULTIPLICADOR);
  and and_3 (RESULTADO_3, MULTIPLICANDO_3, MULTIPLICADOR);
  and and_4 (RESULTADO_4, MULTIPLICANDO_4, MULTIPLICADOR);
  and and_5 (RESULTADO_5, MULTIPLICANDO_5, MULTIPLICADOR);
  and and_6 (RESULTADO_6, in_6, MULTIPLICADOR);
  and and_7 (RESULTADO_7, MULTIPLICANDO_7, MULTIPLICADOR);
  and and_8 (RESULTADO_8, MULTIPLICANDO_8, MULTIPLICADOR);
  and and_9 (RESULTADO_9, in_9, MULTIPLICADOR);
  and and_10 (RESULTADO_10, MULTIPLICANDO_10, MULTIPLICADOR);
  and and_11 (RESULTADO_11, MULTIPLICANDO_11, MULTIPLICADOR);
  and and_12 (RESULTADO_12, in_12, MULTIPLICADOR);

  // Notes on the sheet:
  //   MULTIPLICANDO 1
  //   MULTIPLICANDO 2
  //   MULTIPLICANDO 6
  //   MULTIPLICANDO 9
  //   MULTIPLICANDO 12
endmodule

module \Multiplicación_de_15___1  (
  input  ENTRADAS,
  input  in_2,
  input  MULTIPLICANDO_3,
  input  MULTIPLICANDO_4,
  input  MULTIPLICANDO_5,
  input  in_6,
  input  MULTIPLICANDO_7,
  input  MULTIPLICANDO_8,
  input  in_9,
  input  MULTIPLICANDO_10,
  input  MULTIPLICANDO_11,
  input  in_12,
  input  in_13,
  input  in_14,
  input  in_15,
  input  MULTIPLICADOR,
  output RESULTADO_1,
  output RESULTADO_2,
  output RESULTADO_3,
  output RESULTADO_4,
  output RESULTADO_5,
  output RESULTADO_6,
  output RESULTADO_7,
  output RESULTADO_8,
  output RESULTADO_9,
  output RESULTADO_10,
  output RESULTADO_11,
  output RESULTADO_12,
  output RESULTADO_13,
  output RESULTADO_14,
  output RESULTADO_15
);

  and and_1 (RESULTADO_1, ENTRADAS, MULTIPLICADOR);
  and and_2 (RESULTADO_2, in_2, MULTIPLICADOR);
  and and_3 (RESULTADO_3, MULTIPLICANDO_3, MULTIPLICADOR);
  and and_4 (RESULTADO_4, MULTIPLICANDO_4, MULTIPLICADOR);
  and and_5 (RESULTADO_5, MULTIPLICANDO_5, MULTIPLICADOR);
  and and_6 (RESULTADO_6, in_6, MULTIPLICADOR);
  and and_7 (RESULTADO_7, MULTIPLICANDO_7, MULTIPLICADOR);
  and and_8 (RESULTADO_8, MULTIPLICANDO_8, MULTIPLICADOR);
  and and_9 (RESULTADO_9, in_9, MULTIPLICADOR);
  and and_10 (RESULTADO_10, MULTIPLICANDO_10, MULTIPLICADOR);
  and and_11 (RESULTADO_11, MULTIPLICANDO_11, MULTIPLICADOR);
  and and_12 (RESULTADO_12, in_12, MULTIPLICADOR);
  and and_13 (RESULTADO_13, in_13, MULTIPLICADOR);
  and and_14 (RESULTADO_14, in_14, MULTIPLICADOR);
  and and_15 (RESULTADO_15, in_15, MULTIPLICADOR);

  // Notes on the sheet:
  //   MULTIPLICANDO 1
  //   MULTIPLICANDO 2
  //   MULTIPLICANDO 6
  //   MULTIPLICANDO 9
  //   MULTIPLICANDO 12
  //   MULTIPLICANDO 13
  //   MULTIPLICANDO 14
  //   MULTIPLICANDO 15
endmodule

module \Multiplicación_de_17___1  (
  input  ENTRADAS,
  input  in_2,
  input  MULTIPLICANDO_3,
  input  MULTIPLICANDO_4,
  input  MULTIPLICANDO_5,
  input  in_6,
  input  MULTIPLICANDO_7,
  input  MULTIPLICANDO_8,
  input  in_9,
  input  MULTIPLICANDO_10,
  input  MULTIPLICANDO_11,
  input  in_12,
  input  in_13,
  input  in_14,
  input  in_15,
  input  in_16,
  input  in_17,
  input  MULTIPLICADOR,
  output RESULTADO_1,
  output RESULTADO_2,
  output RESULTADO_3,
  output RESULTADO_4,
  output RESULTADO_5,
  output RESULTADO_6,
  output RESULTADO_7,
  output RESULTADO_8,
  output RESULTADO_9,
  output RESULTADO_10,
  output RESULTADO_11,
  output RESULTADO_12,
  output RESULTADO_13,
  output RESULTADO_14,
  output RESULTADO_15,
  output RESULTADO_16,
  output RESULTADO_17
);

  and and_1 (RESULTADO_1, ENTRADAS, MULTIPLICADOR);
  and and_2 (RESULTADO_2, in_2, MULTIPLICADOR);
  and and_3 (RESULTADO_3, MULTIPLICANDO_3, MULTIPLICADOR);
  and and_4 (RESULTADO_4, MULTIPLICANDO_4, MULTIPLICADOR);
  and and_5 (RESULTADO_5, MULTIPLICANDO_5, MULTIPLICADOR);
  and and_6 (RESULTADO_6, in_6, MULTIPLICADOR);
  and and_7 (RESULTADO_7, MULTIPLICANDO_7, MULTIPLICADOR);
  and and_8 (RESULTADO_8, MULTIPLICANDO_8, MULTIPLICADOR);
  and and_9 (RESULTADO_9, in_9, MULTIPLICADOR);
  and and_10 (RESULTADO_10, MULTIPLICANDO_10, MULTIPLICADOR);
  and and_11 (RESULTADO_11, MULTIPLICANDO_11, MULTIPLICADOR);
  and and_12 (RESULTADO_12, in_12, MULTIPLICADOR);
  and and_13 (RESULTADO_13, in_13, MULTIPLICADOR);
  and and_14 (RESULTADO_14, in_14, MULTIPLICADOR);
  and and_15 (RESULTADO_15, in_15, MULTIPLICADOR);
  and and_16 (RESULTADO_16, in_16, MULTIPLICADOR);
  and and_17 (RESULTADO_17, in_17, MULTIPLICADOR);

  // Notes on the sheet:
  //   MULTIPLICANDO 1
  //   MULTIPLICANDO 2
  //   MULTIPLICANDO 6
  //   MULTIPLICANDO 9
  //   MULTIPLICANDO 12
  //   MULTIPLICANDO 13
  //   MULTIPLICANDO 14
  //   MULTIPLICANDO 15
  //   MULTIPLICANDO 16
  //   MULTIPLICANDO 17
endmodule

module \Elección_Potencia_p___0  (
  input  EXPONENTE,
  input  E2,
  input  E3,
  input  BASE,
  input  B2,
  input  B3,
  output out_7,
  output out_8,
  output out_9
);

  wire and_1_out, and_2_out, and_3_out, not_1_out, not_2_out, not_3_out, not_4_out, not_5_out;

  not not_1 (not_1_out, EXPONENTE);
  not not_2 (not_2_out, E2);
  not not_3 (not_3_out, E3);
  not not_4 (not_4_out, BASE);
  not not_5 (not_5_out, B2);
  and and_1 (and_1_out, not_1_out, not_2_out, not_3_out);
  and and_2 (and_2_out, not_4_out, not_5_out, B3);
  and and_3 (and_3_out, and_2_out, B2);
  and and_4 (out_9, and_1_out, and_3_out);
  and and_5 (out_8, and_1_out, and_3_out);
  or or_1 (out_7, and_1_out, and_3_out);

  // Notes on the sheet:
  //   E1
  //   B1
endmodule

module \Elección_Potencia_p___1  (
  input  EXPONENTE,
  input  E2,
  input  E3,
  input  BASE,
  input  B2,
  input  B3,
  output out_7,
  output out_8,
  output out_9
);

  wire and_1_out, not_1_out, not_2_out;

  not not_1 (not_1_out, EXPONENTE);
  not not_2 (not_2_out, E2);
  and and_1 (and_1_out, not_1_out, not_2_out, E3);
  and and_2 (out_9, and_1_out, B3);
  and and_3 (out_8, and_1_out, B2);
  and and_4 (out_7, and_1_out, BASE);

  // Notes on the sheet:
  //   E1
  //   B1
endmodule

module Potencia__P___P (
  input  E1,
  input  E2,
  input  E3,
  output out_4,
  output out_5,
  output out_6,
  output out_7,
  output out_8,
  output out_9
);

  wire \multiplicación_de_3_1_1_resultado_1 , \multiplicación_de_3_1_1_resultado_2 ,
       \multiplicación_de_3_1_2_resultado_1 , \multiplicación_de_3_1_2_resultado_2 ,
       \multiplicación_de_3_1_2_resultado_3 , \multiplicación_de_3_1_3_resultado_1 ,
       \multiplicación_de_3_1_3_resultado_2 , \multiplicación_de_3_1_3_resultado_3 ,
       suma_de_2_entradas_1_acarreo_1, suma_de_3_entradas_1_acarreo_1, suma_de_4_entradas_1_acarreo_1,
       suma_de_4_entradas_1_acarreo_2;

  \Multiplicación_de_3___1  \multiplicación_de_3_1_1  (
    .ENTRADAS(E1), .in_2(E2), .MULTIPLICANDO_3(E3), .MULTIPLICADOR(E3),
    .RESULTADO_1(\multiplicación_de_3_1_1_resultado_1 ), .RESULTADO_2(\multiplicación_de_3_1_1_resultado_2 ),
    .RESULTADO_3(out_7));
  \Multiplicación_de_3___1  \multiplicación_de_3_1_2  (
    .ENTRADAS(E1), .in_2(E2), .MULTIPLICANDO_3(E3), .MULTIPLICADOR(E2),
    .RESULTADO_1(\multiplicación_de_3_1_2_resultado_1 ), .RESULTADO_2(\multiplicación_de_3_1_2_resultado_2 ),
    .RESULTADO_3(\multiplicación_de_3_1_2_resultado_3 ));
  \Multiplicación_de_3___1  \multiplicación_de_3_1_3  (
    .ENTRADAS(E1), .in_2(E2), .MULTIPLICANDO_3(E3), .MULTIPLICADOR(E1),
    .RESULTADO_1(\multiplicación_de_3_1_3_resultado_1 ), .RESULTADO_2(\multiplicación_de_3_1_3_resultado_2 ),
    .RESULTADO_3(\multiplicación_de_3_1_3_resultado_3 ));
  Suma_de_2_Entradas suma_de_2_entradas_1 (
    .E1(\multiplicación_de_3_1_1_resultado_2 ), .E2(\multiplicación_de_3_1_2_resultado_3 ),
    .ACARREO_1(suma_de_2_entradas_1_acarreo_1), .out_3(out_4));
  Suma_de_4_Entradas suma_de_4_entradas_1 (
    .E1(suma_de_2_entradas_1_acarreo_1), .E2(\multiplicación_de_3_1_1_resultado_1 ),
    .E3(\multiplicación_de_3_1_2_resultado_2 ), .E4(\multiplicación_de_3_1_3_resultado_3 ), .out_5(out_5),
    .ACARREO_1(suma_de_4_entradas_1_acarreo_1), .ACARREO_2(suma_de_4_entradas_1_acarreo_2));
  Suma_de_3_Entradas suma_de_3_entradas_1 (
    .E1(suma_de_4_entradas_1_acarreo_1), .E2(\multiplicación_de_3_1_2_resultado_1 ),
    .E3(\multiplicación_de_3_1_3_resultado_2 ), .out_4(out_8), .ACARREO_1(suma_de_3_entradas_1_acarreo_1));
  Suma_de_3_Entradas suma_de_3_entradas_2 (
    .E1(suma_de_4_entradas_1_acarreo_2), .E2(suma_de_3_entradas_1_acarreo_1),
    .E3(\multiplicación_de_3_1_3_resultado_1 ), .out_4(out_6), .ACARREO_1(out_9));

  // Notes on the sheet:
  //   ENTRADAS
endmodule

module \Elección_Potencia_p___2  (
  input  E1,
  input  E2,
  input  E3,
  input  BASE,
  input  B2,
  input  B3,
  output out_7,
  output out_8,
  output out_9,
  output out_10,
  output out_11,
  output out_12
);

  wire and_1_out, \multiplicación_de_3_1_1_resultado_1 , \multiplicación_de_3_1_1_resultado_2 ,
       \multiplicación_de_3_1_1_resultado_3 , \multiplicación_de_3_1_2_resultado_1 ,
       \multiplicación_de_3_1_2_resultado_2 , \multiplicación_de_3_1_2_resultado_3 ,
       \multiplicación_de_3_1_3_resultado_1 , \multiplicación_de_3_1_3_resultado_2 ,
       \multiplicación_de_3_1_3_resultado_3 , not_1_out, not_2_out, suma_de_2_entradas_1_acarreo_1,
       suma_de_2_entradas_1_out_3, suma_de_3_entradas_1_acarreo_1, suma_de_3_entradas_1_out_4,
       suma_de_3_entradas_2_acarreo_1, suma_de_3_entradas_2_out_4, suma_de_4_entradas_1_acarreo_1,
       suma_de_4_entradas_1_acarreo_2, suma_de_4_entradas_1_out_5;

  not not_1 (not_1_out, E1);
  not not_2 (not_2_out, E3);
  and and_1 (and_1_out, not_1_out, E2, not_2_out);
  \Multiplicación_de_3___1  \multiplicación_de_3_1_1  (
    .ENTRADAS(BASE), .in_2(B2), .MULTIPLICANDO_3(B3), .MULTIPLICADOR(B3),
    .RESULTADO_1(\multiplicación_de_3_1_1_resultado_1 ), .RESULTADO_2(\multiplicación_de_3_1_1_resultado_2 ),
    .RESULTADO_3(\multiplicación_de_3_1_1_resultado_3 ));
  \Multiplicación_de_3___1  \multiplicación_de_3_1_2  (
    .ENTRADAS(BASE), .in_2(B2), .MULTIPLICANDO_3(B3), .MULTIPLICADOR(B2),
    .RESULTADO_1(\multiplicación_de_3_1_2_resultado_1 ), .RESULTADO_2(\multiplicación_de_3_1_2_resultado_2 ),
    .RESULTADO_3(\multiplicación_de_3_1_2_resultado_3 ));
  \Multiplicación_de_3___1  \multiplicación_de_3_1_3  (
    .ENTRADAS(BASE), .in_2(B2), .MULTIPLICANDO_3(B3), .MULTIPLICADOR(BASE),
    .RESULTADO_1(\multiplicación_de_3_1_3_resultado_1 ), .RESULTADO_2(\multiplicación_de_3_1_3_resultado_2 ),
    .RESULTADO_3(\multiplicación_de_3_1_3_resultado_3 ));
  and and_2 (out_12, and_1_out, \multiplicación_de_3_1_1_resultado_3 );
  and and_3 (out_11, and_1_out, suma_de_2_entradas_1_out_3);
  Suma_de_2_Entradas suma_de_2_entradas_1 (
    .E1(\multiplicación_de_3_1_1_resultado_2 ), .E2(\multiplicación_de_3_1_2_resultado_3 ),
    .ACARREO_1(suma_de_2_entradas_1_acarreo_1), .out_3(suma_de_2_entradas_1_out_3));
  Suma_de_4_Entradas suma_de_4_entradas_1 (
    .E1(suma_de_2_entradas_1_acarreo_1), .E2(\multiplicación_de_3_1_1_resultado_1 ),
    .E3(\multiplicación_de_3_1_2_resultado_2 ), .E4(\multiplicación_de_3_1_3_resultado_3 ),
    .out_5(suma_de_4_entradas_1_out_5), .ACARREO_1(suma_de_4_entradas_1_acarreo_1),
    .ACARREO_2(suma_de_4_entradas_1_acarreo_2));
  and and_4 (out_10, and_1_out, suma_de_4_entradas_1_out_5);
  Suma_de_3_Entradas suma_de_3_entradas_1 (
    .E1(suma_de_4_entradas_1_acarreo_1), .E2(\multiplicación_de_3_1_2_resultado_1 ),
    .E3(\multiplicación_de_3_1_3_resultado_2 ), .out_4(suma_de_3_entradas_1_out_4),
    .ACARREO_1(suma_de_3_entradas_1_acarreo_1));
  and and_5 (out_9, and_1_out, suma_de_3_entradas_1_out_4);
  and and_6 (out_8, and_1_out, suma_de_3_entradas_2_out_4);
  Suma_de_3_Entradas suma_de_3_entradas_2 (
    .E1(suma_de_4_entradas_1_acarreo_2), .E2(suma_de_3_entradas_1_acarreo_1),
    .E3(\multiplicación_de_3_1_3_resultado_1 ), .out_4(suma_de_3_entradas_2_out_4),
    .ACARREO_1(suma_de_3_entradas_2_acarreo_1));
  and and_7 (out_7, and_1_out, suma_de_3_entradas_2_acarreo_1);

  // Notes on the sheet:
  //   EXPONENTE
  //   B1
endmodule

module Potencia__P___P___P (
  input  E1,
  input  E2,
  input  E3,
  output out_4,
  output out_5,
  output out_6,
  output out_7,
  output out_8,
  output out_9,
  output out_10,
  output out_11,
  output out_12
);

  wire \multiplicación_de_6_1_1_resultado_1 , \multiplicación_de_6_1_1_resultado_2 ,
       \multiplicación_de_6_1_1_resultado_3 , \multiplicación_de_6_1_1_resultado_4 ,
       \multiplicación_de_6_1_1_resultado_5 , \multiplicación_de_6_1_2_resultado_1 ,
       \multiplicación_de_6_1_2_resultado_2 , \multiplicación_de_6_1_2_resultado_3 ,
       \multiplicación_de_6_1_2_resultado_4 , \multiplicación_de_6_1_2_resultado_5 ,
       \multiplicación_de_6_1_2_resultado_6 , \multiplicación_de_6_1_3_resultado_1 ,
       \multiplicación_de_6_1_3_resultado_2 , \multiplicación_de_6_1_3_resultado_3 ,
       \multiplicación_de_6_1_3_resultado_4 , \multiplicación_de_6_1_3_resultado_5 ,
       \multiplicación_de_6_1_3_resultado_6 , potencia_p_p_1_out_4, potencia_p_p_1_out_5,
       potencia_p_p_1_out_6, potencia_p_p_1_out_7, potencia_p_p_1_out_8, potencia_p_p_1_out_9,
       suma_de_2_entradas_1_acarreo_1, suma_de_3_entradas_1_acarreo_1, suma_de_4_entradas_1_acarreo_1,
       suma_de_4_entradas_1_acarreo_2, suma_de_4_entradas_2_acarreo_1, suma_de_4_entradas_2_acarreo_2,
       suma_de_4_entradas_3_acarreo_1, suma_de_4_entradas_3_acarreo_2, suma_de_4_entradas_4_acarreo_1,
       suma_de_4_entradas_4_acarreo_2;

  Potencia__P___P potencia_p_p_1 (
    .E1(E1), .E2(E2), .E3(E3), .out_4(potencia_p_p_1_out_4), .out_5(potencia_p_p_1_out_5),
    .out_6(potencia_p_p_1_out_6), .out_7(potencia_p_p_1_out_7), .out_8(potencia_p_p_1_out_8),
    .out_9(potencia_p_p_1_out_9));
  \Multiplicación_de_6___1  \multiplicación_de_6_1_1  (
    .ENTRADAS(potencia_p_p_1_out_9), .in_2(potencia_p_p_1_out_6), .MULTIPLICANDO_3(potencia_p_p_1_out_8),
    .MULTIPLICANDO_4(potencia_p_p_1_out_5), .MULTIPLICANDO_5(potencia_p_p_1_out_4),
    .in_6(potencia_p_p_1_out_7), .MULTIPLICADOR(E3), .RESULTADO_1(\multiplicación_de_6_1_1_resultado_1 ),
    .RESULTADO_2(\multiplicación_de_6_1_1_resultado_2 ), .RESULTADO_3(\multiplicación_de_6_1_1_resultado_3 ),
    .RESULTADO_4(\multiplicación_de_6_1_1_resultado_4 ), .RESULTADO_5(\multiplicación_de_6_1_1_resultado_5 ),
    .RESULTADO_6(out_5));
  \Multiplicación_de_6___1  \multiplicación_de_6_1_2  (
    .ENTRADAS(potencia_p_p_1_out_9), .in_2(potencia_p_p_1_out_6), .MULTIPLICANDO_3(potencia_p_p_1_out_8),
    .MULTIPLICANDO_4(potencia_p_p_1_out_5), .MULTIPLICANDO_5(potencia_p_p_1_out_4),
    .in_6(potencia_p_p_1_out_7), .MULTIPLICADOR(E2), .RESULTADO_1(\multiplicación_de_6_1_2_resultado_1 ),
    .RESULTADO_2(\multiplicación_de_6_1_2_resultado_2 ), .RESULTADO_3(\multiplicación_de_6_1_2_resultado_3 ),
    .RESULTADO_4(\multiplicación_de_6_1_2_resultado_4 ), .RESULTADO_5(\multiplicación_de_6_1_2_resultado_5 ),
    .RESULTADO_6(\multiplicación_de_6_1_2_resultado_6 ));
  \Multiplicación_de_6___1  \multiplicación_de_6_1_3  (
    .ENTRADAS(potencia_p_p_1_out_9), .in_2(potencia_p_p_1_out_6), .MULTIPLICANDO_3(potencia_p_p_1_out_8),
    .MULTIPLICANDO_4(potencia_p_p_1_out_5), .MULTIPLICANDO_5(potencia_p_p_1_out_4),
    .in_6(potencia_p_p_1_out_7), .MULTIPLICADOR(E1), .RESULTADO_1(\multiplicación_de_6_1_3_resultado_1 ),
    .RESULTADO_2(\multiplicación_de_6_1_3_resultado_2 ), .RESULTADO_3(\multiplicación_de_6_1_3_resultado_3 ),
    .RESULTADO_4(\multiplicación_de_6_1_3_resultado_4 ), .RESULTADO_5(\multiplicación_de_6_1_3_resultado_5 ),
    .RESULTADO_6(\multiplicación_de_6_1_3_resultado_6 ));
  Suma_de_2_Entradas suma_de_2_entradas_1 (
    .E1(\multiplicación_de_6_1_1_resultado_5 ), .E2(\multiplicación_de_6_1_2_resultado_6 ),
    .ACARREO_1(suma_de_2_entradas_1_acarreo_1), .out_3(out_4));
  Suma_de_4_Entradas suma_de_4_entradas_1 (
    .E1(suma_de_2_entradas_1_acarreo_1), .E2(\multiplicación_de_6_1_1_resultado_4 ),
    .E3(\multiplicación_de_6_1_2_resultado_5 ), .E4(\multiplicación_de_6_1_3_resultado_6 ), .out_5(out_6),
    .ACARREO_1(suma_de_4_entradas_1_acarreo_1), .ACARREO_2(suma_de_4_entradas_1_acarreo_2));
  Suma_de_4_Entradas suma_de_4_entradas_2 (
    .E1(suma_de_4_entradas_1_acarreo_1), .E2(\multiplicación_de_6_1_1_resultado_3 ),
    .E3(\multiplicación_de_6_1_2_resultado_4 ), .E4(\multiplicación_de_6_1_3_resultado_5 ), .out_5(out_7),
    .ACARREO_1(suma_de_4_entradas_2_acarreo_1), .ACARREO_2(suma_de_4_entradas_2_acarreo_2));
  Suma_de_4_Entradas suma_de_4_entradas_3 (
    .E1(suma_de_4_entradas_2_acarreo_1), .E2(\multiplicación_de_6_1_1_resultado_2 ),
    .E3(\multiplicación_de_6_1_2_resultado_3 ), .E4(\multiplicación_de_6_1_3_resultado_4 ), .out_5(out_8),
    .ACARREO_1(suma_de_4_entradas_3_acarreo_1), .ACARREO_2(suma_de_4_entradas_3_acarreo_2));
  Suma_de_4_Entradas suma_de_4_entradas_4 (
    .E1(suma_de_4_entradas_3_acarreo_1), .E2(\multiplicación_de_6_1_1_resultado_1 ),
    .E3(\multiplicación_de_6_1_2_resultado_2 ), .E4(\multiplicación_de_6_1_3_resultado_3 ), .out_5(out_9),
    .ACARREO_1(suma_de_4_entradas_4_acarreo_1), .ACARREO_2(suma_de_4_entradas_4_acarreo_2));
  Suma_de_3_Entradas suma_de_3_entradas_1 (
    .E1(suma_de_4_entradas_4_acarreo_1), .E2(\multiplicación_de_6_1_2_resultado_1 ),
    .E3(\multiplicación_de_6_1_3_resultado_2 ), .out_4(out_10), .ACARREO_1(suma_de_3_entradas_1_acarreo_1));
  Suma_de_2_Entradas suma_de_2_entradas_2 (
    .E1(suma_de_3_entradas_1_acarreo_1), .E2(\multiplicación_de_6_1_3_resultado_1 ), .ACARREO_1(out_12),
    .out_3(out_11));
  // also tied to GND on the sheet: {suma_de_4_entradas_1_acarreo_2, suma_de_4_entradas_2_acarreo_2, suma_de_4_entradas_3_acarreo_2, suma_de_4_entradas_4_acarreo_2}

  // Notes on the sheet:
  //   ENTRADAS
endmodule

module \Elección_Potencia_p___3  (
  input  E1,
  input  E2,
  input  E3,
  input  BASE,
  input  B2,
  input  B3,
  output out_7,
  output out_8,
  output out_9,
  output out_10,
  output out_11,
  output out_12,
  output out_13,
  output out_14,
  output out_15
);

  wire and_1_out, \multiplicación_de_6_1_1_resultado_1 , \multiplicación_de_6_1_1_resultado_2 ,
       \multiplicación_de_6_1_1_resultado_3 , \multiplicación_de_6_1_1_resultado_4 ,
       \multiplicación_de_6_1_1_resultado_5 , \multiplicación_de_6_1_1_resultado_6 ,
       \multiplicación_de_6_1_2_resultado_1 , \multiplicación_de_6_1_2_resultado_2 ,
       \multiplicación_de_6_1_2_resultado_3 , \multiplicación_de_6_1_2_resultado_4 ,
       \multiplicación_de_6_1_2_resultado_5 , \multiplicación_de_6_1_2_resultado_6 ,
       \multiplicación_de_6_1_3_resultado_1 , \multiplicación_de_6_1_3_resultado_2 ,
       \multiplicación_de_6_1_3_resultado_3 , \multiplicación_de_6_1_3_resultado_4 ,
       \multiplicación_de_6_1_3_resultado_5 , \multiplicación_de_6_1_3_resultado_6 , not_1_out,
       potencia_p_p_1_out_4, potencia_p_p_1_out_5, potencia_p_p_1_out_6, potencia_p_p_1_out_7,
       potencia_p_p_1_out_8, potencia_p_p_1_out_9, suma_de_2_entradas_1_acarreo_1,
       suma_de_2_entradas_1_out_3, suma_de_2_entradas_2_acarreo_1, suma_de_2_entradas_2_out_3,
       suma_de_3_entradas_1_acarreo_1, suma_de_3_entradas_1_out_4, suma_de_4_entradas_1_acarreo_1,
       suma_de_4_entradas_1_acarreo_2, suma_de_4_entradas_1_out_5, suma_de_4_entradas_2_acarreo_1,
       suma_de_4_entradas_2_acarreo_2, suma_de_4_entradas_2_out_5, suma_de_4_entradas_3_acarreo_1,
       suma_de_4_entradas_3_acarreo_2, suma_de_4_entradas_3_out_5, suma_de_4_entradas_4_acarreo_1,
       suma_de_4_entradas_4_acarreo_2, suma_de_4_entradas_4_out_5;

  not not_1 (not_1_out, E1);
  Potencia__P___P potencia_p_p_1 (
    .E1(BASE), .E2(B2), .E3(B3), .out_4(potencia_p_p_1_out_4), .out_5(potencia_p_p_1_out_5),
    .out_6(potencia_p_p_1_out_6), .out_7(potencia_p_p_1_out_7), .out_8(potencia_p_p_1_out_8),
    .out_9(potencia_p_p_1_out_9));
  and and_1 (and_1_out, not_1_out, E2, E3);
  \Multiplicación_de_6___1  \multiplicación_de_6_1_1  (
    .ENTRADAS(potencia_p_p_1_out_9), .in_2(potencia_p_p_1_out_6), .MULTIPLICANDO_3(potencia_p_p_1_out_8),
    .MULTIPLICANDO_4(potencia_p_p_1_out_5), .MULTIPLICANDO_5(potencia_p_p_1_out_4),
    .in_6(potencia_p_p_1_out_7), .MULTIPLICADOR(B3), .RESULTADO_1(\multiplicación_de_6_1_1_resultado_1 ),
    .RESULTADO_2(\multiplicación_de_6_1_1_resultado_2 ), .RESULTADO_3(\multiplicación_de_6_1_1_resultado_3 ),
    .RESULTADO_4(\multiplicación_de_6_1_1_resultado_4 ), .RESULTADO_5(\multiplicación_de_6_1_1_resultado_5 ),
    .RESULTADO_6(\multiplicación_de_6_1_1_resultado_6 ));
  \Multiplicación_de_6___1  \multiplicación_de_6_1_2  (
    .ENTRADAS(potencia_p_p_1_out_9), .in_2(potencia_p_p_1_out_6), .MULTIPLICANDO_3(potencia_p_p_1_out_8),
    .MULTIPLICANDO_4(potencia_p_p_1_out_5), .MULTIPLICANDO_5(potencia_p_p_1_out_4),
    .in_6(potencia_p_p_1_out_7), .MULTIPLICADOR(B2), .RESULTADO_1(\multiplicación_de_6_1_2_resultado_1 ),
    .RESULTADO_2(\multiplicación_de_6_1_2_resultado_2 ), .RESULTADO_3(\multiplicación_de_6_1_2_resultado_3 ),
    .RESULTADO_4(\multiplicación_de_6_1_2_resultado_4 ), .RESULTADO_5(\multiplicación_de_6_1_2_resultado_5 ),
    .RESULTADO_6(\multiplicación_de_6_1_2_resultado_6 ));
  \Multiplicación_de_6___1  \multiplicación_de_6_1_3  (
    .ENTRADAS(potencia_p_p_1_out_9), .in_2(potencia_p_p_1_out_6), .MULTIPLICANDO_3(potencia_p_p_1_out_8),
    .MULTIPLICANDO_4(potencia_p_p_1_out_5), .MULTIPLICANDO_5(potencia_p_p_1_out_4),
    .in_6(potencia_p_p_1_out_7), .MULTIPLICADOR(BASE), .RESULTADO_1(\multiplicación_de_6_1_3_resultado_1 ),
    .RESULTADO_2(\multiplicación_de_6_1_3_resultado_2 ), .RESULTADO_3(\multiplicación_de_6_1_3_resultado_3 ),
    .RESULTADO_4(\multiplicación_de_6_1_3_resultado_4 ), .RESULTADO_5(\multiplicación_de_6_1_3_resultado_5 ),
    .RESULTADO_6(\multiplicación_de_6_1_3_resultado_6 ));
  and and_2 (out_15, and_1_out, \multiplicación_de_6_1_1_resultado_6 );
  Suma_de_2_Entradas suma_de_2_entradas_1 (
    .E1(\multiplicación_de_6_1_1_resultado_5 ), .E2(\multiplicación_de_6_1_2_resultado_6 ),
    .ACARREO_1(suma_de_2_entradas_1_acarreo_1), .out_3(suma_de_2_entradas_1_out_3));
  and and_3 (out_14, and_1_out, suma_de_2_entradas_1_out_3);
  Suma_de_4_Entradas suma_de_4_entradas_1 (
    .E1(suma_de_2_entradas_1_acarreo_1), .E2(\multiplicación_de_6_1_1_resultado_4 ),
    .E3(\multiplicación_de_6_1_2_resultado_5 ), .E4(\multiplicación_de_6_1_3_resultado_6 ),
    .out_5(suma_de_4_entradas_1_out_5), .ACARREO_1(suma_de_4_entradas_1_acarreo_1),
    .ACARREO_2(suma_de_4_entradas_1_acarreo_2));
  and and_4 (out_13, and_1_out, suma_de_4_entradas_1_out_5);
  Suma_de_4_Entradas suma_de_4_entradas_2 (
    .E1(suma_de_4_entradas_1_acarreo_1), .E2(\multiplicación_de_6_1_1_resultado_3 ),
    .E3(\multiplicación_de_6_1_2_resultado_4 ), .E4(\multiplicación_de_6_1_3_resultado_5 ),
    .out_5(suma_de_4_entradas_2_out_5), .ACARREO_1(suma_de_4_entradas_2_acarreo_1),
    .ACARREO_2(suma_de_4_entradas_2_acarreo_2));
  and and_5 (out_12, and_1_out, suma_de_4_entradas_2_out_5);
  Suma_de_4_Entradas suma_de_4_entradas_3 (
    .E1(suma_de_4_entradas_2_acarreo_1), .E2(\multiplicación_de_6_1_1_resultado_2 ),
    .E3(\multiplicación_de_6_1_2_resultado_3 ), .E4(\multiplicación_de_6_1_3_resultado_4 ),
    .out_5(suma_de_4_entradas_3_out_5), .ACARREO_1(suma_de_4_entradas_3_acarreo_1),
    .ACARREO_2(suma_de_4_entradas_3_acarreo_2));
  Suma_de_4_Entradas suma_de_4_entradas_4 (
    .E1(suma_de_4_entradas_3_acarreo_1), .E2(\multiplicación_de_6_1_1_resultado_1 ),
    .E3(\multiplicación_de_6_1_2_resultado_2 ), .E4(\multiplicación_de_6_1_3_resultado_3 ),
    .out_5(suma_de_4_entradas_4_out_5), .ACARREO_1(suma_de_4_entradas_4_acarreo_1),
    .ACARREO_2(suma_de_4_entradas_4_acarreo_2));
  and and_6 (out_11, and_1_out, suma_de_4_entradas_3_out_5);
  Suma_de_3_Entradas suma_de_3_entradas_1 (
    .E1(suma_de_4_entradas_4_acarreo_1), .E2(\multiplicación_de_6_1_2_resultado_1 ),
    .E3(\multiplicación_de_6_1_3_resultado_2 ), .out_4(suma_de_3_entradas_1_out_4),
    .ACARREO_1(suma_de_3_entradas_1_acarreo_1));
  and and_7 (out_10, and_1_out, suma_de_4_entradas_4_out_5);
  Suma_de_2_Entradas suma_de_2_entradas_2 (
    .E1(suma_de_3_entradas_1_acarreo_1), .E2(\multiplicación_de_6_1_3_resultado_1 ),
    .ACARREO_1(suma_de_2_entradas_2_acarreo_1), .out_3(suma_de_2_entradas_2_out_3));
  and and_8 (out_9, and_1_out, suma_de_3_entradas_1_out_4);
  and and_9 (out_8, and_1_out, suma_de_2_entradas_2_out_3);
  and and_10 (out_7, and_1_out, suma_de_2_entradas_2_acarreo_1);
  // also tied to GND on the sheet: {suma_de_4_entradas_1_acarreo_2, suma_de_4_entradas_2_acarreo_2, suma_de_4_entradas_3_acarreo_2, suma_de_4_entradas_4_acarreo_2}

  // Notes on the sheet:
  //   EXPONENTE
  //   B1
endmodule

module Potencia__P___P___P___P (
  input  E1,
  input  E2,
  input  E3,
  output out_4,
  output out_5,
  output out_6,
  output out_7,
  output out_8,
  output out_9,
  output out_10,
  output out_11,
  output out_12,
  output out_13,
  output out_14,
  output out_15
);

  wire \multiplicación_de_9_1_1_resultado_1 , \multiplicación_de_9_1_1_resultado_2 ,
       \multiplicación_de_9_1_1_resultado_3 , \multiplicación_de_9_1_1_resultado_4 ,
       \multiplicación_de_9_1_1_resultado_5 , \multiplicación_de_9_1_1_resultado_6 ,
       \multiplicación_de_9_1_1_resultado_7 , \multiplicación_de_9_1_1_resultado_8 ,
       \multiplicación_de_9_1_2_resultado_1 , \multiplicación_de_9_1_2_resultado_2 ,
       \multiplicación_de_9_1_2_resultado_3 , \multiplicación_de_9_1_2_resultado_4 ,
       \multiplicación_de_9_1_2_resultado_5 , \multiplicación_de_9_1_2_resultado_6 ,
       \multiplicación_de_9_1_2_resultado_7 , \multiplicación_de_9_1_2_resultado_8 ,
       \multiplicación_de_9_1_2_resultado_9 , \multiplicación_de_9_1_3_resultado_1 ,
       \multiplicación_de_9_1_3_resultado_2 , \multiplicación_de_9_1_3_resultado_3 ,
       \multiplicación_de_9_1_3_resultado_4 , \multiplicación_de_9_1_3_resultado_5 ,
       \multiplicación_de_9_1_3_resultado_6 , \multiplicación_de_9_1_3_resultado_7 ,
       \multiplicación_de_9_1_3_resultado_8 , \multiplicación_de_9_1_3_resultado_9 , potencia_p_p_p_1_out_4,
       potencia_p_p_p_1_out_5, potencia_p_p_p_1_out_6, potencia_p_p_p_1_out_7, potencia_p_p_p_1_out_8,
       potencia_p_p_p_1_out_9, potencia_p_p_p_1_out_10, potencia_p_p_p_1_out_11, potencia_p_p_p_1_out_12,
       suma_de_2_entradas_1_acarreo_1, suma_de_3_entradas_1_acarreo_1, suma_de_4_entradas_1_acarreo_1,
       suma_de_4_entradas_1_acarreo_2, suma_de_4_entradas_2_acarreo_1, suma_de_4_entradas_2_acarreo_2,
       suma_de_4_entradas_3_acarreo_1, suma_de_4_entradas_3_acarreo_2, suma_de_4_entradas_4_acarreo_1,
       suma_de_4_entradas_4_acarreo_2, suma_de_4_entradas_5_acarreo_1, suma_de_4_entradas_5_acarreo_2,
       suma_de_5_entradas_1_acarreo_1, suma_de_5_entradas_1_acarreo_2, suma_de_5_entradas_2_acarreo_1,
       suma_de_5_entradas_2_acarreo_2;

  Potencia__P___P___P potencia_p_p_p_1 (
    .E1(E1), .E2(E2), .E3(E3), .out_4(potencia_p_p_p_1_out_4), .out_5(potencia_p_p_p_1_out_5),
    .out_6(potencia_p_p_p_1_out_6), .out_7(potencia_p_p_p_1_out_7), .out_8(potencia_p_p_p_1_out_8),
    .out_9(potencia_p_p_p_1_out_9), .out_10(potencia_p_p_p_1_out_10), .out_11(potencia_p_p_p_1_out_11),
    .out_12(potencia_p_p_p_1_out_12));
  \Multiplicación_de_9___1  \multiplicación_de_9_1_1  (
    .ENTRADAS(potencia_p_p_p_1_out_12), .in_2(potencia_p_p_p_1_out_11),
    .MULTIPLICANDO_3(potencia_p_p_p_1_out_10), .MULTIPLICANDO_4(potencia_p_p_p_1_out_9),
    .MULTIPLICANDO_5(potencia_p_p_p_1_out_8), .in_6(potencia_p_p_p_1_out_7),
    .MULTIPLICANDO_7(potencia_p_p_p_1_out_6), .MULTIPLICANDO_8(potencia_p_p_p_1_out_4),
    .in_9(potencia_p_p_p_1_out_5), .MULTIPLICADOR(E3), .RESULTADO_1(\multiplicación_de_9_1_1_resultado_1 ),
    .RESULTADO_2(\multiplicación_de_9_1_1_resultado_2 ), .RESULTADO_3(\multiplicación_de_9_1_1_resultado_3 ),
    .RESULTADO_4(\multiplicación_de_9_1_1_resultado_4 ), .RESULTADO_5(\multiplicación_de_9_1_1_resultado_5 ),
    .RESULTADO_6(\multiplicación_de_9_1_1_resultado_6 ), .RESULTADO_7(\multiplicación_de_9_1_1_resultado_7 ),
    .RESULTADO_8(\multiplicación_de_9_1_1_resultado_8 ), .RESULTADO_9(out_5));
  \Multiplicación_de_9___1  \multiplicación_de_9_1_2  (
    .ENTRADAS(potencia_p_p_p_1_out_12), .in_2(potencia_p_p_p_1_out_11),
    .MULTIPLICANDO_3(potencia_p_p_p_1_out_10), .MULTIPLICANDO_4(potencia_p_p_p_1_out_9),
    .MULTIPLICANDO_5(potencia_p_p_p_1_out_8), .in_6(potencia_p_p_p_1_out_7),
    .MULTIPLICANDO_7(potencia_p_p_p_1_out_6), .MULTIPLICANDO_8(potencia_p_p_p_1_out_4),
    .in_9(potencia_p_p_p_1_out_5), .MULTIPLICADOR(E2), .RESULTADO_1(\multiplicación_de_9_1_2_resultado_1 ),
    .RESULTADO_2(\multiplicación_de_9_1_2_resultado_2 ), .RESULTADO_3(\multiplicación_de_9_1_2_resultado_3 ),
    .RESULTADO_4(\multiplicación_de_9_1_2_resultado_4 ), .RESULTADO_5(\multiplicación_de_9_1_2_resultado_5 ),
    .RESULTADO_6(\multiplicación_de_9_1_2_resultado_6 ), .RESULTADO_7(\multiplicación_de_9_1_2_resultado_7 ),
    .RESULTADO_8(\multiplicación_de_9_1_2_resultado_8 ), .RESULTADO_9(\multiplicación_de_9_1_2_resultado_9 ));
  \Multiplicación_de_9___1  \multiplicación_de_9_1_3  (
    .ENTRADAS(potencia_p_p_p_1_out_12), .in_2(potencia_p_p_p_1_out_11),
    .MULTIPLICANDO_3(potencia_p_p_p_1_out_10), .MULTIPLICANDO_4(potencia_p_p_p_1_out_9),
    .MULTIPLICANDO_5(potencia_p_p_p_1_out_8), .in_6(potencia_p_p_p_1_out_7),
    .MULTIPLICANDO_7(potencia_p_p_p_1_out_6), .MULTIPLICANDO_8(potencia_p_p_p_1_out_4),
    .in_9(potencia_p_p_p_1_out_5), .MULTIPLICADOR(E1), .RESULTADO_1(\multiplicación_de_9_1_3_resultado_1 ),
    .RESULTADO_2(\multiplicación_de_9_1_3_resultado_2 ), .RESULTADO_3(\multiplicación_de_9_1_3_resultado_3 ),
    .RESULTADO_4(\multiplicación_de_9_1_3_resultado_4 ), .RESULTADO_5(\multiplicación_de_9_1_3_resultado_5 ),
    .RESULTADO_6(\multiplicación_de_9_1_3_resultado_6 ), .RESULTADO_7(\multiplicación_de_9_1_3_resultado_7 ),
    .RESULTADO_8(\multiplicación_de_9_1_3_resultado_8 ), .RESULTADO_9(\multiplicación_de_9_1_3_resultado_9 ));
  Suma_de_2_Entradas suma_de_2_entradas_1 (
    .E1(\multiplicación_de_9_1_1_resultado_8 ), .E2(\multiplicación_de_9_1_2_resultado_9 ),
    .ACARREO_1(suma_de_2_entradas_1_acarreo_1), .out_3(out_4));
  Suma_de_4_Entradas suma_de_4_entradas_1 (
    .E1(suma_de_2_entradas_1_acarreo_1), .E2(\multiplicación_de_9_1_1_resultado_7 ),
    .E3(\multiplicación_de_9_1_2_resultado_8 ), .E4(\multiplicación_de_9_1_3_resultado_9 ), .out_5(out_6),
    .ACARREO_1(suma_de_4_entradas_1_acarreo_1), .ACARREO_2(suma_de_4_entradas_1_acarreo_2));
  Suma_de_4_Entradas suma_de_4_entradas_2 (
    .E1(suma_de_4_entradas_1_acarreo_1), .E2(\multiplicación_de_9_1_1_resultado_6 ),
    .E3(\multiplicación_de_9_1_2_resultado_7 ), .E4(\multiplicación_de_9_1_3_resultado_8 ), .out_5(out_7),
    .ACARREO_1(suma_de_4_entradas_2_acarreo_1), .ACARREO_2(suma_de_4_entradas_2_acarreo_2));
  Suma_de_5_Entradas suma_de_5_entradas_1 (
    .E1(suma_de_4_entradas_1_acarreo_2), .E2(suma_de_4_entradas_2_acarreo_1),
    .E3(\multiplicación_de_9_1_1_resultado_5 ), .E4(\multiplicación_de_9_1_2_resultado_6 ),
    .E5(\multiplicación_de_9_1_3_resultado_7 ), .out_6(out_8), .ACARREO_1(suma_de_5_entradas_1_acarreo_1),
    .ACARREO_2(suma_de_5_entradas_1_acarreo_2));
  Suma_de_4_Entradas suma_de_4_entradas_3 (
    .E1(suma_de_5_entradas_1_acarreo_1), .E2(\multiplicación_de_9_1_1_resultado_4 ),
    .E3(\multiplicación_de_9_1_2_resultado_5 ), .E4(\multiplicación_de_9_1_3_resultado_6 ), .out_5(out_9),
    .ACARREO_1(suma_de_4_entradas_3_acarreo_1), .ACARREO_2(suma_de_4_entradas_3_acarreo_2));
  Suma_de_5_Entradas suma_de_5_entradas_2 (
    .E1(suma_de_5_entradas_1_acarreo_2), .E2(suma_de_4_entradas_3_acarreo_1),
    .E3(\multiplicación_de_9_1_1_resultado_3 ), .E4(\multiplicación_de_9_1_2_resultado_4 ),
    .E5(\multiplicación_de_9_1_3_resultado_5 ), .out_6(out_10), .ACARREO_1(suma_de_5_entradas_2_acarreo_1),
    .ACARREO_2(suma_de_5_entradas_2_acarreo_2));
  Suma_de_4_Entradas suma_de_4_entradas_4 (
    .E1(suma_de_5_entradas_2_acarreo_1), .E2(\multiplicación_de_9_1_1_resultado_2 ),
    .E3(\multiplicación_de_9_1_2_resultado_3 ), .E4(\multiplicación_de_9_1_3_resultado_4 ), .out_5(out_11),
    .ACARREO_1(suma_de_4_entradas_4_acarreo_1), .ACARREO_2(suma_de_4_entradas_4_acarreo_2));
  Suma_de_4_Entradas suma_de_4_entradas_5 (
    .E1(suma_de_4_entradas_4_acarreo_1), .E2(\multiplicación_de_9_1_1_resultado_1 ),
    .E3(\multiplicación_de_9_1_2_resultado_2 ), .E4(\multiplicación_de_9_1_3_resultado_3 ), .out_5(out_12),
    .ACARREO_1(suma_de_4_entradas_5_acarreo_1), .ACARREO_2(suma_de_4_entradas_5_acarreo_2));
  Suma_de_3_Entradas suma_de_3_entradas_1 (
    .E1(suma_de_4_entradas_5_acarreo_1), .E2(\multiplicación_de_9_1_2_resultado_1 ),
    .E3(\multiplicación_de_9_1_3_resultado_2 ), .out_4(out_13), .ACARREO_1(suma_de_3_entradas_1_acarreo_1));
  Suma_de_2_Entradas suma_de_2_entradas_2 (
    .E1(suma_de_3_entradas_1_acarreo_1), .E2(\multiplicación_de_9_1_3_resultado_1 ), .ACARREO_1(out_15),
    .out_3(out_14));
  // also tied to GND on the sheet: {suma_de_4_entradas_2_acarreo_2, suma_de_4_entradas_3_acarreo_2, suma_de_5_entradas_2_acarreo_2, suma_de_4_entradas_4_acarreo_2, suma_de_4_entradas_5_acarreo_2}

  // Notes on the sheet:
  //   ENTRADAS
endmodule

module \Elección_Potencia_p___4  (
  input  E1,
  input  E2,
  input  E3,
  input  BASE,
  input  B2,
  input  B3,
  output out_7,
  output out_8,
  output out_9,
  output out_10,
  output out_11,
  output out_12,
  output out_13,
  output out_14,
  output out_15,
  output out_16,
  output out_17,
  output out_18
);

  wire and_1_out, \multiplicación_de_9_1_1_resultado_1 , \multiplicación_de_9_1_1_resultado_2 ,
       \multiplicación_de_9_1_1_resultado_3 , \multiplicación_de_9_1_1_resultado_4 ,
       \multiplicación_de_9_1_1_resultado_5 , \multiplicación_de_9_1_1_resultado_6 ,
       \multiplicación_de_9_1_1_resultado_7 , \multiplicación_de_9_1_1_resultado_8 ,
       \multiplicación_de_9_1_1_resultado_9 , \multiplicación_de_9_1_2_resultado_1 ,
       \multiplicación_de_9_1_2_resultado_2 , \multiplicación_de_9_1_2_resultado_3 ,
       \multiplicación_de_9_1_2_resultado_4 , \multiplicación_de_9_1_2_resultado_5 ,
       \multiplicación_de_9_1_2_resultado_6 , \multiplicación_de_9_1_2_resultado_7 ,
       \multiplicación_de_9_1_2_resultado_8 , \multiplicación_de_9_1_2_resultado_9 ,
       \multiplicación_de_9_1_3_resultado_1 , \multiplicación_de_9_1_3_resultado_2 ,
       \multiplicación_de_9_1_3_resultado_3 , \multiplicación_de_9_1_3_resultado_4 ,
       \multiplicación_de_9_1_3_resultado_5 , \multiplicación_de_9_1_3_resultado_6 ,
       \multiplicación_de_9_1_3_resultado_7 , \multiplicación_de_9_1_3_resultado_8 ,
       \multiplicación_de_9_1_3_resultado_9 , not_1_out, not_2_out, potencia_p_p_p_1_out_4,
       potencia_p_p_p_1_out_5, potencia_p_p_p_1_out_6, potencia_p_p_p_1_out_7, potencia_p_p_p_1_out_8,
       potencia_p_p_p_1_out_9, potencia_p_p_p_1_out_10, potencia_p_p_p_1_out_11, potencia_p_p_p_1_out_12,
       suma_de_2_entradas_1_acarreo_1, suma_de_2_entradas_1_out_3, suma_de_2_entradas_2_acarreo_1,
       suma_de_2_entradas_2_out_3, suma_de_3_entradas_1_acarreo_1, suma_de_3_entradas_1_out_4,
       suma_de_4_entradas_1_acarreo_1, suma_de_4_entradas_1_acarreo_2, suma_de_4_entradas_1_out_5,
       suma_de_4_entradas_2_acarreo_1, suma_de_4_entradas_2_acarreo_2, suma_de_4_entradas_2_out_5,
       suma_de_4_entradas_3_acarreo_1, suma_de_4_entradas_3_acarreo_2, suma_de_4_entradas_3_out_5,
       suma_de_4_entradas_4_acarreo_1, suma_de_4_entradas_4_acarreo_2, suma_de_4_entradas_4_out_5,
       suma_de_4_entradas_5_acarreo_1, suma_de_4_entradas_5_acarreo_2, suma_de_4_entradas_5_out_5,
       suma_de_5_entradas_1_acarreo_1, suma_de_5_entradas_1_acarreo_2, suma_de_5_entradas_1_out_6,
       suma_de_5_entradas_2_acarreo_1, suma_de_5_entradas_2_acarreo_2, suma_de_5_entradas_2_out_6;

  not not_1 (not_1_out, E2);
  not not_2 (not_2_out, E3);
  Potencia__P___P___P potencia_p_p_p_1 (
    .E1(BASE), .E2(B2), .E3(B3), .out_4(potencia_p_p_p_1_out_4), .out_5(potencia_p_p_p_1_out_5),
    .out_6(potencia_p_p_p_1_out_6), .out_7(potencia_p_p_p_1_out_7), .out_8(potencia_p_p_p_1_out_8),
    .out_9(potencia_p_p_p_1_out_9), .out_10(potencia_p_p_p_1_out_10), .out_11(potencia_p_p_p_1_out_11),
    .out_12(potencia_p_p_p_1_out_12));
  and and_1 (and_1_out, E1, not_1_out, not_2_out);
  \Multiplicación_de_9___1  \multiplicación_de_9_1_1  (
    .ENTRADAS(potencia_p_p_p_1_out_12), .in_2(potencia_p_p_p_1_out_11),
    .MULTIPLICANDO_3(potencia_p_p_p_1_out_10), .MULTIPLICANDO_4(potencia_p_p_p_1_out_9),
    .MULTIPLICANDO_5(potencia_p_p_p_1_out_8), .in_6(potencia_p_p_p_1_out_7),
    .MULTIPLICANDO_7(potencia_p_p_p_1_out_6), .MULTIPLICANDO_8(potencia_p_p_p_1_out_4),
    .in_9(potencia_p_p_p_1_out_5), .MULTIPLICADOR(B3), .RESULTADO_1(\multiplicación_de_9_1_1_resultado_1 ),
    .RESULTADO_2(\multiplicación_de_9_1_1_resultado_2 ), .RESULTADO_3(\multiplicación_de_9_1_1_resultado_3 ),
    .RESULTADO_4(\multiplicación_de_9_1_1_resultado_4 ), .RESULTADO_5(\multiplicación_de_9_1_1_resultado_5 ),
    .RESULTADO_6(\multiplicación_de_9_1_1_resultado_6 ), .RESULTADO_7(\multiplicación_de_9_1_1_resultado_7 ),
    .RESULTADO_8(\multiplicación_de_9_1_1_resultado_8 ), .RESULTADO_9(\multiplicación_de_9_1_1_resultado_9 ));
  \Multiplicación_de_9___1  \multiplicación_de_9_1_2  (
    .ENTRADAS(potencia_p_p_p_1_out_12), .in_2(potencia_p_p_p_1_out_11),
    .MULTIPLICANDO_3(potencia_p_p_p_1_out_10), .MULTIPLICANDO_4(potencia_p_p_p_1_out_9),
    .MULTIPLICANDO_5(potencia_p_p_p_1_out_8), .in_6(potencia_p_p_p_1_out_7),
    .MULTIPLICANDO_7(potencia_p_p_p_1_out_6), .MULTIPLICANDO_8(potencia_p_p_p_1_out_4),
    .in_9(potencia_p_p_p_1_out_5), .MULTIPLICADOR(B2), .RESULTADO_1(\multiplicación_de_9_1_2_resultado_1 ),
    .RESULTADO_2(\multiplicación_de_9_1_2_resultado_2 ), .RESULTADO_3(\multiplicación_de_9_1_2_resultado_3 ),
    .RESULTADO_4(\multiplicación_de_9_1_2_resultado_4 ), .RESULTADO_5(\multiplicación_de_9_1_2_resultado_5 ),
    .RESULTADO_6(\multiplicación_de_9_1_2_resultado_6 ), .RESULTADO_7(\multiplicación_de_9_1_2_resultado_7 ),
    .RESULTADO_8(\multiplicación_de_9_1_2_resultado_8 ), .RESULTADO_9(\multiplicación_de_9_1_2_resultado_9 ));
  \Multiplicación_de_9___1  \multiplicación_de_9_1_3  (
    .ENTRADAS(potencia_p_p_p_1_out_12), .in_2(potencia_p_p_p_1_out_11),
    .MULTIPLICANDO_3(potencia_p_p_p_1_out_10), .MULTIPLICANDO_4(potencia_p_p_p_1_out_9),
    .MULTIPLICANDO_5(potencia_p_p_p_1_out_8), .in_6(potencia_p_p_p_1_out_7),
    .MULTIPLICANDO_7(potencia_p_p_p_1_out_6), .MULTIPLICANDO_8(potencia_p_p_p_1_out_4),
    .in_9(potencia_p_p_p_1_out_5), .MULTIPLICADOR(BASE), .RESULTADO_1(\multiplicación_de_9_1_3_resultado_1 ),
    .RESULTADO_2(\multiplicación_de_9_1_3_resultado_2 ), .RESULTADO_3(\multiplicación_de_9_1_3_resultado_3 ),
    .RESULTADO_4(\multiplicación_de_9_1_3_resultado_4 ), .RESULTADO_5(\multiplicación_de_9_1_3_resultado_5 ),
    .RESULTADO_6(\multiplicación_de_9_1_3_resultado_6 ), .RESULTADO_7(\multiplicación_de_9_1_3_resultado_7 ),
    .RESULTADO_8(\multiplicación_de_9_1_3_resultado_8 ), .RESULTADO_9(\multiplicación_de_9_1_3_resultado_9 ));
  and and_2 (out_18, and_1_out, \multiplicación_de_9_1_1_resultado_9 );
  Suma_de_2_Entradas suma_de_2_entradas_1 (
    .E1(\multiplicación_de_9_1_1_resultado_8 ), .E2(\multiplicación_de_9_1_2_resultado_9 ),
    .ACARREO_1(suma_de_2_entradas_1_acarreo_1), .out_3(suma_de_2_entradas_1_out_3));
  and and_3 (out_17, and_1_out, suma_de_2_entradas_1_out_3);
  Suma_de_4_Entradas suma_de_4_entradas_1 (
    .E1(suma_de_2_entradas_1_acarreo_1), .E2(\multiplicación_de_9_1_1_resultado_7 ),
    .E3(\multiplicación_de_9_1_2_resultado_8 ), .E4(\multiplicación_de_9_1_3_resultado_9 ),
    .out_5(suma_de_4_entradas_1_out_5), .ACARREO_1(suma_de_4_entradas_1_acarreo_1),
    .ACARREO_2(suma_de_4_entradas_1_acarreo_2));
  and and_4 (out_16, and_1_out, suma_de_4_entradas_1_out_5);
  Suma_de_4_Entradas suma_de_4_entradas_2 (
    .E1(suma_de_4_entradas_1_acarreo_1), .E2(\multiplicación_de_9_1_1_resultado_6 ),
    .E3(\multiplicación_de_9_1_2_resultado_7 ), .E4(\multiplicación_de_9_1_3_resultado_8 ),
    .out_5(suma_de_4_entradas_2_out_5), .ACARREO_1(suma_de_4_entradas_2_acarreo_1),
    .ACARREO_2(suma_de_4_entradas_2_acarreo_2));
  and and_5 (out_15, and_1_out, suma_de_4_entradas_2_out_5);
  Suma_de_5_Entradas suma_de_5_entradas_1 (
    .E1(suma_de_4_entradas_1_acarreo_2), .E2(suma_de_4_entradas_2_acarreo_1),
    .E3(\multiplicación_de_9_1_1_resultado_5 ), .E4(\multiplicación_de_9_1_2_resultado_6 ),
    .E5(\multiplicación_de_9_1_3_resultado_7 ), .out_6(suma_de_5_entradas_1_out_6),
    .ACARREO_1(suma_de_5_entradas_1_acarreo_1), .ACARREO_2(suma_de_5_entradas_1_acarreo_2));
  and and_6 (out_14, and_1_out, suma_de_5_entradas_1_out_6);
  Suma_de_4_Entradas suma_de_4_entradas_3 (
    .E1(suma_de_5_entradas_1_acarreo_1), .E2(\multiplicación_de_9_1_1_resultado_4 ),
    .E3(\multiplicación_de_9_1_2_resultado_5 ), .E4(\multiplicación_de_9_1_3_resultado_6 ),
    .out_5(suma_de_4_entradas_3_out_5), .ACARREO_1(suma_de_4_entradas_3_acarreo_1),
    .ACARREO_2(suma_de_4_entradas_3_acarreo_2));
  and and_7 (out_13, and_1_out, suma_de_4_entradas_3_out_5);
  Suma_de_5_Entradas suma_de_5_entradas_2 (
    .E1(suma_de_5_entradas_1_acarreo_2), .E2(suma_de_4_entradas_3_acarreo_1),
    .E3(\multiplicación_de_9_1_1_resultado_3 ), .E4(\multiplicación_de_9_1_2_resultado_4 ),
    .E5(\multiplicación_de_9_1_3_resultado_5 ), .out_6(suma_de_5_entradas_2_out_6),
    .ACARREO_1(suma_de_5_entradas_2_acarreo_1), .ACARREO_2(suma_de_5_entradas_2_acarreo_2));
  and and_8 (out_12, and_1_out, suma_de_5_entradas_2_out_6);
  Suma_de_4_Entradas suma_de_4_entradas_4 (
    .E1(suma_de_5_entradas_2_acarreo_1), .E2(\multiplicación_de_9_1_1_resultado_2 ),
    .E3(\multiplicación_de_9_1_2_resultado_3 ), .E4(\multiplicación_de_9_1_3_resultado_4 ),
    .out_5(suma_de_4_entradas_4_out_5), .ACARREO_1(suma_de_4_entradas_4_acarreo_1),
    .ACARREO_2(suma_de_4_entradas_4_acarreo_2));
  Suma_de_4_Entradas suma_de_4_entradas_5 (
    .E1(suma_de_4_entradas_4_acarreo_1), .E2(\multiplicación_de_9_1_1_resultado_1 ),
    .E3(\multiplicación_de_9_1_2_resultado_2 ), .E4(\multiplicación_de_9_1_3_resultado_3 ),
    .out_5(suma_de_4_entradas_5_out_5), .ACARREO_1(suma_de_4_entradas_5_acarreo_1),
    .ACARREO_2(suma_de_4_entradas_5_acarreo_2));
  and and_9 (out_11, and_1_out, suma_de_4_entradas_4_out_5);
  Suma_de_3_Entradas suma_de_3_entradas_1 (
    .E1(suma_de_4_entradas_5_acarreo_1), .E2(\multiplicación_de_9_1_2_resultado_1 ),
    .E3(\multiplicación_de_9_1_3_resultado_2 ), .out_4(suma_de_3_entradas_1_out_4),
    .ACARREO_1(suma_de_3_entradas_1_acarreo_1));
  and and_10 (out_10, and_1_out, suma_de_4_entradas_5_out_5);
  Suma_de_2_Entradas suma_de_2_entradas_2 (
    .E1(suma_de_3_entradas_1_acarreo_1), .E2(\multiplicación_de_9_1_3_resultado_1 ),
    .ACARREO_1(suma_de_2_entradas_2_acarreo_1), .out_3(suma_de_2_entradas_2_out_3));
  and and_11 (out_9, and_1_out, suma_de_3_entradas_1_out_4);
  and and_12 (out_8, and_1_out, suma_de_2_entradas_2_out_3);
  and and_13 (out_7, and_1_out, suma_de_2_entradas_2_acarreo_1);
  // also tied to GND on the sheet: {suma_de_4_entradas_2_acarreo_2, suma_de_4_entradas_3_acarreo_2, suma_de_5_entradas_2_acarreo_2, suma_de_4_entradas_4_acarreo_2, suma_de_4_entradas_5_acarreo_2}

  // Notes on the sheet:
  //   EXPONENTE
  //   B1
endmodule
module Potencia__P___P___P___P___P (
  input  E1,
  input  E2,
  input  E3,
  output out_4,
  output out_5,
  output out_6,
  output out_7,
  output out_8,
  output out_9,
  output out_10,
  output out_11,
  output out_12,
  output out_13,
  output out_14,
  output out_15,
  output out_16,
  output out_17,
  output out_18
);

  wire \multiplicación_de_12_1_1_resultado_1 , \multiplicación_de_12_1_1_resultado_2 ,
       \multiplicación_de_12_1_1_resultado_3 , \multiplicación_de_12_1_1_resultado_4 ,
       \multiplicación_de_12_1_1_resultado_5 , \multiplicación_de_12_1_1_resultado_6 ,
       \multiplicación_de_12_1_1_resultado_7 , \multiplicación_de_12_1_1_resultado_8 ,
       \multiplicación_de_12_1_1_resultado_9 , \multiplicación_de_12_1_1_resultado_10 ,
       \multiplicación_de_12_1_1_resultado_11 , \multiplicación_de_12_1_2_resultado_1 ,
       \multiplicación_de_12_1_2_resultado_2 , \multiplicación_de_12_1_2_resultado_3 ,
       \multiplicación_de_12_1_2_resultado_4 , \multiplicación_de_12_1_2_resultado_5 ,
       \multiplicación_de_12_1_2_resultado_6 , \multiplicación_de_12_1_2_resultado_7 ,
       \multiplicación_de_12_1_2_resultado_8 , \multiplicación_de_12_1_2_resultado_9 ,
       \multiplicación_de_12_1_2_resultado_10 , \multiplicación_de_12_1_2_resultado_11 ,
       \multiplicación_de_12_1_2_resultado_12 , \multiplicación_de_12_1_3_resultado_1 ,
       \multiplicación_de_12_1_3_resultado_2 , \multiplicación_de_12_1_3_resultado_3 ,
       \multiplicación_de_12_1_3_resultado_4 , \multiplicación_de_12_1_3_resultado_5 ,
       \multiplicación_de_12_1_3_resultado_6 , \multiplicación_de_12_1_3_resultado_7 ,
       \multiplicación_de_12_1_3_resultado_8 , \multiplicación_de_12_1_3_resultado_9 ,
       \multiplicación_de_12_1_3_resultado_10 , \multiplicación_de_12_1_3_resultado_11 ,
       \multiplicación_de_12_1_3_resultado_12 , potencia_p_p_p_p_1_out_4, potencia_p_p_p_p_1_out_5,
       potencia_p_p_p_p_1_out_6, potencia_p_p_p_p_1_out_7, potencia_p_p_p_p_1_out_8,
       potencia_p_p_p_p_1_out_9, potencia_p_p_p_p_1_out_10, potencia_p_p_p_p_1_out_11,
       potencia_p_p_p_p_1_out_12, potencia_p_p_p_p_1_out_13, potencia_p_p_p_p_1_out_14,
       potencia_p_p_p_p_1_out_15, suma_de_2_entradas_1_acarreo_1, suma_de_3_entradas_1_acarreo_1,
       suma_de_4_entradas_1_acarreo_1, suma_de_4_entradas_1_acarreo_2, suma_de_4_entradas_2_acarreo_1,
       suma_de_4_entradas_2_acarreo_2, suma_de_4_entradas_3_acarreo_1, suma_de_4_entradas_3_acarreo_2,
       suma_de_4_entradas_4_acarreo_1, suma_de_4_entradas_4_acarreo_2, suma_de_4_entradas_5_acarreo_1,
       suma_de_4_entradas_5_acarreo_2, suma_de_4_entradas_6_acarreo_1, suma_de_4_entradas_6_acarreo_2,
       suma_de_4_entradas_7_acarreo_1, suma_de_4_entradas_7_acarreo_2, suma_de_4_entradas_8_acarreo_1,
       suma_de_4_entradas_8_acarreo_2, suma_de_4_entradas_9_acarreo_1, suma_de_4_entradas_9_acarreo_2,
       suma_de_4_entradas_10_acarreo_1, suma_de_4_entradas_10_acarreo_2;

  Potencia__P___P___P___P potencia_p_p_p_p_1 (
    .E1(E1), .E2(E2), .E3(E3), .out_4(potencia_p_p_p_p_1_out_4), .out_5(potencia_p_p_p_p_1_out_5),
    .out_6(potencia_p_p_p_p_1_out_6), .out_7(potencia_p_p_p_p_1_out_7), .out_8(potencia_p_p_p_p_1_out_8),
    .out_9(potencia_p_p_p_p_1_out_9), .out_10(potencia_p_p_p_p_1_out_10), .out_11(potencia_p_p_p_p_1_out_11),
    .out_12(potencia_p_p_p_p_1_out_12), .out_13(potencia_p_p_p_p_1_out_13),
    .out_14(potencia_p_p_p_p_1_out_14), .out_15(potencia_p_p_p_p_1_out_15));
  \Multiplicación_de_12___1  \multiplicación_de_12_1_1  (
    .ENTRADAS(potencia_p_p_p_p_1_out_15), .in_2(potencia_p_p_p_p_1_out_14),
    .MULTIPLICANDO_3(potencia_p_p_p_p_1_out_13), .MULTIPLICANDO_4(potencia_p_p_p_p_1_out_12),
    .MULTIPLICANDO_5(potencia_p_p_p_p_1_out_11), .in_6(potencia_p_p_p_p_1_out_10),
    .MULTIPLICANDO_7(potencia_p_p_p_p_1_out_9), .MULTIPLICANDO_8(potencia_p_p_p_p_1_out_8),
    .in_9(potencia_p_p_p_p_1_out_7), .MULTIPLICANDO_10(potencia_p_p_p_p_1_out_6),
    .MULTIPLICANDO_11(potencia_p_p_p_p_1_out_4), .in_12(potencia_p_p_p_p_1_out_5), .MULTIPLICADOR(E3),
    .RESULTADO_1(\multiplicación_de_12_1_1_resultado_1 ),
    .RESULTADO_2(\multiplicación_de_12_1_1_resultado_2 ),
    .RESULTADO_3(\multiplicación_de_12_1_1_resultado_3 ),
    .RESULTADO_4(\multiplicación_de_12_1_1_resultado_4 ),
    .RESULTADO_5(\multiplicación_de_12_1_1_resultado_5 ),
    .RESULTADO_6(\multiplicación_de_12_1_1_resultado_6 ),
    .RESULTADO_7(\multiplicación_de_12_1_1_resultado_7 ),
    .RESULTADO_8(\multiplicación_de_12_1_1_resultado_8 ),
    .RESULTADO_9(\multiplicación_de_12_1_1_resultado_9 ),
    .RESULTADO_10(\multiplicación_de_12_1_1_resultado_10 ),
    .RESULTADO_11(\multiplicación_de_12_1_1_resultado_11 ), .RESULTADO_12(out_5));
  \Multiplicación_de_12___1  \multiplicación_de_12_1_2  (
    .ENTRADAS(potencia_p_p_p_p_1_out_15), .in_2(potencia_p_p_p_p_1_out_14),
    .MULTIPLICANDO_3(potencia_p_p_p_p_1_out_13), .MULTIPLICANDO_4(potencia_p_p_p_p_1_out_12),
    .MULTIPLICANDO_5(potencia_p_p_p_p_1_out_11), .in_6(potencia_p_p_p_p_1_out_10),
    .MULTIPLICANDO_7(potencia_p_p_p_p_1_out_9), .MULTIPLICANDO_8(potencia_p_p_p_p_1_out_8),
    .in_9(potencia_p_p_p_p_1_out_7), .MULTIPLICANDO_10(potencia_p_p_p_p_1_out_6),
    .MULTIPLICANDO_11(potencia_p_p_p_p_1_out_4), .in_12(potencia_p_p_p_p_1_out_5), .MULTIPLICADOR(E2),
    .RESULTADO_1(\multiplicación_de_12_1_2_resultado_1 ),
    .RESULTADO_2(\multiplicación_de_12_1_2_resultado_2 ),
    .RESULTADO_3(\multiplicación_de_12_1_2_resultado_3 ),
    .RESULTADO_4(\multiplicación_de_12_1_2_resultado_4 ),
    .RESULTADO_5(\multiplicación_de_12_1_2_resultado_5 ),
    .RESULTADO_6(\multiplicación_de_12_1_2_resultado_6 ),
    .RESULTADO_7(\multiplicación_de_12_1_2_resultado_7 ),
    .RESULTADO_8(\multiplicación_de_12_1_2_resultado_8 ),
    .RESULTADO_9(\multiplicación_de_12_1_2_resultado_9 ),
    .RESULTADO_10(\multiplicación_de_12_1_2_resultado_10 ),
    .RESULTADO_11(\multiplicación_de_12_1_2_resultado_11 ),
    .RESULTADO_12(\multiplicación_de_12_1_2_resultado_12 ));
  \Multiplicación_de_12___1  \multiplicación_de_12_1_3  (
    .ENTRADAS(potencia_p_p_p_p_1_out_15), .in_2(potencia_p_p_p_p_1_out_14),
    .MULTIPLICANDO_3(potencia_p_p_p_p_1_out_13), .MULTIPLICANDO_4(potencia_p_p_p_p_1_out_12),
    .MULTIPLICANDO_5(potencia_p_p_p_p_1_out_11), .in_6(potencia_p_p_p_p_1_out_10),
    .MULTIPLICANDO_7(potencia_p_p_p_p_1_out_9), .MULTIPLICANDO_8(potencia_p_p_p_p_1_out_8),
    .in_9(potencia_p_p_p_p_1_out_7), .MULTIPLICANDO_10(potencia_p_p_p_p_1_out_6),
    .MULTIPLICANDO_11(potencia_p_p_p_p_1_out_4), .in_12(potencia_p_p_p_p_1_out_5), .MULTIPLICADOR(E1),
    .RESULTADO_1(\multiplicación_de_12_1_3_resultado_1 ),
    .RESULTADO_2(\multiplicación_de_12_1_3_resultado_2 ),
    .RESULTADO_3(\multiplicación_de_12_1_3_resultado_3 ),
    .RESULTADO_4(\multiplicación_de_12_1_3_resultado_4 ),
    .RESULTADO_5(\multiplicación_de_12_1_3_resultado_5 ),
    .RESULTADO_6(\multiplicación_de_12_1_3_resultado_6 ),
    .RESULTADO_7(\multiplicación_de_12_1_3_resultado_7 ),
    .RESULTADO_8(\multiplicación_de_12_1_3_resultado_8 ),
    .RESULTADO_9(\multiplicación_de_12_1_3_resultado_9 ),
    .RESULTADO_10(\multiplicación_de_12_1_3_resultado_10 ),
    .RESULTADO_11(\multiplicación_de_12_1_3_resultado_11 ),
    .RESULTADO_12(\multiplicación_de_12_1_3_resultado_12 ));
  Suma_de_2_Entradas suma_de_2_entradas_1 (
    .E1(\multiplicación_de_12_1_1_resultado_11 ), .E2(\multiplicación_de_12_1_2_resultado_12 ),
    .ACARREO_1(suma_de_2_entradas_1_acarreo_1), .out_3(out_4));
  Suma_de_4_Entradas suma_de_4_entradas_1 (
    .E1(suma_de_2_entradas_1_acarreo_1), .E2(\multiplicación_de_12_1_1_resultado_10 ),
    .E3(\multiplicación_de_12_1_2_resultado_11 ), .E4(\multiplicación_de_12_1_3_resultado_12 ),
    .out_5(out_6), .ACARREO_1(suma_de_4_entradas_1_acarreo_1), .ACARREO_2(suma_de_4_entradas_1_acarreo_2));
  Suma_de_4_Entradas suma_de_4_entradas_2 (
    .E1(suma_de_4_entradas_1_acarreo_1), .E2(\multiplicación_de_12_1_1_resultado_9 ),
    .E3(\multiplicación_de_12_1_2_resultado_10 ), .E4(\multiplicación_de_12_1_3_resultado_11 ),
    .out_5(out_7), .ACARREO_1(suma_de_4_entradas_2_acarreo_1), .ACARREO_2(suma_de_4_entradas_2_acarreo_2));
  Suma_de_4_Entradas suma_de_4_entradas_3 (
    .E1(suma_de_4_entradas_2_acarreo_1), .E2(\multiplicación_de_12_1_1_resultado_8 ),
    .E3(\multiplicación_de_12_1_2_resultado_9 ), .E4(\multiplicación_de_12_1_3_resultado_10 ), .out_5(out_8),
    .ACARREO_1(suma_de_4_entradas_3_acarreo_1), .ACARREO_2(suma_de_4_entradas_3_acarreo_2));
  Suma_de_4_Entradas suma_de_4_entradas_4 (
    .E1(suma_de_4_entradas_3_acarreo_1), .E2(\multiplicación_de_12_1_1_resultado_7 ),
    .E3(\multiplicación_de_12_1_2_resultado_8 ), .E4(\multiplicación_de_12_1_3_resultado_9 ), .out_5(out_9),
    .ACARREO_1(suma_de_4_entradas_4_acarreo_1), .ACARREO_2(suma_de_4_entradas_4_acarreo_2));
  Suma_de_4_Entradas suma_de_4_entradas_5 (
    .E1(suma_de_4_entradas_4_acarreo_1), .E2(\multiplicación_de_12_1_1_resultado_6 ),
    .E3(\multiplicación_de_12_1_2_resultado_7 ), .E4(\multiplicación_de_12_1_3_resultado_8 ), .out_5(out_10),
    .ACARREO_1(suma_de_4_entradas_5_acarreo_1), .ACARREO_2(suma_de_4_entradas_5_acarreo_2));
  Suma_de_4_Entradas suma_de_4_entradas_6 (
    .E1(suma_de_4_entradas_5_acarreo_1), .E2(\multiplicación_de_12_1_1_resultado_5 ),
    .E3(\multiplicación_de_12_1_2_resultado_6 ), .E4(\multiplicación_de_12_1_3_resultado_7 ), .out_5(out_11),
    .ACARREO_1(suma_de_4_entradas_6_acarreo_1), .ACARREO_2(suma_de_4_entradas_6_acarreo_2));
  Suma_de_4_Entradas suma_de_4_entradas_7 (
    .E1(suma_de_4_entradas_6_acarreo_1), .E2(\multiplicación_de_12_1_1_resultado_4 ),
    .E3(\multiplicación_de_12_1_2_resultado_5 ), .E4(\multiplicación_de_12_1_3_resultado_6 ), .out_5(out_12),
    .ACARREO_1(suma_de_4_entradas_7_acarreo_1), .ACARREO_2(suma_de_4_entradas_7_acarreo_2));
  Suma_de_4_Entradas suma_de_4_entradas_8 (
    .E1(suma_de_4_entradas_7_acarreo_1), .E2(\multiplicación_de_12_1_1_resultado_3 ),
    .E3(\multiplicación_de_12_1_2_resultado_4 ), .E4(\multiplicación_de_12_1_3_resultado_5 ), .out_5(out_13),
    .ACARREO_1(suma_de_4_entradas_8_acarreo_1), .ACARREO_2(suma_de_4_entradas_8_acarreo_2));
  Suma_de_4_Entradas suma_de_4_entradas_9 (
    .E1(suma_de_4_entradas_8_acarreo_1), .E2(\multiplicación_de_12_1_1_resultado_2 ),
    .E3(\multiplicación_de_12_1_2_resultado_3 ), .E4(\multiplicación_de_12_1_3_resultado_4 ), .out_5(out_14),
    .ACARREO_1(suma_de_4_entradas_9_acarreo_1), .ACARREO_2(suma_de_4_entradas_9_acarreo_2));
  Suma_de_4_Entradas suma_de_4_entradas_10 (
    .E1(suma_de_4_entradas_9_acarreo_1), .E2(\multiplicación_de_12_1_1_resultado_1 ),
    .E3(\multiplicación_de_12_1_2_resultado_2 ), .E4(\multiplicación_de_12_1_3_resultado_3 ), .out_5(out_15),
    .ACARREO_1(suma_de_4_entradas_10_acarreo_1), .ACARREO_2(suma_de_4_entradas_10_acarreo_2));
  Suma_de_3_Entradas suma_de_3_entradas_1 (
    .E1(suma_de_4_entradas_10_acarreo_1), .E2(\multiplicación_de_12_1_2_resultado_1 ),
    .E3(\multiplicación_de_12_1_3_resultado_2 ), .out_4(out_16), .ACARREO_1(suma_de_3_entradas_1_acarreo_1));
  Suma_de_2_Entradas suma_de_2_entradas_2 (
    .E1(suma_de_3_entradas_1_acarreo_1), .E2(\multiplicación_de_12_1_3_resultado_1 ), .ACARREO_1(out_18),
    .out_3(out_17));
  // also tied to GND on the sheet: {suma_de_4_entradas_1_acarreo_2, suma_de_4_entradas_2_acarreo_2, suma_de_4_entradas_3_acarreo_2, suma_de_4_entradas_4_acarreo_2, suma_de_4_entradas_5_acarreo_2, suma_de_4_entradas_6_acarreo_2, suma_de_4_entradas_7_acarreo_2, suma_de_4_entradas_8_acarreo_2, suma_de_4_entradas_9_acarreo_2, suma_de_4_entradas_10_acarreo_2}

  // Notes on the sheet:
  //   ENTRADAS
endmodule

module \Elección_Potencia_p___5  (
  input  E1,
  input  E2,
  input  E3,
  input  BASE,
  input  B2,
  input  B3,
  output out_7,
  output out_8,
  output out_9,
  output out_10,
  output out_11,
  output out_12,
  output out_13,
  output out_14,
  output out_15,
  output out_16,
  output out_17,
  output out_18,
  output out_19,
  output out_20,
  output out_21
);

  wire and_1_out, \multiplicación_de_12_1_1_resultado_1 , \multiplicación_de_12_1_1_resultado_2 ,
       \multiplicación_de_12_1_1_resultado_3 , \multiplicación_de_12_1_1_resultado_4 ,
       \multiplicación_de_12_1_1_resultado_5 , \multiplicación_de_12_1_1_resultado_6 ,
       \multiplicación_de_12_1_1_resultado_7 , \multiplicación_de_12_1_1_resultado_8 ,
       \multiplicación_de_12_1_1_resultado_9 , \multiplicación_de_12_1_1_resultado_10 ,
       \multiplicación_de_12_1_1_resultado_11 , \multiplicación_de_12_1_1_resultado_12 ,
       \multiplicación_de_12_1_2_resultado_1 , \multiplicación_de_12_1_2_resultado_2 ,
       \multiplicación_de_12_1_2_resultado_3 , \multiplicación_de_12_1_2_resultado_4 ,
       \multiplicación_de_12_1_2_resultado_5 , \multiplicación_de_12_1_2_resultado_6 ,
       \multiplicación_de_12_1_2_resultado_7 , \multiplicación_de_12_1_2_resultado_8 ,
       \multiplicación_de_12_1_2_resultado_9 , \multiplicación_de_12_1_2_resultado_10 ,
       \multiplicación_de_12_1_2_resultado_11 , \multiplicación_de_12_1_2_resultado_12 ,
       \multiplicación_de_12_1_3_resultado_1 , \multiplicación_de_12_1_3_resultado_2 ,
       \multiplicación_de_12_1_3_resultado_3 , \multiplicación_de_12_1_3_resultado_4 ,
       \multiplicación_de_12_1_3_resultado_5 , \multiplicación_de_12_1_3_resultado_6 ,
       \multiplicación_de_12_1_3_resultado_7 , \multiplicación_de_12_1_3_resultado_8 ,
       \multiplicación_de_12_1_3_resultado_9 , \multiplicación_de_12_1_3_resultado_10 ,
       \multiplicación_de_12_1_3_resultado_11 , \multiplicación_de_12_1_3_resultado_12 , not_1_out,
       potencia_p_p_p_p_1_out_4, potencia_p_p_p_p_1_out_5, potencia_p_p_p_p_1_out_6,
       potencia_p_p_p_p_1_out_7, potencia_p_p_p_p_1_out_8, potencia_p_p_p_p_1_out_9,
       potencia_p_p_p_p_1_out_10, potencia_p_p_p_p_1_out_11, potencia_p_p_p_p_1_out_12,
       potencia_p_p_p_p_1_out_13, potencia_p_p_p_p_1_out_14, potencia_p_p_p_p_1_out_15,
       suma_de_2_entradas_1_acarreo_1, suma_de_2_entradas_1_out_3, suma_de_2_entradas_2_acarreo_1,
       suma_de_2_entradas_2_out_3, suma_de_3_entradas_1_acarreo_1, suma_de_3_entradas_1_out_4,
       suma_de_4_entradas_1_acarreo_1, suma_de_4_entradas_1_acarreo_2, suma_de_4_entradas_1_out_5,
       suma_de_4_entradas_2_acarreo_1, suma_de_4_entradas_2_acarreo_2, suma_de_4_entradas_2_out_5,
       suma_de_4_entradas_3_acarreo_1, suma_de_4_entradas_3_acarreo_2, suma_de_4_entradas_3_out_5,
       suma_de_4_entradas_4_acarreo_1, suma_de_4_entradas_4_acarreo_2, suma_de_4_entradas_4_out_5,
       suma_de_4_entradas_5_acarreo_1, suma_de_4_entradas_5_acarreo_2, suma_de_4_entradas_5_out_5,
       suma_de_4_entradas_6_acarreo_1, suma_de_4_entradas_6_acarreo_2, suma_de_4_entradas_6_out_5,
       suma_de_4_entradas_7_acarreo_1, suma_de_4_entradas_7_acarreo_2, suma_de_4_entradas_7_out_5,
       suma_de_4_entradas_8_acarreo_1, suma_de_4_entradas_8_acarreo_2, suma_de_4_entradas_8_out_5,
       suma_de_4_entradas_9_acarreo_1, suma_de_4_entradas_9_acarreo_2, suma_de_4_entradas_9_out_5,
       suma_de_4_entradas_10_acarreo_1, suma_de_4_entradas_10_acarreo_2, suma_de_4_entradas_10_out_5;

  not not_1 (not_1_out, E2);
  Potencia__P___P___P___P potencia_p_p_p_p_1 (
    .E1(BASE), .E2(B2), .E3(B3), .out_4(potencia_p_p_p_p_1_out_4), .out_5(potencia_p_p_p_p_1_out_5),
    .out_6(potencia_p_p_p_p_1_out_6), .out_7(potencia_p_p_p_p_1_out_7), .out_8(potencia_p_p_p_p_1_out_8),
    .out_9(potencia_p_p_p_p_1_out_9), .out_10(potencia_p_p_p_p_1_out_10), .out_11(potencia_p_p_p_p_1_out_11),
    .out_12(potencia_p_p_p_p_1_out_12), .out_13(potencia_p_p_p_p_1_out_13),
    .out_14(potencia_p_p_p_p_1_out_14), .out_15(potencia_p_p_p_p_1_out_15));
  and and_1 (and_1_out, E1, not_1_out, E3);
  \Multiplicación_de_12___1  \multiplicación_de_12_1_1  (
    .ENTRADAS(potencia_p_p_p_p_1_out_15), .in_2(potencia_p_p_p_p_1_out_14),
    .MULTIPLICANDO_3(potencia_p_p_p_p_1_out_13), .MULTIPLICANDO_4(potencia_p_p_p_p_1_out_12),
    .MULTIPLICANDO_5(potencia_p_p_p_p_1_out_11), .in_6(potencia_p_p_p_p_1_out_10),
    .MULTIPLICANDO_7(potencia_p_p_p_p_1_out_9), .MULTIPLICANDO_8(potencia_p_p_p_p_1_out_8),
    .in_9(potencia_p_p_p_p_1_out_7), .MULTIPLICANDO_10(potencia_p_p_p_p_1_out_6),
    .MULTIPLICANDO_11(potencia_p_p_p_p_1_out_4), .in_12(potencia_p_p_p_p_1_out_5), .MULTIPLICADOR(B3),
    .RESULTADO_1(\multiplicación_de_12_1_1_resultado_1 ),
    .RESULTADO_2(\multiplicación_de_12_1_1_resultado_2 ),
    .RESULTADO_3(\multiplicación_de_12_1_1_resultado_3 ),
    .RESULTADO_4(\multiplicación_de_12_1_1_resultado_4 ),
    .RESULTADO_5(\multiplicación_de_12_1_1_resultado_5 ),
    .RESULTADO_6(\multiplicación_de_12_1_1_resultado_6 ),
    .RESULTADO_7(\multiplicación_de_12_1_1_resultado_7 ),
    .RESULTADO_8(\multiplicación_de_12_1_1_resultado_8 ),
    .RESULTADO_9(\multiplicación_de_12_1_1_resultado_9 ),
    .RESULTADO_10(\multiplicación_de_12_1_1_resultado_10 ),
    .RESULTADO_11(\multiplicación_de_12_1_1_resultado_11 ),
    .RESULTADO_12(\multiplicación_de_12_1_1_resultado_12 ));
  \Multiplicación_de_12___1  \multiplicación_de_12_1_2  (
    .ENTRADAS(potencia_p_p_p_p_1_out_15), .in_2(potencia_p_p_p_p_1_out_14),
    .MULTIPLICANDO_3(potencia_p_p_p_p_1_out_13), .MULTIPLICANDO_4(potencia_p_p_p_p_1_out_12),
    .MULTIPLICANDO_5(potencia_p_p_p_p_1_out_11), .in_6(potencia_p_p_p_p_1_out_10),
    .MULTIPLICANDO_7(potencia_p_p_p_p_1_out_9), .MULTIPLICANDO_8(potencia_p_p_p_p_1_out_8),
    .in_9(potencia_p_p_p_p_1_out_7), .MULTIPLICANDO_10(potencia_p_p_p_p_1_out_6),
    .MULTIPLICANDO_11(potencia_p_p_p_p_1_out_4), .in_12(potencia_p_p_p_p_1_out_5), .MULTIPLICADOR(B2),
    .RESULTADO_1(\multiplicación_de_12_1_2_resultado_1 ),
    .RESULTADO_2(\multiplicación_de_12_1_2_resultado_2 ),
    .RESULTADO_3(\multiplicación_de_12_1_2_resultado_3 ),
    .RESULTADO_4(\multiplicación_de_12_1_2_resultado_4 ),
    .RESULTADO_5(\multiplicación_de_12_1_2_resultado_5 ),
    .RESULTADO_6(\multiplicación_de_12_1_2_resultado_6 ),
    .RESULTADO_7(\multiplicación_de_12_1_2_resultado_7 ),
    .RESULTADO_8(\multiplicación_de_12_1_2_resultado_8 ),
    .RESULTADO_9(\multiplicación_de_12_1_2_resultado_9 ),
    .RESULTADO_10(\multiplicación_de_12_1_2_resultado_10 ),
    .RESULTADO_11(\multiplicación_de_12_1_2_resultado_11 ),
    .RESULTADO_12(\multiplicación_de_12_1_2_resultado_12 ));
  \Multiplicación_de_12___1  \multiplicación_de_12_1_3  (
    .ENTRADAS(potencia_p_p_p_p_1_out_15), .in_2(potencia_p_p_p_p_1_out_14),
    .MULTIPLICANDO_3(potencia_p_p_p_p_1_out_13), .MULTIPLICANDO_4(potencia_p_p_p_p_1_out_12),
    .MULTIPLICANDO_5(potencia_p_p_p_p_1_out_11), .in_6(potencia_p_p_p_p_1_out_10),
    .MULTIPLICANDO_7(potencia_p_p_p_p_1_out_9), .MULTIPLICANDO_8(potencia_p_p_p_p_1_out_8),
    .in_9(potencia_p_p_p_p_1_out_7), .MULTIPLICANDO_10(potencia_p_p_p_p_1_out_6),
    .MULTIPLICANDO_11(potencia_p_p_p_p_1_out_4), .in_12(potencia_p_p_p_p_1_out_5), .MULTIPLICADOR(BASE),
    .RESULTADO_1(\multiplicación_de_12_1_3_resultado_1 ),
    .RESULTADO_2(\multiplicación_de_12_1_3_resultado_2 ),
    .RESULTADO_3(\multiplicación_de_12_1_3_resultado_3 ),
    .RESULTADO_4(\multiplicación_de_12_1_3_resultado_4 ),
    .RESULTADO_5(\multiplicación_de_12_1_3_resultado_5 ),
    .RESULTADO_6(\multiplicación_de_12_1_3_resultado_6 ),
    .RESULTADO_7(\multiplicación_de_12_1_3_resultado_7 ),
    .RESULTADO_8(\multiplicación_de_12_1_3_resultado_8 ),
    .RESULTADO_9(\multiplicación_de_12_1_3_resultado_9 ),
    .RESULTADO_10(\multiplicación_de_12_1_3_resultado_10 ),
    .RESULTADO_11(\multiplicación_de_12_1_3_resultado_11 ),
    .RESULTADO_12(\multiplicación_de_12_1_3_resultado_12 ));
  and and_2 (out_21, and_1_out, \multiplicación_de_12_1_1_resultado_12 );
  Suma_de_2_Entradas suma_de_2_entradas_1 (
    .E1(\multiplicación_de_12_1_1_resultado_11 ), .E2(\multiplicación_de_12_1_2_resultado_12 ),
    .ACARREO_1(suma_de_2_entradas_1_acarreo_1), .out_3(suma_de_2_entradas_1_out_3));
  and and_3 (out_20, and_1_out, suma_de_2_entradas_1_out_3);
  Suma_de_4_Entradas suma_de_4_entradas_1 (
    .E1(suma_de_2_entradas_1_acarreo_1), .E2(\multiplicación_de_12_1_1_resultado_10 ),
    .E3(\multiplicación_de_12_1_2_resultado_11 ), .E4(\multiplicación_de_12_1_3_resultado_12 ),
    .out_5(suma_de_4_entradas_1_out_5), .ACARREO_1(suma_de_4_entradas_1_acarreo_1),
    .ACARREO_2(suma_de_4_entradas_1_acarreo_2));
  and and_4 (out_19, and_1_out, suma_de_4_entradas_1_out_5);
  Suma_de_4_Entradas suma_de_4_entradas_2 (
    .E1(suma_de_4_entradas_1_acarreo_1), .E2(\multiplicación_de_12_1_1_resultado_9 ),
    .E3(\multiplicación_de_12_1_2_resultado_10 ), .E4(\multiplicación_de_12_1_3_resultado_11 ),
    .out_5(suma_de_4_entradas_2_out_5), .ACARREO_1(suma_de_4_entradas_2_acarreo_1),
    .ACARREO_2(suma_de_4_entradas_2_acarreo_2));
  and and_5 (out_18, and_1_out, suma_de_4_entradas_2_out_5);
  Suma_de_4_Entradas suma_de_4_entradas_3 (
    .E1(suma_de_4_entradas_2_acarreo_1), .E2(\multiplicación_de_12_1_1_resultado_8 ),
    .E3(\multiplicación_de_12_1_2_resultado_9 ), .E4(\multiplicación_de_12_1_3_resultado_10 ),
    .out_5(suma_de_4_entradas_3_out_5), .ACARREO_1(suma_de_4_entradas_3_acarreo_1),
    .ACARREO_2(suma_de_4_entradas_3_acarreo_2));
  and and_6 (out_17, and_1_out, suma_de_4_entradas_3_out_5);
  Suma_de_4_Entradas suma_de_4_entradas_4 (
    .E1(suma_de_4_entradas_3_acarreo_1), .E2(\multiplicación_de_12_1_1_resultado_7 ),
    .E3(\multiplicación_de_12_1_2_resultado_8 ), .E4(\multiplicación_de_12_1_3_resultado_9 ),
    .out_5(suma_de_4_entradas_4_out_5), .ACARREO_1(suma_de_4_entradas_4_acarreo_1),
    .ACARREO_2(suma_de_4_entradas_4_acarreo_2));
  and and_7 (out_16, and_1_out, suma_de_4_entradas_4_out_5);
  Suma_de_4_Entradas suma_de_4_entradas_5 (
    .E1(suma_de_4_entradas_4_acarreo_1), .E2(\multiplicación_de_12_1_1_resultado_6 ),
    .E3(\multiplicación_de_12_1_2_resultado_7 ), .E4(\multiplicación_de_12_1_3_resultado_8 ),
    .out_5(suma_de_4_entradas_5_out_5), .ACARREO_1(suma_de_4_entradas_5_acarreo_1),
    .ACARREO_2(suma_de_4_entradas_5_acarreo_2));
  and and_8 (out_15, and_1_out, suma_de_4_entradas_5_out_5);
  Suma_de_4_Entradas suma_de_4_entradas_6 (
    .E1(suma_de_4_entradas_5_acarreo_1), .E2(\multiplicación_de_12_1_1_resultado_5 ),
    .E3(\multiplicación_de_12_1_2_resultado_6 ), .E4(\multiplicación_de_12_1_3_resultado_7 ),
    .out_5(suma_de_4_entradas_6_out_5), .ACARREO_1(suma_de_4_entradas_6_acarreo_1),
    .ACARREO_2(suma_de_4_entradas_6_acarreo_2));
  and and_9 (out_14, and_1_out, suma_de_4_entradas_6_out_5);
  Suma_de_4_Entradas suma_de_4_entradas_7 (
    .E1(suma_de_4_entradas_6_acarreo_1), .E2(\multiplicación_de_12_1_1_resultado_4 ),
    .E3(\multiplicación_de_12_1_2_resultado_5 ), .E4(\multiplicación_de_12_1_3_resultado_6 ),
    .out_5(suma_de_4_entradas_7_out_5), .ACARREO_1(suma_de_4_entradas_7_acarreo_1),
    .ACARREO_2(suma_de_4_entradas_7_acarreo_2));
  and and_10 (out_13, and_1_out, suma_de_4_entradas_7_out_5);
  Suma_de_4_Entradas suma_de_4_entradas_8 (
    .E1(suma_de_4_entradas_7_acarreo_1), .E2(\multiplicación_de_12_1_1_resultado_3 ),
    .E3(\multiplicación_de_12_1_2_resultado_4 ), .E4(\multiplicación_de_12_1_3_resultado_5 ),
    .out_5(suma_de_4_entradas_8_out_5), .ACARREO_1(suma_de_4_entradas_8_acarreo_1),
    .ACARREO_2(suma_de_4_entradas_8_acarreo_2));
  Suma_de_4_Entradas suma_de_4_entradas_9 (
    .E1(suma_de_4_entradas_8_acarreo_1), .E2(\multiplicación_de_12_1_1_resultado_2 ),
    .E3(\multiplicación_de_12_1_2_resultado_3 ), .E4(\multiplicación_de_12_1_3_resultado_4 ),
    .out_5(suma_de_4_entradas_9_out_5), .ACARREO_1(suma_de_4_entradas_9_acarreo_1),
    .ACARREO_2(suma_de_4_entradas_9_acarreo_2));
  and and_11 (out_12, and_1_out, suma_de_4_entradas_8_out_5);
  Suma_de_4_Entradas suma_de_4_entradas_10 (
    .E1(suma_de_4_entradas_9_acarreo_1), .E2(\multiplicación_de_12_1_1_resultado_1 ),
    .E3(\multiplicación_de_12_1_2_resultado_2 ), .E4(\multiplicación_de_12_1_3_resultado_3 ),
    .out_5(suma_de_4_entradas_10_out_5), .ACARREO_1(suma_de_4_entradas_10_acarreo_1),
    .ACARREO_2(suma_de_4_entradas_10_acarreo_2));
  and and_12 (out_11, and_1_out, suma_de_4_entradas_9_out_5);
  and and_13 (out_10, and_1_out, suma_de_4_entradas_10_out_5);
  Suma_de_3_Entradas suma_de_3_entradas_1 (
    .E1(suma_de_4_entradas_10_acarreo_1), .E2(\multiplicación_de_12_1_2_resultado_1 ),
    .E3(\multiplicación_de_12_1_3_resultado_2 ), .out_4(suma_de_3_entradas_1_out_4),
    .ACARREO_1(suma_de_3_entradas_1_acarreo_1));
  Suma_de_2_Entradas suma_de_2_entradas_2 (
    .E1(suma_de_3_entradas_1_acarreo_1), .E2(\multiplicación_de_12_1_3_resultado_1 ),
    .ACARREO_1(suma_de_2_entradas_2_acarreo_1), .out_3(suma_de_2_entradas_2_out_3));
  and and_14 (out_9, and_1_out, suma_de_3_entradas_1_out_4);
  and and_15 (out_8, and_1_out, suma_de_2_entradas_2_out_3);
  and and_16 (out_7, and_1_out, suma_de_2_entradas_2_acarreo_1);
  // also tied to GND on the sheet: {suma_de_4_entradas_1_acarreo_2, suma_de_4_entradas_2_acarreo_2, suma_de_4_entradas_3_acarreo_2, suma_de_4_entradas_4_acarreo_2, suma_de_4_entradas_5_acarreo_2, suma_de_4_entradas_6_acarreo_2, suma_de_4_entradas_7_acarreo_2, suma_de_4_entradas_8_acarreo_2, suma_de_4_entradas_9_acarreo_2, suma_de_4_entradas_10_acarreo_2}

  // Notes on the sheet:
  //   EXPONENTE
  //   B1
endmodule

module Potencia__P___P___P___P___P___P (
  input  E1,
  input  E2,
  input  E3,
  output out_4,
  output out_5,
  output out_6,
  output out_7,
  output out_8,
  output out_9,
  output out_10,
  output out_11,
  output out_12,
  output out_13,
  output out_14,
  output out_15,
  output out_16,
  output out_17,
  output out_18,
  output out_19,
  output out_20
);

  wire \multiplicación_de_15_1_1_resultado_1 , \multiplicación_de_15_1_1_resultado_2 ,
       \multiplicación_de_15_1_1_resultado_3 , \multiplicación_de_15_1_1_resultado_4 ,
       \multiplicación_de_15_1_1_resultado_5 , \multiplicación_de_15_1_1_resultado_6 ,
       \multiplicación_de_15_1_1_resultado_7 , \multiplicación_de_15_1_1_resultado_8 ,
       \multiplicación_de_15_1_1_resultado_9 , \multiplicación_de_15_1_1_resultado_10 ,
       \multiplicación_de_15_1_1_resultado_11 , \multiplicación_de_15_1_1_resultado_12 ,
       \multiplicación_de_15_1_1_resultado_13 , \multiplicación_de_15_1_1_resultado_14 ,
       \multiplicación_de_15_1_2_resultado_1 , \multiplicación_de_15_1_2_resultado_2 ,
       \multiplicación_de_15_1_2_resultado_3 , \multiplicación_de_15_1_2_resultado_4 ,
       \multiplicación_de_15_1_2_resultado_5 , \multiplicación_de_15_1_2_resultado_6 ,
       \multiplicación_de_15_1_2_resultado_7 , \multiplicación_de_15_1_2_resultado_8 ,
       \multiplicación_de_15_1_2_resultado_9 , \multiplicación_de_15_1_2_resultado_10 ,
       \multiplicación_de_15_1_2_resultado_11 , \multiplicación_de_15_1_2_resultado_12 ,
       \multiplicación_de_15_1_2_resultado_13 , \multiplicación_de_15_1_2_resultado_14 ,
       \multiplicación_de_15_1_2_resultado_15 , \multiplicación_de_15_1_3_resultado_1 ,
       \multiplicación_de_15_1_3_resultado_2 , \multiplicación_de_15_1_3_resultado_3 ,
       \multiplicación_de_15_1_3_resultado_4 , \multiplicación_de_15_1_3_resultado_5 ,
       \multiplicación_de_15_1_3_resultado_6 , \multiplicación_de_15_1_3_resultado_7 ,
       \multiplicación_de_15_1_3_resultado_8 , \multiplicación_de_15_1_3_resultado_9 ,
       \multiplicación_de_15_1_3_resultado_10 , \multiplicación_de_15_1_3_resultado_11 ,
       \multiplicación_de_15_1_3_resultado_12 , \multiplicación_de_15_1_3_resultado_13 ,
       \multiplicación_de_15_1_3_resultado_14 , \multiplicación_de_15_1_3_resultado_15 ,
       potencia_p_p_p_p_p_1_out_4, potencia_p_p_p_p_p_1_out_5, potencia_p_p_p_p_p_1_out_6,
       potencia_p_p_p_p_p_1_out_7, potencia_p_p_p_p_p_1_out_8, potencia_p_p_p_p_p_1_out_9,
       potencia_p_p_p_p_p_1_out_10, potencia_p_p_p_p_p_1_out_11, potencia_p_p_p_p_p_1_out_12,
       potencia_p_p_p_p_p_1_out_13, potencia_p_p_p_p_p_1_out_14, potencia_p_p_p_p_p_1_out_15,
       potencia_p_p_p_p_p_1_out_16, potencia_p_p_p_p_p_1_out_17, potencia_p_p_p_p_p_1_out_18,
       suma_de_2_entradas_1_acarreo_1, suma_de_2_entradas_2_acarreo_1, suma_de_3_entradas_1_acarreo_1,
       suma_de_4_entradas_1_acarreo_1, suma_de_4_entradas_1_acarreo_2, suma_de_4_entradas_2_acarreo_1,
       suma_de_4_entradas_2_acarreo_2, suma_de_4_entradas_3_acarreo_1, suma_de_4_entradas_3_acarreo_2,
       suma_de_4_entradas_4_acarreo_1, suma_de_4_entradas_4_acarreo_2, suma_de_4_entradas_5_acarreo_1,
       suma_de_4_entradas_5_acarreo_2, suma_de_4_entradas_6_acarreo_1, suma_de_4_entradas_6_acarreo_2,
       suma_de_4_entradas_7_acarreo_1, suma_de_4_entradas_7_acarreo_2, suma_de_4_entradas_8_acarreo_1,
       suma_de_4_entradas_8_acarreo_2, suma_de_4_entradas_9_acarreo_1, suma_de_4_entradas_9_acarreo_2,
       suma_de_4_entradas_10_acarreo_1, suma_de_4_entradas_10_acarreo_2, suma_de_4_entradas_11_acarreo_1,
       suma_de_4_entradas_11_acarreo_2, suma_de_4_entradas_12_acarreo_1, suma_de_4_entradas_12_acarreo_2,
       suma_de_5_entradas_1_acarreo_1, suma_de_5_entradas_1_acarreo_2;

  Potencia__P___P___P___P___P potencia_p_p_p_p_p_1 (
    .E1(E1), .E2(E2), .E3(E3), .out_4(potencia_p_p_p_p_p_1_out_4), .out_5(potencia_p_p_p_p_p_1_out_5),
    .out_6(potencia_p_p_p_p_p_1_out_6), .out_7(potencia_p_p_p_p_p_1_out_7),
    .out_8(potencia_p_p_p_p_p_1_out_8), .out_9(potencia_p_p_p_p_p_1_out_9),
    .out_10(potencia_p_p_p_p_p_1_out_10), .out_11(potencia_p_p_p_p_p_1_out_11),
    .out_12(potencia_p_p_p_p_p_1_out_12), .out_13(potencia_p_p_p_p_p_1_out_13),
    .out_14(potencia_p_p_p_p_p_1_out_14), .out_15(potencia_p_p_p_p_p_1_out_15),
    .out_16(potencia_p_p_p_p_p_1_out_16), .out_17(potencia_p_p_p_p_p_1_out_17),
    .out_18(potencia_p_p_p_p_p_1_out_18));
  \Multiplicación_de_15___1  \multiplicación_de_15_1_1  (
    .ENTRADAS(potencia_p_p_p_p_p_1_out_18), .in_2(potencia_p_p_p_p_p_1_out_17),
    .MULTIPLICANDO_3(potencia_p_p_p_p_p_1_out_16), .MULTIPLICANDO_4(potencia_p_p_p_p_p_1_out_15),
    .MULTIPLICANDO_5(potencia_p_p_p_p_p_1_out_14), .in_6(potencia_p_p_p_p_p_1_out_13),
    .MULTIPLICANDO_7(potencia_p_p_p_p_p_1_out_12), .MULTIPLICANDO_8(potencia_p_p_p_p_p_1_out_11),
    .in_9(potencia_p_p_p_p_p_1_out_10), .MULTIPLICANDO_10(potencia_p_p_p_p_p_1_out_9),
    .MULTIPLICANDO_11(potencia_p_p_p_p_p_1_out_8), .in_12(potencia_p_p_p_p_p_1_out_7),
    .in_13(potencia_p_p_p_p_p_1_out_6), .in_14(potencia_p_p_p_p_p_1_out_4),
    .in_15(potencia_p_p_p_p_p_1_out_5), .MULTIPLICADOR(E3),
    .RESULTADO_1(\multiplicación_de_15_1_1_resultado_1 ),
    .RESULTADO_2(\multiplicación_de_15_1_1_resultado_2 ),
    .RESULTADO_3(\multiplicación_de_15_1_1_resultado_3 ),
    .RESULTADO_4(\multiplicación_de_15_1_1_resultado_4 ),
    .RESULTADO_5(\multiplicación_de_15_1_1_resultado_5 ),
    .RESULTADO_6(\multiplicación_de_15_1_1_resultado_6 ),
    .RESULTADO_7(\multiplicación_de_15_1_1_resultado_7 ),
    .RESULTADO_8(\multiplicación_de_15_1_1_resultado_8 ),
    .RESULTADO_9(\multiplicación_de_15_1_1_resultado_9 ),
    .RESULTADO_10(\multiplicación_de_15_1_1_resultado_10 ),
    .RESULTADO_11(\multiplicación_de_15_1_1_resultado_11 ),
    .RESULTADO_12(\multiplicación_de_15_1_1_resultado_12 ),
    .RESULTADO_13(\multiplicación_de_15_1_1_resultado_13 ),
    .RESULTADO_14(\multiplicación_de_15_1_1_resultado_14 ), .RESULTADO_15(out_5));
  \Multiplicación_de_15___1  \multiplicación_de_15_1_2  (
    .ENTRADAS(potencia_p_p_p_p_p_1_out_18), .in_2(potencia_p_p_p_p_p_1_out_17),
    .MULTIPLICANDO_3(potencia_p_p_p_p_p_1_out_16), .MULTIPLICANDO_4(potencia_p_p_p_p_p_1_out_15),
    .MULTIPLICANDO_5(potencia_p_p_p_p_p_1_out_14), .in_6(potencia_p_p_p_p_p_1_out_13),
    .MULTIPLICANDO_7(potencia_p_p_p_p_p_1_out_12), .MULTIPLICANDO_8(potencia_p_p_p_p_p_1_out_11),
    .in_9(potencia_p_p_p_p_p_1_out_10), .MULTIPLICANDO_10(potencia_p_p_p_p_p_1_out_9),
    .MULTIPLICANDO_11(potencia_p_p_p_p_p_1_out_8), .in_12(potencia_p_p_p_p_p_1_out_7),
    .in_13(potencia_p_p_p_p_p_1_out_6), .in_14(potencia_p_p_p_p_p_1_out_4),
    .in_15(potencia_p_p_p_p_p_1_out_5), .MULTIPLICADOR(E2),
    .RESULTADO_1(\multiplicación_de_15_1_2_resultado_1 ),
    .RESULTADO_2(\multiplicación_de_15_1_2_resultado_2 ),
    .RESULTADO_3(\multiplicación_de_15_1_2_resultado_3 ),
    .RESULTADO_4(\multiplicación_de_15_1_2_resultado_4 ),
    .RESULTADO_5(\multiplicación_de_15_1_2_resultado_5 ),
    .RESULTADO_6(\multiplicación_de_15_1_2_resultado_6 ),
    .RESULTADO_7(\multiplicación_de_15_1_2_resultado_7 ),
    .RESULTADO_8(\multiplicación_de_15_1_2_resultado_8 ),
    .RESULTADO_9(\multiplicación_de_15_1_2_resultado_9 ),
    .RESULTADO_10(\multiplicación_de_15_1_2_resultado_10 ),
    .RESULTADO_11(\multiplicación_de_15_1_2_resultado_11 ),
    .RESULTADO_12(\multiplicación_de_15_1_2_resultado_12 ),
    .RESULTADO_13(\multiplicación_de_15_1_2_resultado_13 ),
    .RESULTADO_14(\multiplicación_de_15_1_2_resultado_14 ),
    .RESULTADO_15(\multiplicación_de_15_1_2_resultado_15 ));
  \Multiplicación_de_15___1  \multiplicación_de_15_1_3  (
    .ENTRADAS(potencia_p_p_p_p_p_1_out_18), .in_2(potencia_p_p_p_p_p_1_out_17),
    .MULTIPLICANDO_3(potencia_p_p_p_p_p_1_out_16), .MULTIPLICANDO_4(potencia_p_p_p_p_p_1_out_15),
    .MULTIPLICANDO_5(potencia_p_p_p_p_p_1_out_14), .in_6(potencia_p_p_p_p_p_1_out_13),
    .MULTIPLICANDO_7(potencia_p_p_p_p_p_1_out_12), .MULTIPLICANDO_8(potencia_p_p_p_p_p_1_out_11),
    .in_9(potencia_p_p_p_p_p_1_out_10), .MULTIPLICANDO_10(potencia_p_p_p_p_p_1_out_9),
    .MULTIPLICANDO_11(potencia_p_p_p_p_p_1_out_8), .in_12(potencia_p_p_p_p_p_1_out_7),
    .in_13(potencia_p_p_p_p_p_1_out_6), .in_14(potencia_p_p_p_p_p_1_out_4),
    .in_15(potencia_p_p_p_p_p_1_out_5), .MULTIPLICADOR(E1),
    .RESULTADO_1(\multiplicación_de_15_1_3_resultado_1 ),
    .RESULTADO_2(\multiplicación_de_15_1_3_resultado_2 ),
    .RESULTADO_3(\multiplicación_de_15_1_3_resultado_3 ),
    .RESULTADO_4(\multiplicación_de_15_1_3_resultado_4 ),
    .RESULTADO_5(\multiplicación_de_15_1_3_resultado_5 ),
    .RESULTADO_6(\multiplicación_de_15_1_3_resultado_6 ),
    .RESULTADO_7(\multiplicación_de_15_1_3_resultado_7 ),
    .RESULTADO_8(\multiplicación_de_15_1_3_resultado_8 ),
    .RESULTADO_9(\multiplicación_de_15_1_3_resultado_9 ),
    .RESULTADO_10(\multiplicación_de_15_1_3_resultado_10 ),
    .RESULTADO_11(\multiplicación_de_15_1_3_resultado_11 ),
    .RESULTADO_12(\multiplicación_de_15_1_3_resultado_12 ),
    .RESULTADO_13(\multiplicación_de_15_1_3_resultado_13 ),
    .RESULTADO_14(\multiplicación_de_15_1_3_resultado_14 ),
    .RESULTADO_15(\multiplicación_de_15_1_3_resultado_15 ));
  Suma_de_2_Entradas suma_de_2_entradas_1 (
    .E1(\multiplicación_de_15_1_1_resultado_14 ), .E2(\multiplicación_de_15_1_2_resultado_15 ),
    .ACARREO_1(suma_de_2_entradas_1_acarreo_1), .out_3(out_4));
  Suma_de_4_Entradas suma_de_4_entradas_1 (
    .E1(suma_de_2_entradas_1_acarreo_1), .E2(\multiplicación_de_15_1_1_resultado_13 ),
    .E3(\multiplicación_de_15_1_2_resultado_14 ), .E4(\multiplicación_de_15_1_3_resultado_15 ),
    .out_5(out_6), .ACARREO_1(suma_de_4_entradas_1_acarreo_1), .ACARREO_2(suma_de_4_entradas_1_acarreo_2));
  Suma_de_4_Entradas suma_de_4_entradas_2 (
    .E1(suma_de_4_entradas_1_acarreo_1), .E2(\multiplicación_de_15_1_1_resultado_12 ),
    .E3(\multiplicación_de_15_1_2_resultado_13 ), .E4(\multiplicación_de_15_1_3_resultado_14 ),
    .out_5(out_7), .ACARREO_1(suma_de_4_entradas_2_acarreo_1), .ACARREO_2(suma_de_4_entradas_2_acarreo_2));
  Suma_de_5_Entradas suma_de_5_entradas_1 (
    .E1(suma_de_4_entradas_1_acarreo_2), .E2(suma_de_4_entradas_2_acarreo_1),
    .E3(\multiplicación_de_15_1_1_resultado_11 ), .E4(\multiplicación_de_15_1_2_resultado_12 ),
    .E5(\multiplicación_de_15_1_3_resultado_13 ), .out_6(out_8), .ACARREO_1(suma_de_5_entradas_1_acarreo_1),
    .ACARREO_2(suma_de_5_entradas_1_acarreo_2));
  Suma_de_4_Entradas suma_de_4_entradas_3 (
    .E1(suma_de_5_entradas_1_acarreo_1), .E2(\multiplicación_de_15_1_1_resultado_10 ),
    .E3(\multiplicación_de_15_1_2_resultado_11 ), .E4(\multiplicación_de_15_1_3_resultado_12 ),
    .out_5(out_9), .ACARREO_1(suma_de_4_entradas_3_acarreo_1), .ACARREO_2(suma_de_4_entradas_3_acarreo_2));
  Suma_de_4_Entradas suma_de_4_entradas_4 (
    .E1(suma_de_4_entradas_3_acarreo_1), .E2(\multiplicación_de_15_1_1_resultado_9 ),
    .E3(\multiplicación_de_15_1_2_resultado_10 ), .E4(\multiplicación_de_15_1_3_resultado_11 ),
    .out_5(out_10), .ACARREO_1(suma_de_4_entradas_4_acarreo_1), .ACARREO_2(suma_de_4_entradas_4_acarreo_2));
  Suma_de_4_Entradas suma_de_4_entradas_5 (
    .E1(suma_de_4_entradas_4_acarreo_1), .E2(\multiplicación_de_15_1_1_resultado_8 ),
    .E3(\multiplicación_de_15_1_2_resultado_9 ), .E4(\multiplicación_de_15_1_3_resultado_10 ),
    .out_5(out_11), .ACARREO_1(suma_de_4_entradas_5_acarreo_1), .ACARREO_2(suma_de_4_entradas_5_acarreo_2));
  Suma_de_4_Entradas suma_de_4_entradas_6 (
    .E1(suma_de_4_entradas_5_acarreo_1), .E2(\multiplicación_de_15_1_1_resultado_7 ),
    .E3(\multiplicación_de_15_1_2_resultado_8 ), .E4(\multiplicación_de_15_1_3_resultado_9 ), .out_5(out_12),
    .ACARREO_1(suma_de_4_entradas_6_acarreo_1), .ACARREO_2(suma_de_4_entradas_6_acarreo_2));
  Suma_de_4_Entradas suma_de_4_entradas_7 (
    .E1(suma_de_4_entradas_6_acarreo_1), .E2(\multiplicación_de_15_1_1_resultado_6 ),
    .E3(\multiplicación_de_15_1_2_resultado_7 ), .E4(\multiplicación_de_15_1_3_resultado_8 ), .out_5(out_13),
    .ACARREO_1(suma_de_4_entradas_7_acarreo_1), .ACARREO_2(suma_de_4_entradas_7_acarreo_2));
  Suma_de_4_Entradas suma_de_4_entradas_8 (
    .E1(suma_de_4_entradas_7_acarreo_1), .E2(\multiplicación_de_15_1_1_resultado_5 ),
    .E3(\multiplicación_de_15_1_2_resultado_6 ), .E4(\multiplicación_de_15_1_3_resultado_7 ), .out_5(out_14),
    .ACARREO_1(suma_de_4_entradas_8_acarreo_1), .ACARREO_2(suma_de_4_entradas_8_acarreo_2));
  Suma_de_4_Entradas suma_de_4_entradas_9 (
    .E1(suma_de_4_entradas_8_acarreo_1), .E2(\multiplicación_de_15_1_1_resultado_4 ),
    .E3(\multiplicación_de_15_1_2_resultado_5 ), .E4(\multiplicación_de_15_1_3_resultado_6 ), .out_5(out_15),
    .ACARREO_1(suma_de_4_entradas_9_acarreo_1), .ACARREO_2(suma_de_4_entradas_9_acarreo_2));
  Suma_de_4_Entradas suma_de_4_entradas_10 (
    .E1(suma_de_4_entradas_9_acarreo_1), .E2(\multiplicación_de_15_1_1_resultado_3 ),
    .E3(\multiplicación_de_15_1_2_resultado_4 ), .E4(\multiplicación_de_15_1_3_resultado_5 ), .out_5(out_16),
    .ACARREO_1(suma_de_4_entradas_10_acarreo_1), .ACARREO_2(suma_de_4_entradas_10_acarreo_2));
  Suma_de_4_Entradas suma_de_4_entradas_11 (
    .E1(suma_de_4_entradas_10_acarreo_1), .E2(\multiplicación_de_15_1_1_resultado_2 ),
    .E3(\multiplicación_de_15_1_2_resultado_3 ), .E4(\multiplicación_de_15_1_3_resultado_4 ), .out_5(out_17),
    .ACARREO_1(suma_de_4_entradas_11_acarreo_1), .ACARREO_2(suma_de_4_entradas_11_acarreo_2));
  Suma_de_4_Entradas suma_de_4_entradas_12 (
    .E1(suma_de_4_entradas_11_acarreo_1), .E2(\multiplicación_de_15_1_1_resultado_1 ),
    .E3(\multiplicación_de_15_1_2_resultado_2 ), .E4(\multiplicación_de_15_1_3_resultado_3 ), .out_5(out_18),
    .ACARREO_1(suma_de_4_entradas_12_acarreo_1), .ACARREO_2(suma_de_4_entradas_12_acarreo_2));
  Suma_de_3_Entradas suma_de_3_entradas_1 (
    .E1(suma_de_4_entradas_12_acarreo_1), .E2(\multiplicación_de_15_1_2_resultado_1 ),
    .E3(\multiplicación_de_15_1_3_resultado_2 ), .out_4(out_19), .ACARREO_1(suma_de_3_entradas_1_acarreo_1));
  Suma_de_2_Entradas suma_de_2_entradas_2 (
    .E1(suma_de_3_entradas_1_acarreo_1), .E2(\multiplicación_de_15_1_3_resultado_1 ),
    .ACARREO_1(suma_de_2_entradas_2_acarreo_1), .out_3(out_20));
  // also tied to GND on the sheet: {suma_de_4_entradas_2_acarreo_2, suma_de_5_entradas_1_acarreo_2, suma_de_4_entradas_3_acarreo_2, suma_de_4_entradas_4_acarreo_2, suma_de_4_entradas_5_acarreo_2, suma_de_4_entradas_6_acarreo_2, suma_de_4_entradas_7_acarreo_2, suma_de_4_entradas_8_acarreo_2, suma_de_4_entradas_9_acarreo_2, suma_de_4_entradas_10_acarreo_2, suma_de_4_entradas_11_acarreo_2, suma_de_4_entradas_12_acarreo_2, suma_de_2_entradas_2_acarreo_1}

  // Notes on the sheet:
  //   ENTRADAS
endmodule

module \Elección_Potencia_p___6  (
  input  E1,
  input  E2,
  input  E3,
  input  BASE,
  input  B2,
  input  B3,
  output out_7,
  output out_8,
  output out_9,
  output out_10,
  output out_11,
  output out_12,
  output out_13,
  output out_14,
  output out_15,
  output out_16,
  output out_17,
  output out_18,
  output out_19,
  output out_20,
  output out_21,
  output out_22,
  output out_23
);

  wire and_1_out, \multiplicación_de_15_1_1_resultado_1 , \multiplicación_de_15_1_1_resultado_2 ,
       \multiplicación_de_15_1_1_resultado_3 , \multiplicación_de_15_1_1_resultado_4 ,
       \multiplicación_de_15_1_1_resultado_5 , \multiplicación_de_15_1_1_resultado_6 ,
       \multiplicación_de_15_1_1_resultado_7 , \multiplicación_de_15_1_1_resultado_8 ,
       \multiplicación_de_15_1_1_resultado_9 , \multiplicación_de_15_1_1_resultado_10 ,
       \multiplicación_de_15_1_1_resultado_11 , \multiplicación_de_15_1_1_resultado_12 ,
       \multiplicación_de_15_1_1_resultado_13 , \multiplicación_de_15_1_1_resultado_14 ,
       \multiplicación_de_15_1_1_resultado_15 , \multiplicación_de_15_1_2_resultado_1 ,
       \multiplicación_de_15_1_2_resultado_2 , \multiplicación_de_15_1_2_resultado_3 ,
       \multiplicación_de_15_1_2_resultado_4 , \multiplicación_de_15_1_2_resultado_5 ,
       \multiplicación_de_15_1_2_resultado_6 , \multiplicación_de_15_1_2_resultado_7 ,
       \multiplicación_de_15_1_2_resultado_8 , \multiplicación_de_15_1_2_resultado_9 ,
       \multiplicación_de_15_1_2_resultado_10 , \multiplicación_de_15_1_2_resultado_11 ,
       \multiplicación_de_15_1_2_resultado_12 , \multiplicación_de_15_1_2_resultado_13 ,
       \multiplicación_de_15_1_2_resultado_14 , \multiplicación_de_15_1_2_resultado_15 ,
       \multiplicación_de_15_1_3_resultado_1 , \multiplicación_de_15_1_3_resultado_2 ,
       \multiplicación_de_15_1_3_resultado_3 , \multiplicación_de_15_1_3_resultado_4 ,
       \multiplicación_de_15_1_3_resultado_5 , \multiplicación_de_15_1_3_resultado_6 ,
       \multiplicación_de_15_1_3_resultado_7 , \multiplicación_de_15_1_3_resultado_8 ,
       \multiplicación_de_15_1_3_resultado_9 , \multiplicación_de_15_1_3_resultado_10 ,
       \multiplicación_de_15_1_3_resultado_11 , \multiplicación_de_15_1_3_resultado_12 ,
       \multiplicación_de_15_1_3_resultado_13 , \multiplicación_de_15_1_3_resultado_14 ,
       \multiplicación_de_15_1_3_resultado_15 , not_1_out, potencia_p_p_p_p_p_1_out_4,
       potencia_p_p_p_p_p_1_out_5, potencia_p_p_p_p_p_1_out_6, potencia_p_p_p_p_p_1_out_7,
       potencia_p_p_p_p_p_1_out_8, potencia_p_p_p_p_p_1_out_9, potencia_p_p_p_p_p_1_out_10,
       potencia_p_p_p_p_p_1_out_11, potencia_p_p_p_p_p_1_out_12, potencia_p_p_p_p_p_1_out_13,
       potencia_p_p_p_p_p_1_out_14, potencia_p_p_p_p_p_1_out_15, potencia_p_p_p_p_p_1_out_16,
       potencia_p_p_p_p_p_1_out_17, potencia_p_p_p_p_p_1_out_18, suma_de_2_entradas_1_acarreo_1,
       suma_de_2_entradas_1_out_3, suma_de_2_entradas_2_acarreo_1, suma_de_2_entradas_2_out_3,
       suma_de_3_entradas_1_acarreo_1, suma_de_3_entradas_1_out_4, suma_de_4_entradas_1_acarreo_1,
       suma_de_4_entradas_1_acarreo_2, suma_de_4_entradas_1_out_5, suma_de_4_entradas_2_acarreo_1,
       suma_de_4_entradas_2_acarreo_2, suma_de_4_entradas_2_out_5, suma_de_4_entradas_3_acarreo_1,
       suma_de_4_entradas_3_acarreo_2, suma_de_4_entradas_3_out_5, suma_de_4_entradas_4_acarreo_1,
       suma_de_4_entradas_4_acarreo_2, suma_de_4_entradas_4_out_5, suma_de_4_entradas_5_acarreo_1,
       suma_de_4_entradas_5_acarreo_2, suma_de_4_entradas_5_out_5, suma_de_4_entradas_6_acarreo_1,
       suma_de_4_entradas_6_acarreo_2, suma_de_4_entradas_6_out_5, suma_de_4_entradas_7_acarreo_1,
       suma_de_4_entradas_7_acarreo_2, suma_de_4_entradas_7_out_5, suma_de_4_entradas_8_acarreo_1,
       suma_de_4_entradas_8_acarreo_2, suma_de_4_entradas_8_out_5, suma_de_4_entradas_9_acarreo_1,
       suma_de_4_entradas_9_acarreo_2, suma_de_4_entradas_9_out_5, suma_de_4_entradas_10_acarreo_1,
       suma_de_4_entradas_10_acarreo_2, suma_de_4_entradas_10_out_5, suma_de_4_entradas_11_acarreo_1,
       suma_de_4_entradas_11_acarreo_2, suma_de_4_entradas_11_out_5, suma_de_4_entradas_12_acarreo_1,
       suma_de_4_entradas_12_acarreo_2, suma_de_4_entradas_12_out_5, suma_de_5_entradas_1_acarreo_1,
       suma_de_5_entradas_1_acarreo_2, suma_de_5_entradas_1_out_6;

  not not_1 (not_1_out, E3);
  Potencia__P___P___P___P___P potencia_p_p_p_p_p_1 (
    .E1(BASE), .E2(B2), .E3(B3), .out_4(potencia_p_p_p_p_p_1_out_4), .out_5(potencia_p_p_p_p_p_1_out_5),
    .out_6(potencia_p_p_p_p_p_1_out_6), .out_7(potencia_p_p_p_p_p_1_out_7),
    .out_8(potencia_p_p_p_p_p_1_out_8), .out_9(potencia_p_p_p_p_p_1_out_9),
    .out_10(potencia_p_p_p_p_p_1_out_10), .out_11(potencia_p_p_p_p_p_1_out_11),
    .out_12(potencia_p_p_p_p_p_1_out_12), .out_13(potencia_p_p_p_p_p_1_out_13),
    .out_14(potencia_p_p_p_p_p_1_out_14), .out_15(potencia_p_p_p_p_p_1_out_15),
    .out_16(potencia_p_p_p_p_p_1_out_16), .out_17(potencia_p_p_p_p_p_1_out_17),
    .out_18(potencia_p_p_p_p_p_1_out_18));
  and and_1 (and_1_out, E1, E2, not_1_out);
  \Multiplicación_de_15___1  \multiplicación_de_15_1_1  (
    .ENTRADAS(potencia_p_p_p_p_p_1_out_18), .in_2(potencia_p_p_p_p_p_1_out_17),
    .MULTIPLICANDO_3(potencia_p_p_p_p_p_1_out_16), .MULTIPLICANDO_4(potencia_p_p_p_p_p_1_out_15),
    .MULTIPLICANDO_5(potencia_p_p_p_p_p_1_out_14), .in_6(potencia_p_p_p_p_p_1_out_13),
    .MULTIPLICANDO_7(potencia_p_p_p_p_p_1_out_12), .MULTIPLICANDO_8(potencia_p_p_p_p_p_1_out_11),
    .in_9(potencia_p_p_p_p_p_1_out_10), .MULTIPLICANDO_10(potencia_p_p_p_p_p_1_out_9),
    .MULTIPLICANDO_11(potencia_p_p_p_p_p_1_out_8), .in_12(potencia_p_p_p_p_p_1_out_7),
    .in_13(potencia_p_p_p_p_p_1_out_6), .in_14(potencia_p_p_p_p_p_1_out_4),
    .in_15(potencia_p_p_p_p_p_1_out_5), .MULTIPLICADOR(B3),
    .RESULTADO_1(\multiplicación_de_15_1_1_resultado_1 ),
    .RESULTADO_2(\multiplicación_de_15_1_1_resultado_2 ),
    .RESULTADO_3(\multiplicación_de_15_1_1_resultado_3 ),
    .RESULTADO_4(\multiplicación_de_15_1_1_resultado_4 ),
    .RESULTADO_5(\multiplicación_de_15_1_1_resultado_5 ),
    .RESULTADO_6(\multiplicación_de_15_1_1_resultado_6 ),
    .RESULTADO_7(\multiplicación_de_15_1_1_resultado_7 ),
    .RESULTADO_8(\multiplicación_de_15_1_1_resultado_8 ),
    .RESULTADO_9(\multiplicación_de_15_1_1_resultado_9 ),
    .RESULTADO_10(\multiplicación_de_15_1_1_resultado_10 ),
    .RESULTADO_11(\multiplicación_de_15_1_1_resultado_11 ),
    .RESULTADO_12(\multiplicación_de_15_1_1_resultado_12 ),
    .RESULTADO_13(\multiplicación_de_15_1_1_resultado_13 ),
    .RESULTADO_14(\multiplicación_de_15_1_1_resultado_14 ),
    .RESULTADO_15(\multiplicación_de_15_1_1_resultado_15 ));
  \Multiplicación_de_15___1  \multiplicación_de_15_1_2  (
    .ENTRADAS(potencia_p_p_p_p_p_1_out_18), .in_2(potencia_p_p_p_p_p_1_out_17),
    .MULTIPLICANDO_3(potencia_p_p_p_p_p_1_out_16), .MULTIPLICANDO_4(potencia_p_p_p_p_p_1_out_15),
    .MULTIPLICANDO_5(potencia_p_p_p_p_p_1_out_14), .in_6(potencia_p_p_p_p_p_1_out_13),
    .MULTIPLICANDO_7(potencia_p_p_p_p_p_1_out_12), .MULTIPLICANDO_8(potencia_p_p_p_p_p_1_out_11),
    .in_9(potencia_p_p_p_p_p_1_out_10), .MULTIPLICANDO_10(potencia_p_p_p_p_p_1_out_9),
    .MULTIPLICANDO_11(potencia_p_p_p_p_p_1_out_8), .in_12(potencia_p_p_p_p_p_1_out_7),
    .in_13(potencia_p_p_p_p_p_1_out_6), .in_14(potencia_p_p_p_p_p_1_out_4),
    .in_15(potencia_p_p_p_p_p_1_out_5), .MULTIPLICADOR(B2),
    .RESULTADO_1(\multiplicación_de_15_1_2_resultado_1 ),
    .RESULTADO_2(\multiplicación_de_15_1_2_resultado_2 ),
    .RESULTADO_3(\multiplicación_de_15_1_2_resultado_3 ),
    .RESULTADO_4(\multiplicación_de_15_1_2_resultado_4 ),
    .RESULTADO_5(\multiplicación_de_15_1_2_resultado_5 ),
    .RESULTADO_6(\multiplicación_de_15_1_2_resultado_6 ),
    .RESULTADO_7(\multiplicación_de_15_1_2_resultado_7 ),
    .RESULTADO_8(\multiplicación_de_15_1_2_resultado_8 ),
    .RESULTADO_9(\multiplicación_de_15_1_2_resultado_9 ),
    .RESULTADO_10(\multiplicación_de_15_1_2_resultado_10 ),
    .RESULTADO_11(\multiplicación_de_15_1_2_resultado_11 ),
    .RESULTADO_12(\multiplicación_de_15_1_2_resultado_12 ),
    .RESULTADO_13(\multiplicación_de_15_1_2_resultado_13 ),
    .RESULTADO_14(\multiplicación_de_15_1_2_resultado_14 ),
    .RESULTADO_15(\multiplicación_de_15_1_2_resultado_15 ));
  \Multiplicación_de_15___1  \multiplicación_de_15_1_3  (
    .ENTRADAS(potencia_p_p_p_p_p_1_out_18), .in_2(potencia_p_p_p_p_p_1_out_17),
    .MULTIPLICANDO_3(potencia_p_p_p_p_p_1_out_16), .MULTIPLICANDO_4(potencia_p_p_p_p_p_1_out_15),
    .MULTIPLICANDO_5(potencia_p_p_p_p_p_1_out_14), .in_6(potencia_p_p_p_p_p_1_out_13),
    .MULTIPLICANDO_7(potencia_p_p_p_p_p_1_out_12), .MULTIPLICANDO_8(potencia_p_p_p_p_p_1_out_11),
    .in_9(potencia_p_p_p_p_p_1_out_10), .MULTIPLICANDO_10(potencia_p_p_p_p_p_1_out_9),
    .MULTIPLICANDO_11(potencia_p_p_p_p_p_1_out_8), .in_12(potencia_p_p_p_p_p_1_out_7),
    .in_13(potencia_p_p_p_p_p_1_out_6), .in_14(potencia_p_p_p_p_p_1_out_4),
    .in_15(potencia_p_p_p_p_p_1_out_5), .MULTIPLICADOR(BASE),
    .RESULTADO_1(\multiplicación_de_15_1_3_resultado_1 ),
    .RESULTADO_2(\multiplicación_de_15_1_3_resultado_2 ),
    .RESULTADO_3(\multiplicación_de_15_1_3_resultado_3 ),
    .RESULTADO_4(\multiplicación_de_15_1_3_resultado_4 ),
    .RESULTADO_5(\multiplicación_de_15_1_3_resultado_5 ),
    .RESULTADO_6(\multiplicación_de_15_1_3_resultado_6 ),
    .RESULTADO_7(\multiplicación_de_15_1_3_resultado_7 ),
    .RESULTADO_8(\multiplicación_de_15_1_3_resultado_8 ),
    .RESULTADO_9(\multiplicación_de_15_1_3_resultado_9 ),
    .RESULTADO_10(\multiplicación_de_15_1_3_resultado_10 ),
    .RESULTADO_11(\multiplicación_de_15_1_3_resultado_11 ),
    .RESULTADO_12(\multiplicación_de_15_1_3_resultado_12 ),
    .RESULTADO_13(\multiplicación_de_15_1_3_resultado_13 ),
    .RESULTADO_14(\multiplicación_de_15_1_3_resultado_14 ),
    .RESULTADO_15(\multiplicación_de_15_1_3_resultado_15 ));
  and and_2 (out_23, and_1_out, \multiplicación_de_15_1_1_resultado_15 );
  Suma_de_2_Entradas suma_de_2_entradas_1 (
    .E1(\multiplicación_de_15_1_1_resultado_14 ), .E2(\multiplicación_de_15_1_2_resultado_15 ),
    .ACARREO_1(suma_de_2_entradas_1_acarreo_1), .out_3(suma_de_2_entradas_1_out_3));
  and and_3 (out_22, and_1_out, suma_de_2_entradas_1_out_3);
  Suma_de_4_Entradas suma_de_4_entradas_1 (
    .E1(suma_de_2_entradas_1_acarreo_1), .E2(\multiplicación_de_15_1_1_resultado_13 ),
    .E3(\multiplicación_de_15_1_2_resultado_14 ), .E4(\multiplicación_de_15_1_3_resultado_15 ),
    .out_5(suma_de_4_entradas_1_out_5), .ACARREO_1(suma_de_4_entradas_1_acarreo_1),
    .ACARREO_2(suma_de_4_entradas_1_acarreo_2));
  and and_4 (out_21, and_1_out, suma_de_4_entradas_1_out_5);
  Suma_de_4_Entradas suma_de_4_entradas_2 (
    .E1(suma_de_4_entradas_1_acarreo_1), .E2(\multiplicación_de_15_1_1_resultado_12 ),
    .E3(\multiplicación_de_15_1_2_resultado_13 ), .E4(\multiplicación_de_15_1_3_resultado_14 ),
    .out_5(suma_de_4_entradas_2_out_5), .ACARREO_1(suma_de_4_entradas_2_acarreo_1),
    .ACARREO_2(suma_de_4_entradas_2_acarreo_2));
  and and_5 (out_20, and_1_out, suma_de_4_entradas_2_out_5);
  Suma_de_5_Entradas suma_de_5_entradas_1 (
    .E1(suma_de_4_entradas_1_acarreo_2), .E2(suma_de_4_entradas_2_acarreo_1),
    .E3(\multiplicación_de_15_1_1_resultado_11 ), .E4(\multiplicación_de_15_1_2_resultado_12 ),
    .E5(\multiplicación_de_15_1_3_resultado_13 ), .out_6(suma_de_5_entradas_1_out_6),
    .ACARREO_1(suma_de_5_entradas_1_acarreo_1), .ACARREO_2(suma_de_5_entradas_1_acarreo_2));
  Suma_de_4_Entradas suma_de_4_entradas_3 (
    .E1(suma_de_5_entradas_1_acarreo_1), .E2(\multiplicación_de_15_1_1_resultado_10 ),
    .E3(\multiplicación_de_15_1_2_resultado_11 ), .E4(\multiplicación_de_15_1_3_resultado_12 ),
    .out_5(suma_de_4_entradas_3_out_5), .ACARREO_1(suma_de_4_entradas_3_acarreo_1),
    .ACARREO_2(suma_de_4_entradas_3_acarreo_2));
  and and_6 (out_19, and_1_out, suma_de_5_entradas_1_out_6);
  Suma_de_4_Entradas suma_de_4_entradas_4 (
    .E1(suma_de_4_entradas_3_acarreo_1), .E2(\multiplicación_de_15_1_1_resultado_9 ),
    .E3(\multiplicación_de_15_1_2_resultado_10 ), .E4(\multiplicación_de_15_1_3_resultado_11 ),
    .out_5(suma_de_4_entradas_4_out_5), .ACARREO_1(suma_de_4_entradas_4_acarreo_1),
    .ACARREO_2(suma_de_4_entradas_4_acarreo_2));
  and and_7 (out_18, and_1_out, suma_de_4_entradas_3_out_5);
  and and_8 (out_17, and_1_out, suma_de_4_entradas_4_out_5);
  Suma_de_4_Entradas suma_de_4_entradas_5 (
    .E1(suma_de_4_entradas_4_acarreo_1), .E2(\multiplicación_de_15_1_1_resultado_8 ),
    .E3(\multiplicación_de_15_1_2_resultado_9 ), .E4(\multiplicación_de_15_1_3_resultado_10 ),
    .out_5(suma_de_4_entradas_5_out_5), .ACARREO_1(suma_de_4_entradas_5_acarreo_1),
    .ACARREO_2(suma_de_4_entradas_5_acarreo_2));
  and and_9 (out_16, and_1_out, suma_de_4_entradas_5_out_5);
  Suma_de_4_Entradas suma_de_4_entradas_6 (
    .E1(suma_de_4_entradas_5_acarreo_1), .E2(\multiplicación_de_15_1_1_resultado_7 ),
    .E3(\multiplicación_de_15_1_2_resultado_8 ), .E4(\multiplicación_de_15_1_3_resultado_9 ),
    .out_5(suma_de_4_entradas_6_out_5), .ACARREO_1(suma_de_4_entradas_6_acarreo_1),
    .ACARREO_2(suma_de_4_entradas_6_acarreo_2));
  and and_10 (out_15, and_1_out, suma_de_4_entradas_6_out_5);
  Suma_de_4_Entradas suma_de_4_entradas_7 (
    .E1(suma_de_4_entradas_6_acarreo_1), .E2(\multiplicación_de_15_1_1_resultado_6 ),
    .E3(\multiplicación_de_15_1_2_resultado_7 ), .E4(\multiplicación_de_15_1_3_resultado_8 ),
    .out_5(suma_de_4_entradas_7_out_5), .ACARREO_1(suma_de_4_entradas_7_acarreo_1),
    .ACARREO_2(suma_de_4_entradas_7_acarreo_2));
  and and_11 (out_14, and_1_out, suma_de_4_entradas_7_out_5);
  Suma_de_4_Entradas suma_de_4_entradas_8 (
    .E1(suma_de_4_entradas_7_acarreo_1), .E2(\multiplicación_de_15_1_1_resultado_5 ),
    .E3(\multiplicación_de_15_1_2_resultado_6 ), .E4(\multiplicación_de_15_1_3_resultado_7 ),
    .out_5(suma_de_4_entradas_8_out_5), .ACARREO_1(suma_de_4_entradas_8_acarreo_1),
    .ACARREO_2(suma_de_4_entradas_8_acarreo_2));
  and and_12 (out_13, and_1_out, suma_de_4_entradas_8_out_5);
  Suma_de_4_Entradas suma_de_4_entradas_9 (
    .E1(suma_de_4_entradas_8_acarreo_1), .E2(\multiplicación_de_15_1_1_resultado_4 ),
    .E3(\multiplicación_de_15_1_2_resultado_5 ), .E4(\multiplicación_de_15_1_3_resultado_6 ),
    .out_5(suma_de_4_entradas_9_out_5), .ACARREO_1(suma_de_4_entradas_9_acarreo_1),
    .ACARREO_2(suma_de_4_entradas_9_acarreo_2));
  Suma_de_4_Entradas suma_de_4_entradas_10 (
    .E1(suma_de_4_entradas_9_acarreo_1), .E2(\multiplicación_de_15_1_1_resultado_3 ),
    .E3(\multiplicación_de_15_1_2_resultado_4 ), .E4(\multiplicación_de_15_1_3_resultado_5 ),
    .out_5(suma_de_4_entradas_10_out_5), .ACARREO_1(suma_de_4_entradas_10_acarreo_1),
    .ACARREO_2(suma_de_4_entradas_10_acarreo_2));
  and and_13 (out_12, and_1_out, suma_de_4_entradas_9_out_5);
  Suma_de_4_Entradas suma_de_4_entradas_11 (
    .E1(suma_de_4_entradas_10_acarreo_1), .E2(\multiplicación_de_15_1_1_resultado_2 ),
    .E3(\multiplicación_de_15_1_2_resultado_3 ), .E4(\multiplicación_de_15_1_3_resultado_4 ),
    .out_5(suma_de_4_entradas_11_out_5), .ACARREO_1(suma_de_4_entradas_11_acarreo_1),
    .ACARREO_2(suma_de_4_entradas_11_acarreo_2));
  and and_14 (out_11, and_1_out, suma_de_4_entradas_10_out_5);
  and and_15 (out_10, and_1_out, suma_de_4_entradas_11_out_5);
  Suma_de_4_Entradas suma_de_4_entradas_12 (
    .E1(suma_de_4_entradas_11_acarreo_1), .E2(\multiplicación_de_15_1_1_resultado_1 ),
    .E3(\multiplicación_de_15_1_2_resultado_2 ), .E4(\multiplicación_de_15_1_3_resultado_3 ),
    .out_5(suma_de_4_entradas_12_out_5), .ACARREO_1(suma_de_4_entradas_12_acarreo_1),
    .ACARREO_2(suma_de_4_entradas_12_acarreo_2));
  and and_16 (out_9, and_1_out, suma_de_4_entradas_12_out_5);
  Suma_de_3_Entradas suma_de_3_entradas_1 (
    .E1(suma_de_4_entradas_12_acarreo_1), .E2(\multiplicación_de_15_1_2_resultado_1 ),
    .E3(\multiplicación_de_15_1_3_resultado_2 ), .out_4(suma_de_3_entradas_1_out_4),
    .ACARREO_1(suma_de_3_entradas_1_acarreo_1));
  and and_17 (out_8, and_1_out, suma_de_3_entradas_1_out_4);
  Suma_de_2_Entradas suma_de_2_entradas_2 (
    .E1(suma_de_3_entradas_1_acarreo_1), .E2(\multiplicación_de_15_1_3_resultado_1 ),
    .ACARREO_1(suma_de_2_entradas_2_acarreo_1), .out_3(suma_de_2_entradas_2_out_3));
  and and_18 (out_7, and_1_out, suma_de_2_entradas_2_out_3);
  // also tied to GND on the sheet: {suma_de_4_entradas_2_acarreo_2, suma_de_5_entradas_1_acarreo_2, suma_de_4_entradas_3_acarreo_2, suma_de_4_entradas_4_acarreo_2, suma_de_4_entradas_5_acarreo_2, suma_de_4_entradas_6_acarreo_2, suma_de_4_entradas_7_acarreo_2, suma_de_4_entradas_8_acarreo_2, suma_de_4_entradas_9_acarreo_2, suma_de_4_entradas_10_acarreo_2, suma_de_4_entradas_11_acarreo_2, suma_de_4_entradas_12_acarreo_2, suma_de_2_entradas_2_acarreo_1}

  // Notes on the sheet:
  //   EXPONENTE
  //   B1
endmodule

module Potencia__P___P___P___P___P___P___P (
  input  E1,
  input  E2,
  input  E3,
  output out_4,
  output out_5,
  output out_6,
  output out_7,
  output out_8,
  output out_9,
  output out_10,
  output out_11,
  output out_12,
  output out_13,
  output out_14,
  output out_15,
  output out_16,
  output out_17,
  output out_18,
  output out_19,
  output out_20,
  output out_21,
  output out_22,
  output out_23
);

  wire \multiplicación_de_17_1_1_resultado_1 , \multiplicación_de_17_1_1_resultado_2 ,
       \multiplicación_de_17_1_1_resultado_3 , \multiplicación_de_17_1_1_resultado_4 ,
       \multiplicación_de_17_1_1_resultado_5 , \multiplicación_de_17_1_1_resultado_6 ,
       \multiplicación_de_17_1_1_resultado_7 , \multiplicación_de_17_1_1_resultado_8 ,
       \multiplicación_de_17_1_1_resultado_9 , \multiplicación_de_17_1_1_resultado_10 ,
       \multiplicación_de_17_1_1_resultado_11 , \multiplicación_de_17_1_1_resultado_12 ,
       \multiplicación_de_17_1_1_resultado_13 , \multiplicación_de_17_1_1_resultado_14 ,
       \multiplicación_de_17_1_1_resultado_15 , \multiplicación_de_17_1_1_resultado_16 ,
       \multiplicación_de_17_1_2_resultado_1 , \multiplicación_de_17_1_2_resultado_2 ,
       \multiplicación_de_17_1_2_resultado_3 , \multiplicación_de_17_1_2_resultado_4 ,
       \multiplicación_de_17_1_2_resultado_5 , \multiplicación_de_17_1_2_resultado_6 ,
       \multiplicación_de_17_1_2_resultado_7 , \multiplicación_de_17_1_2_resultado_8 ,
       \multiplicación_de_17_1_2_resultado_9 , \multiplicación_de_17_1_2_resultado_10 ,
       \multiplicación_de_17_1_2_resultado_11 , \multiplicación_de_17_1_2_resultado_12 ,
       \multiplicación_de_17_1_2_resultado_13 , \multiplicación_de_17_1_2_resultado_14 ,
       \multiplicación_de_17_1_2_resultado_15 , \multiplicación_de_17_1_2_resultado_16 ,
       \multiplicación_de_17_1_2_resultado_17 , \multiplicación_de_17_1_3_resultado_1 ,
       \multiplicación_de_17_1_3_resultado_2 , \multiplicación_de_17_1_3_resultado_3 ,
       \multiplicación_de_17_1_3_resultado_4 , \multiplicación_de_17_1_3_resultado_5 ,
       \multiplicación_de_17_1_3_resultado_6 , \multiplicación_de_17_1_3_resultado_7 ,
       \multiplicación_de_17_1_3_resultado_8 , \multiplicación_de_17_1_3_resultado_9 ,
       \multiplicación_de_17_1_3_resultado_10 , \multiplicación_de_17_1_3_resultado_11 ,
       \multiplicación_de_17_1_3_resultado_12 , \multiplicación_de_17_1_3_resultado_13 ,
       \multiplicación_de_17_1_3_resultado_14 , \multiplicación_de_17_1_3_resultado_15 ,
       \multiplicación_de_17_1_3_resultado_16 , \multiplicación_de_17_1_3_resultado_17 ,
       potencia_p_p_p_p_p_p_1_out_4, potencia_p_p_p_p_p_p_1_out_5, potencia_p_p_p_p_p_p_1_out_6,
       potencia_p_p_p_p_p_p_1_out_7, potencia_p_p_p_p_p_p_1_out_8, potencia_p_p_p_p_p_p_1_out_9,
       potencia_p_p_p_p_p_p_1_out_10, potencia_p_p_p_p_p_p_1_out_11, potencia_p_p_p_p_p_p_1_out_12,
       potencia_p_p_p_p_p_p_1_out_13, potencia_p_p_p_p_p_p_1_out_14, potencia_p_p_p_p_p_p_1_out_15,
       potencia_p_p_p_p_p_p_1_out_16, potencia_p_p_p_p_p_p_1_out_17, potencia_p_p_p_p_p_p_1_out_18,
       potencia_p_p_p_p_p_p_1_out_19, potencia_p_p_p_p_p_p_1_out_20, suma_de_2_entradas_1_acarreo_1,
       suma_de_3_entradas_1_acarreo_1, suma_de_4_entradas_1_acarreo_1, suma_de_4_entradas_1_acarreo_2,
       suma_de_4_entradas_2_acarreo_1, suma_de_4_entradas_2_acarreo_2, suma_de_4_entradas_3_acarreo_1,
       suma_de_4_entradas_3_acarreo_2, suma_de_4_entradas_4_acarreo_1, suma_de_4_entradas_4_acarreo_2,
       suma_de_4_entradas_5_acarreo_1, suma_de_4_entradas_5_acarreo_2, suma_de_4_entradas_6_acarreo_1,
       suma_de_4_entradas_6_acarreo_2, suma_de_4_entradas_7_acarreo_1, suma_de_4_entradas_7_acarreo_2,
       suma_de_4_entradas_8_acarreo_1, suma_de_4_entradas_8_acarreo_2, suma_de_4_entradas_9_acarreo_1,
       suma_de_4_entradas_9_acarreo_2, suma_de_4_entradas_10_acarreo_1, suma_de_4_entradas_10_acarreo_2,
       suma_de_4_entradas_11_acarreo_1, suma_de_4_entradas_11_acarreo_2, suma_de_4_entradas_12_acarreo_1,
       suma_de_4_entradas_12_acarreo_2, suma_de_4_entradas_13_acarreo_1, suma_de_4_entradas_13_acarreo_2,
       suma_de_5_entradas_1_acarreo_1, suma_de_5_entradas_1_acarreo_2, suma_de_5_entradas_2_acarreo_1,
       suma_de_5_entradas_2_acarreo_2;

  Potencia__P___P___P___P___P___P potencia_p_p_p_p_p_p_1 (
    .E1(E1), .E2(E2), .E3(E3), .out_4(potencia_p_p_p_p_p_p_1_out_4), .out_5(potencia_p_p_p_p_p_p_1_out_5),
    .out_6(potencia_p_p_p_p_p_p_1_out_6), .out_7(potencia_p_p_p_p_p_p_1_out_7),
    .out_8(potencia_p_p_p_p_p_p_1_out_8), .out_9(potencia_p_p_p_p_p_p_1_out_9),
    .out_10(potencia_p_p_p_p_p_p_1_out_10), .out_11(potencia_p_p_p_p_p_p_1_out_11),
    .out_12(potencia_p_p_p_p_p_p_1_out_12), .out_13(potencia_p_p_p_p_p_p_1_out_13),
    .out_14(potencia_p_p_p_p_p_p_1_out_14), .out_15(potencia_p_p_p_p_p_p_1_out_15),
    .out_16(potencia_p_p_p_p_p_p_1_out_16), .out_17(potencia_p_p_p_p_p_p_1_out_17),
    .out_18(potencia_p_p_p_p_p_p_1_out_18), .out_19(potencia_p_p_p_p_p_p_1_out_19),
    .out_20(potencia_p_p_p_p_p_p_1_out_20));
  \Multiplicación_de_17___1  \multiplicación_de_17_1_1  (
    .ENTRADAS(potencia_p_p_p_p_p_p_1_out_20), .in_2(potencia_p_p_p_p_p_p_1_out_19),
    .MULTIPLICANDO_3(potencia_p_p_p_p_p_p_1_out_18), .MULTIPLICANDO_4(potencia_p_p_p_p_p_p_1_out_17),
    .MULTIPLICANDO_5(potencia_p_p_p_p_p_p_1_out_16), .in_6(potencia_p_p_p_p_p_p_1_out_15),
    .MULTIPLICANDO_7(potencia_p_p_p_p_p_p_1_out_14), .MULTIPLICANDO_8(potencia_p_p_p_p_p_p_1_out_13),
    .in_9(potencia_p_p_p_p_p_p_1_out_12), .MULTIPLICANDO_10(potencia_p_p_p_p_p_p_1_out_11),
    .MULTIPLICANDO_11(potencia_p_p_p_p_p_p_1_out_10), .in_12(potencia_p_p_p_p_p_p_1_out_9),
    .in_13(potencia_p_p_p_p_p_p_1_out_8), .in_14(potencia_p_p_p_p_p_p_1_out_7),
    .in_15(potencia_p_p_p_p_p_p_1_out_6), .in_16(potencia_p_p_p_p_p_p_1_out_4),
    .in_17(potencia_p_p_p_p_p_p_1_out_5), .MULTIPLICADOR(E3),
    .RESULTADO_1(\multiplicación_de_17_1_1_resultado_1 ),
    .RESULTADO_2(\multiplicación_de_17_1_1_resultado_2 ),
    .RESULTADO_3(\multiplicación_de_17_1_1_resultado_3 ),
    .RESULTADO_4(\multiplicación_de_17_1_1_resultado_4 ),
    .RESULTADO_5(\multiplicación_de_17_1_1_resultado_5 ),
    .RESULTADO_6(\multiplicación_de_17_1_1_resultado_6 ),
    .RESULTADO_7(\multiplicación_de_17_1_1_resultado_7 ),
    .RESULTADO_8(\multiplicación_de_17_1_1_resultado_8 ),
    .RESULTADO_9(\multiplicación_de_17_1_1_resultado_9 ),
    .RESULTADO_10(\multiplicación_de_17_1_1_resultado_10 ),
    .RESULTADO_11(\multiplicación_de_17_1_1_resultado_11 ),
    .RESULTADO_12(\multiplicación_de_17_1_1_resultado_12 ),
    .RESULTADO_13(\multiplicación_de_17_1_1_resultado_13 ),
    .RESULTADO_14(\multiplicación_de_17_1_1_resultado_14 ),
    .RESULTADO_15(\multiplicación_de_17_1_1_resultado_15 ),
    .RESULTADO_16(\multiplicación_de_17_1_1_resultado_16 ), .RESULTADO_17(out_5));
  \Multiplicación_de_17___1  \multiplicación_de_17_1_2  (
    .ENTRADAS(potencia_p_p_p_p_p_p_1_out_20), .in_2(potencia_p_p_p_p_p_p_1_out_19),
    .MULTIPLICANDO_3(potencia_p_p_p_p_p_p_1_out_18), .MULTIPLICANDO_4(potencia_p_p_p_p_p_p_1_out_17),
    .MULTIPLICANDO_5(potencia_p_p_p_p_p_p_1_out_16), .in_6(potencia_p_p_p_p_p_p_1_out_15),
    .MULTIPLICANDO_7(potencia_p_p_p_p_p_p_1_out_14), .MULTIPLICANDO_8(potencia_p_p_p_p_p_p_1_out_13),
    .in_9(potencia_p_p_p_p_p_p_1_out_12), .MULTIPLICANDO_10(potencia_p_p_p_p_p_p_1_out_11),
    .MULTIPLICANDO_11(potencia_p_p_p_p_p_p_1_out_10), .in_12(potencia_p_p_p_p_p_p_1_out_9),
    .in_13(potencia_p_p_p_p_p_p_1_out_8), .in_14(potencia_p_p_p_p_p_p_1_out_7),
    .in_15(potencia_p_p_p_p_p_p_1_out_6), .in_16(potencia_p_p_p_p_p_p_1_out_4),
    .in_17(potencia_p_p_p_p_p_p_1_out_5), .MULTIPLICADOR(E2),
    .RESULTADO_1(\multiplicación_de_17_1_2_resultado_1 ),
    .RESULTADO_2(\multiplicación_de_17_1_2_resultado_2 ),
    .RESULTADO_3(\multiplicación_de_17_1_2_resultado_3 ),
    .RESULTADO_4(\multiplicación_de_17_1_2_resultado_4 ),
    .RESULTADO_5(\multiplicación_de_17_1_2_resultado_5 ),
    .RESULTADO_6(\multiplicación_de_17_1_2_resultado_6 ),
    .RESULTADO_7(\multiplicación_de_17_1_2_resultado_7 ),
    .RESULTADO_8(\multiplicación_de_17_1_2_resultado_8 ),
    .RESULTADO_9(\multiplicación_de_17_1_2_resultado_9 ),
    .RESULTADO_10(\multiplicación_de_17_1_2_resultado_10 ),
    .RESULTADO_11(\multiplicación_de_17_1_2_resultado_11 ),
    .RESULTADO_12(\multiplicación_de_17_1_2_resultado_12 ),
    .RESULTADO_13(\multiplicación_de_17_1_2_resultado_13 ),
    .RESULTADO_14(\multiplicación_de_17_1_2_resultado_14 ),
    .RESULTADO_15(\multiplicación_de_17_1_2_resultado_15 ),
    .RESULTADO_16(\multiplicación_de_17_1_2_resultado_16 ),
    .RESULTADO_17(\multiplicación_de_17_1_2_resultado_17 ));
  \Multiplicación_de_17___1  \multiplicación_de_17_1_3  (
    .ENTRADAS(potencia_p_p_p_p_p_p_1_out_20), .in_2(potencia_p_p_p_p_p_p_1_out_19),
    .MULTIPLICANDO_3(potencia_p_p_p_p_p_p_1_out_18), .MULTIPLICANDO_4(potencia_p_p_p_p_p_p_1_out_17),
    .MULTIPLICANDO_5(potencia_p_p_p_p_p_p_1_out_16), .in_6(potencia_p_p_p_p_p_p_1_out_15),
    .MULTIPLICANDO_7(potencia_p_p_p_p_p_p_1_out_14), .MULTIPLICANDO_8(potencia_p_p_p_p_p_p_1_out_13),
    .in_9(potencia_p_p_p_p_p_p_1_out_12), .MULTIPLICANDO_10(potencia_p_p_p_p_p_p_1_out_11),
    .MULTIPLICANDO_11(potencia_p_p_p_p_p_p_1_out_10), .in_12(potencia_p_p_p_p_p_p_1_out_9),
    .in_13(potencia_p_p_p_p_p_p_1_out_8), .in_14(potencia_p_p_p_p_p_p_1_out_7),
    .in_15(potencia_p_p_p_p_p_p_1_out_6), .in_16(potencia_p_p_p_p_p_p_1_out_4),
    .in_17(potencia_p_p_p_p_p_p_1_out_5), .MULTIPLICADOR(E1),
    .RESULTADO_1(\multiplicación_de_17_1_3_resultado_1 ),
    .RESULTADO_2(\multiplicación_de_17_1_3_resultado_2 ),
    .RESULTADO_3(\multiplicación_de_17_1_3_resultado_3 ),
    .RESULTADO_4(\multiplicación_de_17_1_3_resultado_4 ),
    .RESULTADO_5(\multiplicación_de_17_1_3_resultado_5 ),
    .RESULTADO_6(\multiplicación_de_17_1_3_resultado_6 ),
    .RESULTADO_7(\multiplicación_de_17_1_3_resultado_7 ),
    .RESULTADO_8(\multiplicación_de_17_1_3_resultado_8 ),
    .RESULTADO_9(\multiplicación_de_17_1_3_resultado_9 ),
    .RESULTADO_10(\multiplicación_de_17_1_3_resultado_10 ),
    .RESULTADO_11(\multiplicación_de_17_1_3_resultado_11 ),
    .RESULTADO_12(\multiplicación_de_17_1_3_resultado_12 ),
    .RESULTADO_13(\multiplicación_de_17_1_3_resultado_13 ),
    .RESULTADO_14(\multiplicación_de_17_1_3_resultado_14 ),
    .RESULTADO_15(\multiplicación_de_17_1_3_resultado_15 ),
    .RESULTADO_16(\multiplicación_de_17_1_3_resultado_16 ),
    .RESULTADO_17(\multiplicación_de_17_1_3_resultado_17 ));
  Suma_de_2_Entradas suma_de_2_entradas_1 (
    .E1(\multiplicación_de_17_1_1_resultado_16 ), .E2(\multiplicación_de_17_1_2_resultado_17 ),
    .ACARREO_1(suma_de_2_entradas_1_acarreo_1), .out_3(out_4));
  Suma_de_4_Entradas suma_de_4_entradas_1 (
    .E1(suma_de_2_entradas_1_acarreo_1), .E2(\multiplicación_de_17_1_1_resultado_15 ),
    .E3(\multiplicación_de_17_1_2_resultado_16 ), .E4(\multiplicación_de_17_1_3_resultado_17 ),
    .out_5(out_6), .ACARREO_1(suma_de_4_entradas_1_acarreo_1), .ACARREO_2(suma_de_4_entradas_1_acarreo_2));
  Suma_de_4_Entradas suma_de_4_entradas_2 (
    .E1(suma_de_4_entradas_1_acarreo_1), .E2(\multiplicación_de_17_1_1_resultado_14 ),
    .E3(\multiplicación_de_17_1_2_resultado_15 ), .E4(\multiplicación_de_17_1_3_resultado_16 ),
    .out_5(out_7), .ACARREO_1(suma_de_4_entradas_2_acarreo_1), .ACARREO_2(suma_de_4_entradas_2_acarreo_2));
  Suma_de_4_Entradas suma_de_4_entradas_3 (
    .E1(suma_de_4_entradas_2_acarreo_1), .E2(\multiplicación_de_17_1_1_resultado_13 ),
    .E3(\multiplicación_de_17_1_2_resultado_14 ), .E4(\multiplicación_de_17_1_3_resultado_15 ),
    .out_5(out_8), .ACARREO_1(suma_de_4_entradas_3_acarreo_1), .ACARREO_2(suma_de_4_entradas_3_acarreo_2));
  Suma_de_4_Entradas suma_de_4_entradas_4 (
    .E1(suma_de_4_entradas_3_acarreo_1), .E2(\multiplicación_de_17_1_1_resultado_12 ),
    .E3(\multiplicación_de_17_1_2_resultado_13 ), .E4(\multiplicación_de_17_1_3_resultado_14 ),
    .out_5(out_9), .ACARREO_1(suma_de_4_entradas_4_acarreo_1), .ACARREO_2(suma_de_4_entradas_4_acarreo_2));
  Suma_de_4_Entradas suma_de_4_entradas_5 (
    .E1(suma_de_4_entradas_4_acarreo_1), .E2(\multiplicación_de_17_1_1_resultado_11 ),
    .E3(\multiplicación_de_17_1_2_resultado_12 ), .E4(\multiplicación_de_17_1_3_resultado_13 ),
    .out_5(out_10), .ACARREO_1(suma_de_4_entradas_5_acarreo_1), .ACARREO_2(suma_de_4_entradas_5_acarreo_2));
  Suma_de_4_Entradas suma_de_4_entradas_6 (
    .E1(suma_de_4_entradas_5_acarreo_1), .E2(\multiplicación_de_17_1_1_resultado_10 ),
    .E3(\multiplicación_de_17_1_2_resultado_11 ), .E4(\multiplicación_de_17_1_3_resultado_12 ),
    .out_5(out_11), .ACARREO_1(suma_de_4_entradas_6_acarreo_1), .ACARREO_2(suma_de_4_entradas_6_acarreo_2));
  Suma_de_4_Entradas suma_de_4_entradas_7 (
    .E1(suma_de_4_entradas_6_acarreo_1), .E2(\multiplicación_de_17_1_1_resultado_9 ),
    .E3(\multiplicación_de_17_1_2_resultado_10 ), .E4(\multiplicación_de_17_1_3_resultado_11 ),
    .out_5(out_12), .ACARREO_1(suma_de_4_entradas_7_acarreo_1), .ACARREO_2(suma_de_4_entradas_7_acarreo_2));
  Suma_de_4_Entradas suma_de_4_entradas_8 (
    .E1(suma_de_4_entradas_7_acarreo_1), .E2(\multiplicación_de_17_1_1_resultado_8 ),
    .E3(\multiplicación_de_17_1_2_resultado_9 ), .E4(\multiplicación_de_17_1_3_resultado_10 ),
    .out_5(out_13), .ACARREO_1(suma_de_4_entradas_8_acarreo_1), .ACARREO_2(suma_de_4_entradas_8_acarreo_2));
  Suma_de_4_Entradas suma_de_4_entradas_9 (
    .E1(suma_de_4_entradas_8_acarreo_1), .E2(\multiplicación_de_17_1_1_resultado_7 ),
    .E3(\multiplicación_de_17_1_2_resultado_8 ), .E4(\multiplicación_de_17_1_3_resultado_9 ), .out_5(out_14),
    .ACARREO_1(suma_de_4_entradas_9_acarreo_1), .ACARREO_2(suma_de_4_entradas_9_acarreo_2));
  Suma_de_5_Entradas suma_de_5_entradas_1 (
    .E1(suma_de_4_entradas_9_acarreo_1), .E2(suma_de_4_entradas_8_acarreo_2),
    .E3(\multiplicación_de_17_1_1_resultado_6 ), .E4(\multiplicación_de_17_1_2_resultado_7 ),
    .E5(\multiplicación_de_17_1_3_resultado_8 ), .out_6(out_15), .ACARREO_1(suma_de_5_entradas_1_acarreo_1),
    .ACARREO_2(suma_de_5_entradas_1_acarreo_2));
  Suma_de_4_Entradas suma_de_4_entradas_10 (
    .E1(suma_de_5_entradas_1_acarreo_1), .E2(\multiplicación_de_17_1_1_resultado_5 ),
    .E3(\multiplicación_de_17_1_2_resultado_6 ), .E4(\multiplicación_de_17_1_3_resultado_7 ), .out_5(out_16),
    .ACARREO_1(suma_de_4_entradas_10_acarreo_1), .ACARREO_2(suma_de_4_entradas_10_acarreo_2));
  Suma_de_5_Entradas suma_de_5_entradas_2 (
    .E1(suma_de_4_entradas_10_acarreo_1), .E2(suma_de_5_entradas_1_acarreo_2),
    .E3(\multiplicación_de_17_1_1_resultado_4 ), .E4(\multiplicación_de_17_1_2_resultado_5 ),
    .E5(\multiplicación_de_17_1_3_resultado_6 ), .out_6(out_17), .ACARREO_1(suma_de_5_entradas_2_acarreo_1),
    .ACARREO_2(suma_de_5_entradas_2_acarreo_2));
  Suma_de_4_Entradas suma_de_4_entradas_11 (
    .E1(suma_de_5_entradas_2_acarreo_1), .E2(\multiplicación_de_17_1_1_resultado_3 ),
    .E3(\multiplicación_de_17_1_2_resultado_4 ), .E4(\multiplicación_de_17_1_3_resultado_5 ), .out_5(out_18),
    .ACARREO_1(suma_de_4_entradas_11_acarreo_1), .ACARREO_2(suma_de_4_entradas_11_acarreo_2));
  Suma_de_4_Entradas suma_de_4_entradas_12 (
    .E1(suma_de_4_entradas_11_acarreo_1), .E2(\multiplicación_de_17_1_1_resultado_2 ),
    .E3(\multiplicación_de_17_1_2_resultado_3 ), .E4(\multiplicación_de_17_1_3_resultado_4 ), .out_5(out_19),
    .ACARREO_1(suma_de_4_entradas_12_acarreo_1), .ACARREO_2(suma_de_4_entradas_12_acarreo_2));
  Suma_de_4_Entradas suma_de_4_entradas_13 (
    .E1(suma_de_4_entradas_12_acarreo_1), .E2(\multiplicación_de_17_1_1_resultado_1 ),
    .E3(\multiplicación_de_17_1_2_resultado_2 ), .E4(\multiplicación_de_17_1_3_resultado_3 ), .out_5(out_20),
    .ACARREO_1(suma_de_4_entradas_13_acarreo_1), .ACARREO_2(suma_de_4_entradas_13_acarreo_2));
  Suma_de_3_Entradas suma_de_3_entradas_1 (
    .E1(suma_de_4_entradas_13_acarreo_1), .E2(\multiplicación_de_17_1_2_resultado_1 ),
    .E3(\multiplicación_de_17_1_3_resultado_2 ), .out_4(out_21), .ACARREO_1(suma_de_3_entradas_1_acarreo_1));
  Suma_de_3_Entradas suma_de_3_entradas_2 (
    .E1(suma_de_3_entradas_1_acarreo_1), .E2(suma_de_4_entradas_13_acarreo_2),
    .E3(\multiplicación_de_17_1_3_resultado_1 ), .out_4(out_22), .ACARREO_1(out_23));
  // also tied to GND on the sheet: {suma_de_4_entradas_1_acarreo_2, suma_de_4_entradas_2_acarreo_2, suma_de_4_entradas_3_acarreo_2, suma_de_4_entradas_4_acarreo_2, suma_de_4_entradas_5_acarreo_2, suma_de_4_entradas_6_acarreo_2, suma_de_4_entradas_7_acarreo_2, suma_de_4_entradas_9_acarreo_2, suma_de_4_entradas_10_acarreo_2, suma_de_5_entradas_2_acarreo_2, suma_de_4_entradas_11_acarreo_2, suma_de_4_entradas_12_acarreo_2}

  // Notes on the sheet:
  //   ENTRADAS
endmodule

module \Elección_Potencia_p___7  (
  input  E1,
  input  E2,
  input  E3,
  input  B1,
  input  B2,
  input  B3,
  output out_7,
  output out_8,
  output out_9,
  output out_10,
  output out_11,
  output out_12,
  output out_13,
  output out_14,
  output out_15,
  output out_16,
  output out_17,
  output out_18,
  output out_19,
  output out_20,
  output out_21,
  output out_22,
  output out_23,
  output out_24,
  output out_25,
  output out_26
);

  wire and_1_out, \multiplicación_de_17_1_1_resultado_1 , \multiplicación_de_17_1_1_resultado_2 ,
       \multiplicación_de_17_1_1_resultado_3 , \multiplicación_de_17_1_1_resultado_4 ,
       \multiplicación_de_17_1_1_resultado_5 , \multiplicación_de_17_1_1_resultado_6 ,
       \multiplicación_de_17_1_1_resultado_7 , \multiplicación_de_17_1_1_resultado_8 ,
       \multiplicación_de_17_1_1_resultado_9 , \multiplicación_de_17_1_1_resultado_10 ,
       \multiplicación_de_17_1_1_resultado_11 , \multiplicación_de_17_1_1_resultado_12 ,
       \multiplicación_de_17_1_1_resultado_13 , \multiplicación_de_17_1_1_resultado_14 ,
       \multiplicación_de_17_1_1_resultado_15 , \multiplicación_de_17_1_1_resultado_16 ,
       \multiplicación_de_17_1_1_resultado_17 , \multiplicación_de_17_1_2_resultado_1 ,
       \multiplicación_de_17_1_2_resultado_2 , \multiplicación_de_17_1_2_resultado_3 ,
       \multiplicación_de_17_1_2_resultado_4 , \multiplicación_de_17_1_2_resultado_5 ,
       \multiplicación_de_17_1_2_resultado_6 , \multiplicación_de_17_1_2_resultado_7 ,
       \multiplicación_de_17_1_2_resultado_8 , \multiplicación_de_17_1_2_resultado_9 ,
       \multiplicación_de_17_1_2_resultado_10 , \multiplicación_de_17_1_2_resultado_11 ,
       \multiplicación_de_17_1_2_resultado_12 , \multiplicación_de_17_1_2_resultado_13 ,
       \multiplicación_de_17_1_2_resultado_14 , \multiplicación_de_17_1_2_resultado_15 ,
       \multiplicación_de_17_1_2_resultado_16 , \multiplicación_de_17_1_2_resultado_17 ,
       \multiplicación_de_17_1_3_resultado_1 , \multiplicación_de_17_1_3_resultado_2 ,
       \multiplicación_de_17_1_3_resultado_3 , \multiplicación_de_17_1_3_resultado_4 ,
       \multiplicación_de_17_1_3_resultado_5 , \multiplicación_de_17_1_3_resultado_6 ,
       \multiplicación_de_17_1_3_resultado_7 , \multiplicación_de_17_1_3_resultado_8 ,
       \multiplicación_de_17_1_3_resultado_9 , \multiplicación_de_17_1_3_resultado_10 ,
       \multiplicación_de_17_1_3_resultado_11 , \multiplicación_de_17_1_3_resultado_12 ,
       \multiplicación_de_17_1_3_resultado_13 , \multiplicación_de_17_1_3_resultado_14 ,
       \multiplicación_de_17_1_3_resultado_15 , \multiplicación_de_17_1_3_resultado_16 ,
       \multiplicación_de_17_1_3_resultado_17 , potencia_p_p_p_p_p_p_1_out_4, potencia_p_p_p_p_p_p_1_out_5,
       potencia_p_p_p_p_p_p_1_out_6, potencia_p_p_p_p_p_p_1_out_7, potencia_p_p_p_p_p_p_1_out_8,
       potencia_p_p_p_p_p_p_1_out_9, potencia_p_p_p_p_p_p_1_out_10, potencia_p_p_p_p_p_p_1_out_11,
       potencia_p_p_p_p_p_p_1_out_12, potencia_p_p_p_p_p_p_1_out_13, potencia_p_p_p_p_p_p_1_out_14,
       potencia_p_p_p_p_p_p_1_out_15, potencia_p_p_p_p_p_p_1_out_16, potencia_p_p_p_p_p_p_1_out_17,
       potencia_p_p_p_p_p_p_1_out_18, potencia_p_p_p_p_p_p_1_out_19, potencia_p_p_p_p_p_p_1_out_20,
       suma_de_2_entradas_1_acarreo_1, suma_de_2_entradas_1_out_3, suma_de_3_entradas_1_acarreo_1,
       suma_de_3_entradas_1_out_4, suma_de_3_entradas_2_acarreo_1, suma_de_3_entradas_2_out_4,
       suma_de_4_entradas_1_acarreo_1, suma_de_4_entradas_1_acarreo_2, suma_de_4_entradas_1_out_5,
       suma_de_4_entradas_2_acarreo_1, suma_de_4_entradas_2_acarreo_2, suma_de_4_entradas_2_out_5,
       suma_de_4_entradas_3_acarreo_1, suma_de_4_entradas_3_acarreo_2, suma_de_4_entradas_3_out_5,
       suma_de_4_entradas_4_acarreo_1, suma_de_4_entradas_4_acarreo_2, suma_de_4_entradas_4_out_5,
       suma_de_4_entradas_5_acarreo_1, suma_de_4_entradas_5_acarreo_2, suma_de_4_entradas_5_out_5,
       suma_de_4_entradas_6_acarreo_1, suma_de_4_entradas_6_acarreo_2, suma_de_4_entradas_6_out_5,
       suma_de_4_entradas_7_acarreo_1, suma_de_4_entradas_7_acarreo_2, suma_de_4_entradas_7_out_5,
       suma_de_4_entradas_8_acarreo_1, suma_de_4_entradas_8_acarreo_2, suma_de_4_entradas_8_out_5,
       suma_de_4_entradas_9_acarreo_1, suma_de_4_entradas_9_acarreo_2, suma_de_4_entradas_9_out_5,
       suma_de_4_entradas_10_acarreo_1, suma_de_4_entradas_10_acarreo_2, suma_de_4_entradas_10_out_5,
       suma_de_4_entradas_11_acarreo_1, suma_de_4_entradas_11_acarreo_2, suma_de_4_entradas_11_out_5,
       suma_de_4_entradas_12_acarreo_1, suma_de_4_entradas_12_acarreo_2, suma_de_4_entradas_12_out_5,
       suma_de_4_entradas_13_acarreo_1, suma_de_4_entradas_13_acarreo_2, suma_de_4_entradas_13_out_5,
       suma_de_5_entradas_1_acarreo_1, suma_de_5_entradas_1_acarreo_2, suma_de_5_entradas_1_out_6,
       suma_de_5_entradas_2_acarreo_1, suma_de_5_entradas_2_acarreo_2, suma_de_5_entradas_2_out_6;

  Potencia__P___P___P___P___P___P potencia_p_p_p_p_p_p_1 (
    .E1(B1), .E2(B2), .E3(B3), .out_4(potencia_p_p_p_p_p_p_1_out_4), .out_5(potencia_p_p_p_p_p_p_1_out_5),
    .out_6(potencia_p_p_p_p_p_p_1_out_6), .out_7(potencia_p_p_p_p_p_p_1_out_7),
    .out_8(potencia_p_p_p_p_p_p_1_out_8), .out_9(potencia_p_p_p_p_p_p_1_out_9),
    .out_10(potencia_p_p_p_p_p_p_1_out_10), .out_11(potencia_p_p_p_p_p_p_1_out_11),
    .out_12(potencia_p_p_p_p_p_p_1_out_12), .out_13(potencia_p_p_p_p_p_p_1_out_13),
    .out_14(potencia_p_p_p_p_p_p_1_out_14), .out_15(potencia_p_p_p_p_p_p_1_out_15),
    .out_16(potencia_p_p_p_p_p_p_1_out_16), .out_17(potencia_p_p_p_p_p_p_1_out_17),
    .out_18(potencia_p_p_p_p_p_p_1_out_18), .out_19(potencia_p_p_p_p_p_p_1_out_19),
    .out_20(potencia_p_p_p_p_p_p_1_out_20));
  and and_1 (and_1_out, E1, E2, E3);
  \Multiplicación_de_17___1  \multiplicación_de_17_1_1  (
    .ENTRADAS(potencia_p_p_p_p_p_p_1_out_20), .in_2(potencia_p_p_p_p_p_p_1_out_19),
    .MULTIPLICANDO_3(potencia_p_p_p_p_p_p_1_out_18), .MULTIPLICANDO_4(potencia_p_p_p_p_p_p_1_out_17),
    .MULTIPLICANDO_5(potencia_p_p_p_p_p_p_1_out_16), .in_6(potencia_p_p_p_p_p_p_1_out_15),
    .MULTIPLICANDO_7(potencia_p_p_p_p_p_p_1_out_14), .MULTIPLICANDO_8(potencia_p_p_p_p_p_p_1_out_13),
    .in_9(potencia_p_p_p_p_p_p_1_out_12), .MULTIPLICANDO_10(potencia_p_p_p_p_p_p_1_out_11),
    .MULTIPLICANDO_11(potencia_p_p_p_p_p_p_1_out_10), .in_12(potencia_p_p_p_p_p_p_1_out_9),
    .in_13(potencia_p_p_p_p_p_p_1_out_8), .in_14(potencia_p_p_p_p_p_p_1_out_7),
    .in_15(potencia_p_p_p_p_p_p_1_out_6), .in_16(potencia_p_p_p_p_p_p_1_out_4),
    .in_17(potencia_p_p_p_p_p_p_1_out_5), .MULTIPLICADOR(B3),
    .RESULTADO_1(\multiplicación_de_17_1_1_resultado_1 ),
    .RESULTADO_2(\multiplicación_de_17_1_1_resultado_2 ),
    .RESULTADO_3(\multiplicación_de_17_1_1_resultado_3 ),
    .RESULTADO_4(\multiplicación_de_17_1_1_resultado_4 ),
    .RESULTADO_5(\multiplicación_de_17_1_1_resultado_5 ),
    .RESULTADO_6(\multiplicación_de_17_1_1_resultado_6 ),
    .RESULTADO_7(\multiplicación_de_17_1_1_resultado_7 ),
    .RESULTADO_8(\multiplicación_de_17_1_1_resultado_8 ),
    .RESULTADO_9(\multiplicación_de_17_1_1_resultado_9 ),
    .RESULTADO_10(\multiplicación_de_17_1_1_resultado_10 ),
    .RESULTADO_11(\multiplicación_de_17_1_1_resultado_11 ),
    .RESULTADO_12(\multiplicación_de_17_1_1_resultado_12 ),
    .RESULTADO_13(\multiplicación_de_17_1_1_resultado_13 ),
    .RESULTADO_14(\multiplicación_de_17_1_1_resultado_14 ),
    .RESULTADO_15(\multiplicación_de_17_1_1_resultado_15 ),
    .RESULTADO_16(\multiplicación_de_17_1_1_resultado_16 ),
    .RESULTADO_17(\multiplicación_de_17_1_1_resultado_17 ));
  \Multiplicación_de_17___1  \multiplicación_de_17_1_2  (
    .ENTRADAS(potencia_p_p_p_p_p_p_1_out_20), .in_2(potencia_p_p_p_p_p_p_1_out_19),
    .MULTIPLICANDO_3(potencia_p_p_p_p_p_p_1_out_18), .MULTIPLICANDO_4(potencia_p_p_p_p_p_p_1_out_17),
    .MULTIPLICANDO_5(potencia_p_p_p_p_p_p_1_out_16), .in_6(potencia_p_p_p_p_p_p_1_out_15),
    .MULTIPLICANDO_7(potencia_p_p_p_p_p_p_1_out_14), .MULTIPLICANDO_8(potencia_p_p_p_p_p_p_1_out_13),
    .in_9(potencia_p_p_p_p_p_p_1_out_12), .MULTIPLICANDO_10(potencia_p_p_p_p_p_p_1_out_11),
    .MULTIPLICANDO_11(potencia_p_p_p_p_p_p_1_out_10), .in_12(potencia_p_p_p_p_p_p_1_out_9),
    .in_13(potencia_p_p_p_p_p_p_1_out_8), .in_14(potencia_p_p_p_p_p_p_1_out_7),
    .in_15(potencia_p_p_p_p_p_p_1_out_6), .in_16(potencia_p_p_p_p_p_p_1_out_4),
    .in_17(potencia_p_p_p_p_p_p_1_out_5), .MULTIPLICADOR(B2),
    .RESULTADO_1(\multiplicación_de_17_1_2_resultado_1 ),
    .RESULTADO_2(\multiplicación_de_17_1_2_resultado_2 ),
    .RESULTADO_3(\multiplicación_de_17_1_2_resultado_3 ),
    .RESULTADO_4(\multiplicación_de_17_1_2_resultado_4 ),
    .RESULTADO_5(\multiplicación_de_17_1_2_resultado_5 ),
    .RESULTADO_6(\multiplicación_de_17_1_2_resultado_6 ),
    .RESULTADO_7(\multiplicación_de_17_1_2_resultado_7 ),
    .RESULTADO_8(\multiplicación_de_17_1_2_resultado_8 ),
    .RESULTADO_9(\multiplicación_de_17_1_2_resultado_9 ),
    .RESULTADO_10(\multiplicación_de_17_1_2_resultado_10 ),
    .RESULTADO_11(\multiplicación_de_17_1_2_resultado_11 ),
    .RESULTADO_12(\multiplicación_de_17_1_2_resultado_12 ),
    .RESULTADO_13(\multiplicación_de_17_1_2_resultado_13 ),
    .RESULTADO_14(\multiplicación_de_17_1_2_resultado_14 ),
    .RESULTADO_15(\multiplicación_de_17_1_2_resultado_15 ),
    .RESULTADO_16(\multiplicación_de_17_1_2_resultado_16 ),
    .RESULTADO_17(\multiplicación_de_17_1_2_resultado_17 ));
  \Multiplicación_de_17___1  \multiplicación_de_17_1_3  (
    .ENTRADAS(potencia_p_p_p_p_p_p_1_out_20), .in_2(potencia_p_p_p_p_p_p_1_out_19),
    .MULTIPLICANDO_3(potencia_p_p_p_p_p_p_1_out_18), .MULTIPLICANDO_4(potencia_p_p_p_p_p_p_1_out_17),
    .MULTIPLICANDO_5(potencia_p_p_p_p_p_p_1_out_16), .in_6(potencia_p_p_p_p_p_p_1_out_15),
    .MULTIPLICANDO_7(potencia_p_p_p_p_p_p_1_out_14), .MULTIPLICANDO_8(potencia_p_p_p_p_p_p_1_out_13),
    .in_9(potencia_p_p_p_p_p_p_1_out_12), .MULTIPLICANDO_10(potencia_p_p_p_p_p_p_1_out_11),
    .MULTIPLICANDO_11(potencia_p_p_p_p_p_p_1_out_10), .in_12(potencia_p_p_p_p_p_p_1_out_9),
    .in_13(potencia_p_p_p_p_p_p_1_out_8), .in_14(potencia_p_p_p_p_p_p_1_out_7),
    .in_15(potencia_p_p_p_p_p_p_1_out_6), .in_16(potencia_p_p_p_p_p_p_1_out_4),
    .in_17(potencia_p_p_p_p_p_p_1_out_5), .MULTIPLICADOR(B1),
    .RESULTADO_1(\multiplicación_de_17_1_3_resultado_1 ),
    .RESULTADO_2(\multiplicación_de_17_1_3_resultado_2 ),
    .RESULTADO_3(\multiplicación_de_17_1_3_resultado_3 ),
    .RESULTADO_4(\multiplicación_de_17_1_3_resultado_4 ),
    .RESULTADO_5(\multiplicación_de_17_1_3_resultado_5 ),
    .RESULTADO_6(\multiplicación_de_17_1_3_resultado_6 ),
    .RESULTADO_7(\multiplicación_de_17_1_3_resultado_7 ),
    .RESULTADO_8(\multiplicación_de_17_1_3_resultado_8 ),
    .RESULTADO_9(\multiplicación_de_17_1_3_resultado_9 ),
    .RESULTADO_10(\multiplicación_de_17_1_3_resultado_10 ),
    .RESULTADO_11(\multiplicación_de_17_1_3_resultado_11 ),
    .RESULTADO_12(\multiplicación_de_17_1_3_resultado_12 ),
    .RESULTADO_13(\multiplicación_de_17_1_3_resultado_13 ),
    .RESULTADO_14(\multiplicación_de_17_1_3_resultado_14 ),
    .RESULTADO_15(\multiplicación_de_17_1_3_resultado_15 ),
    .RESULTADO_16(\multiplicación_de_17_1_3_resultado_16 ),
    .RESULTADO_17(\multiplicación_de_17_1_3_resultado_17 ));
  and and_2 (out_26, and_1_out, \multiplicación_de_17_1_1_resultado_17 );
  Suma_de_2_Entradas suma_de_2_entradas_1 (
    .E1(\multiplicación_de_17_1_1_resultado_16 ), .E2(\multiplicación_de_17_1_2_resultado_17 ),
    .ACARREO_1(suma_de_2_entradas_1_acarreo_1), .out_3(suma_de_2_entradas_1_out_3));
  and and_3 (out_25, and_1_out, suma_de_2_entradas_1_out_3);
  Suma_de_4_Entradas suma_de_4_entradas_1 (
    .E1(suma_de_2_entradas_1_acarreo_1), .E2(\multiplicación_de_17_1_1_resultado_15 ),
    .E3(\multiplicación_de_17_1_2_resultado_16 ), .E4(\multiplicación_de_17_1_3_resultado_17 ),
    .out_5(suma_de_4_entradas_1_out_5), .ACARREO_1(suma_de_4_entradas_1_acarreo_1),
    .ACARREO_2(suma_de_4_entradas_1_acarreo_2));
  and and_4 (out_24, and_1_out, suma_de_4_entradas_1_out_5);
  and and_5 (out_23, and_1_out, suma_de_4_entradas_2_out_5);
  Suma_de_4_Entradas suma_de_4_entradas_2 (
    .E1(suma_de_4_entradas_1_acarreo_1), .E2(\multiplicación_de_17_1_1_resultado_14 ),
    .E3(\multiplicación_de_17_1_2_resultado_15 ), .E4(\multiplicación_de_17_1_3_resultado_16 ),
    .out_5(suma_de_4_entradas_2_out_5), .ACARREO_1(suma_de_4_entradas_2_acarreo_1),
    .ACARREO_2(suma_de_4_entradas_2_acarreo_2));
  Suma_de_4_Entradas suma_de_4_entradas_3 (
    .E1(suma_de_4_entradas_2_acarreo_1), .E2(\multiplicación_de_17_1_1_resultado_13 ),
    .E3(\multiplicación_de_17_1_2_resultado_14 ), .E4(\multiplicación_de_17_1_3_resultado_15 ),
    .out_5(suma_de_4_entradas_3_out_5), .ACARREO_1(suma_de_4_entradas_3_acarreo_1),
    .ACARREO_2(suma_de_4_entradas_3_acarreo_2));
  and and_6 (out_22, and_1_out, suma_de_4_entradas_3_out_5);
  Suma_de_4_Entradas suma_de_4_entradas_4 (
    .E1(suma_de_4_entradas_3_acarreo_1), .E2(\multiplicación_de_17_1_1_resultado_12 ),
    .E3(\multiplicación_de_17_1_2_resultado_13 ), .E4(\multiplicación_de_17_1_3_resultado_14 ),
    .out_5(suma_de_4_entradas_4_out_5), .ACARREO_1(suma_de_4_entradas_4_acarreo_1),
    .ACARREO_2(suma_de_4_entradas_4_acarreo_2));
  and and_7 (out_21, and_1_out, suma_de_4_entradas_4_out_5);
  Suma_de_4_Entradas suma_de_4_entradas_5 (
    .E1(suma_de_4_entradas_4_acarreo_1), .E2(\multiplicación_de_17_1_1_resultado_11 ),
    .E3(\multiplicación_de_17_1_2_resultado_12 ), .E4(\multiplicación_de_17_1_3_resultado_13 ),
    .out_5(suma_de_4_entradas_5_out_5), .ACARREO_1(suma_de_4_entradas_5_acarreo_1),
    .ACARREO_2(suma_de_4_entradas_5_acarreo_2));
  and and_8 (out_20, and_1_out, suma_de_4_entradas_5_out_5);
  Suma_de_4_Entradas suma_de_4_entradas_6 (
    .E1(suma_de_4_entradas_5_acarreo_1), .E2(\multiplicación_de_17_1_1_resultado_10 ),
    .E3(\multiplicación_de_17_1_2_resultado_11 ), .E4(\multiplicación_de_17_1_3_resultado_12 ),
    .out_5(suma_de_4_entradas_6_out_5), .ACARREO_1(suma_de_4_entradas_6_acarreo_1),
    .ACARREO_2(suma_de_4_entradas_6_acarreo_2));
  and and_9 (out_19, and_1_out, suma_de_4_entradas_6_out_5);
  Suma_de_4_Entradas suma_de_4_entradas_7 (
    .E1(suma_de_4_entradas_6_acarreo_1), .E2(\multiplicación_de_17_1_1_resultado_9 ),
    .E3(\multiplicación_de_17_1_2_resultado_10 ), .E4(\multiplicación_de_17_1_3_resultado_11 ),
    .out_5(suma_de_4_entradas_7_out_5), .ACARREO_1(suma_de_4_entradas_7_acarreo_1),
    .ACARREO_2(suma_de_4_entradas_7_acarreo_2));
  and and_10 (out_18, and_1_out, suma_de_4_entradas_7_out_5);
  Suma_de_4_Entradas suma_de_4_entradas_8 (
    .E1(suma_de_4_entradas_7_acarreo_1), .E2(\multiplicación_de_17_1_1_resultado_8 ),
    .E3(\multiplicación_de_17_1_2_resultado_9 ), .E4(\multiplicación_de_17_1_3_resultado_10 ),
    .out_5(suma_de_4_entradas_8_out_5), .ACARREO_1(suma_de_4_entradas_8_acarreo_1),
    .ACARREO_2(suma_de_4_entradas_8_acarreo_2));
  and and_11 (out_17, and_1_out, suma_de_4_entradas_8_out_5);
  and and_12 (out_16, and_1_out, suma_de_4_entradas_9_out_5);
  Suma_de_4_Entradas suma_de_4_entradas_9 (
    .E1(suma_de_4_entradas_8_acarreo_1), .E2(\multiplicación_de_17_1_1_resultado_7 ),
    .E3(\multiplicación_de_17_1_2_resultado_8 ), .E4(\multiplicación_de_17_1_3_resultado_9 ),
    .out_5(suma_de_4_entradas_9_out_5), .ACARREO_1(suma_de_4_entradas_9_acarreo_1),
    .ACARREO_2(suma_de_4_entradas_9_acarreo_2));
  Suma_de_5_Entradas suma_de_5_entradas_1 (
    .E1(suma_de_4_entradas_9_acarreo_1), .E2(suma_de_4_entradas_8_acarreo_2),
    .E3(\multiplicación_de_17_1_1_resultado_6 ), .E4(\multiplicación_de_17_1_2_resultado_7 ),
    .E5(\multiplicación_de_17_1_3_resultado_8 ), .out_6(suma_de_5_entradas_1_out_6),
    .ACARREO_1(suma_de_5_entradas_1_acarreo_1), .ACARREO_2(suma_de_5_entradas_1_acarreo_2));
  and and_13 (out_15, and_1_out, suma_de_5_entradas_1_out_6);
  Suma_de_4_Entradas suma_de_4_entradas_10 (
    .E1(suma_de_5_entradas_1_acarreo_1), .E2(\multiplicación_de_17_1_1_resultado_5 ),
    .E3(\multiplicación_de_17_1_2_resultado_6 ), .E4(\multiplicación_de_17_1_3_resultado_7 ),
    .out_5(suma_de_4_entradas_10_out_5), .ACARREO_1(suma_de_4_entradas_10_acarreo_1),
    .ACARREO_2(suma_de_4_entradas_10_acarreo_2));
  and and_14 (out_14, and_1_out, suma_de_4_entradas_10_out_5);
  Suma_de_5_Entradas suma_de_5_entradas_2 (
    .E1(suma_de_4_entradas_10_acarreo_1), .E2(suma_de_5_entradas_1_acarreo_2),
    .E3(\multiplicación_de_17_1_1_resultado_4 ), .E4(\multiplicación_de_17_1_2_resultado_5 ),
    .E5(\multiplicación_de_17_1_3_resultado_6 ), .out_6(suma_de_5_entradas_2_out_6),
    .ACARREO_1(suma_de_5_entradas_2_acarreo_1), .ACARREO_2(suma_de_5_entradas_2_acarreo_2));
  and and_15 (out_13, and_1_out, suma_de_5_entradas_2_out_6);
  Suma_de_4_Entradas suma_de_4_entradas_11 (
    .E1(suma_de_5_entradas_2_acarreo_1), .E2(\multiplicación_de_17_1_1_resultado_3 ),
    .E3(\multiplicación_de_17_1_2_resultado_4 ), .E4(\multiplicación_de_17_1_3_resultado_5 ),
    .out_5(suma_de_4_entradas_11_out_5), .ACARREO_1(suma_de_4_entradas_11_acarreo_1),
    .ACARREO_2(suma_de_4_entradas_11_acarreo_2));
  and and_16 (out_12, and_1_out, suma_de_4_entradas_11_out_5);
  Suma_de_4_Entradas suma_de_4_entradas_12 (
    .E1(suma_de_4_entradas_11_acarreo_1), .E2(\multiplicación_de_17_1_1_resultado_2 ),
    .E3(\multiplicación_de_17_1_2_resultado_3 ), .E4(\multiplicación_de_17_1_3_resultado_4 ),
    .out_5(suma_de_4_entradas_12_out_5), .ACARREO_1(suma_de_4_entradas_12_acarreo_1),
    .ACARREO_2(suma_de_4_entradas_12_acarreo_2));
  and and_17 (out_11, and_1_out, suma_de_4_entradas_12_out_5);
  Suma_de_4_Entradas suma_de_4_entradas_13 (
    .E1(suma_de_4_entradas_12_acarreo_1), .E2(\multiplicación_de_17_1_1_resultado_1 ),
    .E3(\multiplicación_de_17_1_2_resultado_2 ), .E4(\multiplicación_de_17_1_3_resultado_3 ),
    .out_5(suma_de_4_entradas_13_out_5), .ACARREO_1(suma_de_4_entradas_13_acarreo_1),
    .ACARREO_2(suma_de_4_entradas_13_acarreo_2));
  and and_18 (out_10, and_1_out, suma_de_4_entradas_13_out_5);
  Suma_de_3_Entradas suma_de_3_entradas_1 (
    .E1(suma_de_4_entradas_13_acarreo_1), .E2(\multiplicación_de_17_1_2_resultado_1 ),
    .E3(\multiplicación_de_17_1_3_resultado_2 ), .out_4(suma_de_3_entradas_1_out_4),
    .ACARREO_1(suma_de_3_entradas_1_acarreo_1));
  and and_19 (out_9, and_1_out, suma_de_3_entradas_1_out_4);
  Suma_de_3_Entradas suma_de_3_entradas_2 (
    .E1(suma_de_3_entradas_1_acarreo_1), .E2(suma_de_4_entradas_13_acarreo_2),
    .E3(\multiplicación_de_17_1_3_resultado_1 ), .out_4(suma_de_3_entradas_2_out_4),
    .ACARREO_1(suma_de_3_entradas_2_acarreo_1));
  and and_20 (out_8, and_1_out, suma_de_3_entradas_2_out_4);
  and and_21 (out_7, and_1_out, suma_de_3_entradas_2_acarreo_1);
  // also tied to GND on the sheet: {suma_de_4_entradas_1_acarreo_2, suma_de_4_entradas_2_acarreo_2, suma_de_4_entradas_3_acarreo_2, suma_de_4_entradas_4_acarreo_2, suma_de_4_entradas_5_acarreo_2, suma_de_4_entradas_6_acarreo_2, suma_de_4_entradas_7_acarreo_2, suma_de_4_entradas_9_acarreo_2, suma_de_4_entradas_10_acarreo_2, suma_de_5_entradas_2_acarreo_2, suma_de_4_entradas_11_acarreo_2, suma_de_4_entradas_12_acarreo_2}

  // Notes on the sheet:
  //   EXPONENTE
  //   BASE
endmodule

module Segmento_A (
  input  Entrada_A,
  input  Entrada_B,
  input  Entrada_C,
  input  Entrada_D,
  output out_5
);

  wire and_1_out, and_2_out, and_3_out, and_4_out, and_5_out, and_6_out, not_1_out, not_2_out, not_3_out,
       not_4_out;

  not not_1 (not_1_out, Entrada_A);
  not not_2 (not_2_out, Entrada_B);
  not not_3 (not_3_out, Entrada_C);
  not not_4 (not_4_out, Entrada_D);
  and and_1 (and_1_out, not_1_out, Entrada_B, Entrada_D);
  and and_2 (and_2_out, Entrada_A, not_2_out, not_3_out);
  and and_3 (and_3_out, not_2_out, not_4_out);
  and and_4 (and_4_out, not_1_out, Entrada_C);
  and and_5 (and_5_out, Entrada_B, Entrada_C);
  and and_6 (and_6_out, Entrada_A, not_4_out);
  or or_1 (out_5, and_1_out, and_2_out, and_3_out, and_4_out, and_5_out, and_6_out);

  // Notes on the sheet:
  //   Circuito del Segmento A
  //   Salida Segmento A
endmodule

module Segmento_B (
  input  Entrada_A,
  input  Entrada_B,
  input  Entrada_C,
  input  Entrada_D,
  output out_5
);

  wire and_1_out, and_2_out, and_3_out, and_4_out, and_5_out, not_1_out, not_2_out, not_3_out, not_4_out;

  not not_1 (not_1_out, Entrada_A);
  not not_2 (not_2_out, Entrada_B);
  not not_3 (not_3_out, Entrada_C);
  not not_4 (not_4_out, Entrada_D);
  and and_1 (and_1_out, not_1_out, not_3_out, not_4_out);
  and and_2 (and_2_out, not_1_out, Entrada_C, Entrada_D);
  and and_3 (and_3_out, Entrada_A, not_3_out, Entrada_D);
  and and_4 (and_4_out, not_2_out, not_3_out);
  and and_5 (and_5_out, not_2_out, not_4_out);
  or or_1 (out_5, and_1_out, and_2_out, and_3_out, and_4_out, and_5_out);

  // Notes on the sheet:
  //   Circuito del Segmento B
  //   Salida Segmento B
endmodule

module Segmento_C (
  input  Entrada_A,
  input  Entrada_B,
  input  Entrada_C,
  input  Entrada_D,
  output out_5
);

  wire and_1_out, and_2_out, and_3_out, and_4_out, and_5_out, not_1_out, not_2_out, not_3_out;

  not not_1 (not_1_out, Entrada_A);
  not not_2 (not_2_out, Entrada_B);
  not not_3 (not_3_out, Entrada_C);
  // NOT_Gate not_4 has open pins: in=Entrada_D, out=open
  and and_1 (and_1_out, not_2_out, not_3_out);
  and and_2 (and_2_out, not_2_out, Entrada_D);
  and and_3 (and_3_out, not_3_out, Entrada_D);
  and and_4 (and_4_out, not_1_out, Entrada_B);
  and and_5 (and_5_out, Entrada_A, not_2_out);
  or or_1 (out_5, and_1_out, and_2_out, and_3_out, and_4_out, and_5_out);

  // Notes on the sheet:
  //   Circuito del Segmento C
  //   Salida Segmento C
endmodule

module Segmento_D (
  input  Entrada_A,
  input  Entrada_B,
  input  Entrada_C,
  input  Entrada_D,
  output out_5
);

  wire and_1_out, and_2_out, and_3_out, and_4_out, and_5_out, not_1_out, not_2_out, not_3_out, not_4_out;

  not not_1 (not_1_out, Entrada_A);
  not not_2 (not_2_out, Entrada_B);
  not not_3 (not_3_out, Entrada_C);
  not not_4 (not_4_out, Entrada_D);
  and and_1 (and_1_out, not_2_out, not_3_out, not_4_out);
  and and_2 (and_2_out, not_2_out, Entrada_C, Entrada_D);
  and and_3 (and_3_out, not_1_out, Entrada_C, not_4_out);
  and and_4 (and_4_out, Entrada_B, not_3_out, Entrada_D);
  and and_5 (and_5_out, Entrada_A, Entrada_B, not_4_out);
  or or_1 (out_5, and_1_out, and_2_out, and_3_out, and_4_out, and_5_out);

  // Notes on the sheet:
  //   Circuito del Segmento D
  //   Salida Segmento D
endmodule

module Segmento_E (
  input  Entrada_A,
  input  Entrada_B,
  input  Entrada_C,
  input  Entrada_D,
  output out_5
);

  wire and_1_out, and_2_out, and_3_out, and_4_out, not_2_out, not_4_out;

  // NOT_Gate not_1 has open pins: in=Entrada_A, out=open
  not not_2 (not_2_out, Entrada_B);
  // NOT_Gate not_3 has open pins: in=Entrada_C, out=open
  not not_4 (not_4_out, Entrada_D);
  and and_1 (and_1_out, not_2_out, not_4_out);
  and and_2 (and_2_out, Entrada_C, not_4_out);
  and and_3 (and_3_out, Entrada_A, Entrada_B);
  and and_4 (and_4_out, Entrada_A, Entrada_C);
  or or_1 (out_5, and_1_out, and_2_out, and_3_out, and_4_out);

  // Notes on the sheet:
  //   Circuito del Segmento E
  //   Salida Segmento E
endmodule

module Segmento_F (
  input  Entrada_A,
  input  Entrada_B,
  input  Entrada_C,
  input  Entrada_D,
  output out_5
);

  wire and_1_out, and_2_out, and_3_out, and_4_out, and_5_out, not_1_out, not_2_out, not_3_out, not_4_out;

  not not_1 (not_1_out, Entrada_A);
  not not_2 (not_2_out, Entrada_B);
  not not_3 (not_3_out, Entrada_C);
  not not_4 (not_4_out, Entrada_D);
  and and_1 (and_1_out, not_1_out, Entrada_B, not_3_out);
  and and_2 (and_2_out, not_3_out, not_4_out);
  and and_3 (and_3_out, Entrada_B, not_4_out);
  and and_4 (and_4_out, Entrada_A, Entrada_C);
  and and_5 (and_5_out, Entrada_A, not_2_out);
  or or_1 (out_5, and_1_out, and_2_out, and_3_out, and_4_out, and_5_out);

  // Notes on the sheet:
  //   Circuito del Segmento F
  //   Salida Segmento F
endmodule

module Segmento_G (
  input  Entrada_A,
  input  Entrada_B,
  input  Entrada_C,
  input  Entrada_D,
  output out_5
);

  wire and_1_out, and_2_out, and_3_out, and_4_out, and_5_out, not_1_out, not_2_out, not_3_out, not_4_out;

  not not_1 (not_1_out, Entrada_A);
  not not_2 (not_2_out, Entrada_B);
  not not_3 (not_3_out, Entrada_C);
  not not_4 (not_4_out, Entrada_D);
  and and_1 (and_1_out, not_1_out, Entrada_B, not_4_out);
  and and_2 (and_2_out, Entrada_B, not_3_out, Entrada_D);
  and and_3 (and_3_out, not_2_out, Entrada_C);
  and and_4 (and_4_out, Entrada_A, Entrada_C);
  and and_5 (and_5_out, Entrada_A, not_2_out);
  or or_1 (out_5, and_1_out, and_2_out, and_3_out, and_4_out, and_5_out);

  // Notes on the sheet:
  //   Circuito del Segmento G
  //   Salida Segmento G
endmodule
module Display_3_Entradas (
  input  E1,
  input  E2,
  input  E3,
  output a,
  output b,
  output c,
  output d,
  output e,
  output f,
  output g
);

  Segmento_A segmento_a_1 (.Entrada_A(1'b0), .Entrada_B(E1), .Entrada_C(E2), .Entrada_D(E3), .out_5(a));
  Segmento_B segmento_b_1 (.Entrada_A(1'b0), .Entrada_B(E1), .Entrada_C(E2), .Entrada_D(E3), .out_5(b));
  Segmento_C segmento_c_1 (.Entrada_A(1'b0), .Entrada_B(E1), .Entrada_C(E2), .Entrada_D(E3), .out_5(c));
  Segmento_D segmento_d_1 (.Entrada_A(1'b0), .Entrada_B(E1), .Entrada_C(E2), .Entrada_D(E3), .out_5(d));
  Segmento_E segmento_e_1 (.Entrada_A(1'b0), .Entrada_B(E1), .Entrada_C(E2), .Entrada_D(E3), .out_5(e));
  Segmento_F segmento_f_1 (.Entrada_A(1'b0), .Entrada_B(E1), .Entrada_C(E2), .Entrada_D(E3), .out_5(f));
  Segmento_G segmento_g_1 (.Entrada_A(1'b0), .Entrada_B(E1), .Entrada_C(E2), .Entrada_D(E3), .out_5(g));

  // Notes on the sheet:
  //   ENTRADAS
endmodule

module Display_4_Entradas (
  input  E1,
  input  E2,
  input  E3,
  input  E4,
  output a,
  output b,
  output c,
  output d,
  output e,
  output f,
  output g
);

  Segmento_A segmento_a_1 (.Entrada_A(E1), .Entrada_B(E2), .Entrada_C(E3), .Entrada_D(E4), .out_5(a));
  Segmento_B segmento_b_1 (.Entrada_A(E1), .Entrada_B(E2), .Entrada_C(E3), .Entrada_D(E4), .out_5(b));
  Segmento_C segmento_c_1 (.Entrada_A(E1), .Entrada_B(E2), .Entrada_C(E3), .Entrada_D(E4), .out_5(c));
  Segmento_D segmento_d_1 (.Entrada_A(E1), .Entrada_B(E2), .Entrada_C(E3), .Entrada_D(E4), .out_5(d));
  Segmento_E segmento_e_1 (.Entrada_A(E1), .Entrada_B(E2), .Entrada_C(E3), .Entrada_D(E4), .out_5(e));
  Segmento_F segmento_f_1 (.Entrada_A(E1), .Entrada_B(E2), .Entrada_C(E3), .Entrada_D(E4), .out_5(f));
  Segmento_G segmento_g_1 (.Entrada_A(E1), .Entrada_B(E2), .Entrada_C(E3), .Entrada_D(E4), .out_5(g));

  // Notes on the sheet:
  //   ENTRADAS
endmodule

module BCD_3 (
  input  E1,
  input  E2,
  input  E3,
  output R1,
  output R2,
  output R3,
  output R4
);

  wire and_1_out, and_2_out, and_4_out, and_5_out, and_6_out, and_7_out, not_1_out, not_2_out, not_3_out,
       not_4_out;

  and and_1 (and_1_out, E1, E2);
  and and_2 (and_2_out, E1, E3);
  not not_1 (not_1_out, E2);
  not not_2 (not_2_out, E3);
  not not_3 (not_3_out, E1);
  not not_4 (not_4_out, E3);
  or or_1 (R1, and_1_out, and_2_out);
  and and_3 (R2, E1, not_1_out, not_2_out);
  and and_4 (and_4_out, not_3_out, E2);
  and and_5 (and_5_out, E2, E3);
  and and_6 (and_6_out, not_3_out, E3);
  and and_7 (and_7_out, E1, E2, not_4_out);
  or or_2 (R3, and_4_out, and_5_out);
  or or_3 (R4, and_6_out, and_7_out);

  // Notes on the sheet:
  //   ENTRADAS
endmodule

module BCD_4 (
  input  E1,
  input  E2,
  input  E3,
  input  E4,
  output out_5,
  output out_6,
  output out_7,
  output out_8
);

  wire and_1_out, and_2_out, and_3_out, and_4_out, and_5_out, and_6_out, and_7_out, and_8_out, and_9_out,
       and_10_out, and_11_out, not_1_out, not_2_out, not_3_out, not_4_out;

  not not_1 (not_1_out, E1);
  not not_2 (not_2_out, E2);
  not not_3 (not_3_out, E3);
  not not_4 (not_4_out, E4);
  and and_1 (and_1_out, not_1_out, E2, E4);
  and and_2 (and_2_out, not_1_out, E2, E3);
  or or_1 (out_5, and_1_out, and_2_out, and_3_out);
  and and_3 (and_3_out, E1, not_2_out, not_3_out);
  and and_4 (and_4_out, not_1_out, E2, not_3_out, not_4_out);
  or or_2 (out_6, and_4_out, and_5_out);
  and and_5 (and_5_out, E1, not_2_out, not_3_out, E4);
  and and_6 (and_6_out, not_1_out, not_2_out, E3);
  and and_7 (and_7_out, not_1_out, E3, E4);
  or or_3 (out_7, and_6_out, and_7_out, and_8_out);
  and and_8 (and_8_out, E1, not_2_out, not_3_out, not_4_out);
  and and_9 (and_9_out, not_1_out, not_2_out, E4);
  and and_10 (and_10_out, E1, not_2_out, not_3_out, not_4_out);
  or or_4 (out_8, and_9_out, and_10_out, and_11_out);
  and and_11 (and_11_out, not_1_out, E2, E3, not_4_out);

  // Notes on the sheet:
  //   ENTRADAS
endmodule

module Binario_a_BCD (
  input  in_1,
  input  in_2,
  input  in_3,
  input  in_4,
  input  in_5,
  input  in_6,
  input  in_7,
  input  in_8,
  input  in_9,
  input  in_10,
  input  in_11,
  input  in_12,
  input  in_13,
  input  in_14,
  input  in_15,
  input  in_16,
  input  in_17,
  input  in_18,
  input  in_19,
  input  in_20,
  output out_21,
  output out_22,
  output out_23,
  output out_24,
  output out_25,
  output out_26,
  output out_27,
  output out_28,
  output out_29,
  output out_30,
  output out_31,
  output out_32,
  output out_33,
  output out_34,
  output out_35,
  output out_36,
  output out_37,
  output out_38,
  output out_39,
  output out_40,
  output out_41,
  output out_42,
  output out_43,
  output out_44,
  output out_45,
  output out_46
);

  wire bcd_3_1_r1, bcd_3_1_r2, bcd_3_1_r3, bcd_3_1_r4, bcd_3_2_r1, bcd_3_2_r2, bcd_3_2_r3, bcd_3_2_r4,
       bcd_3_3_r1, bcd_3_3_r2, bcd_3_3_r3, bcd_3_3_r4, bcd_3_4_r1, bcd_3_4_r2, bcd_3_4_r3, bcd_3_4_r4,
       bcd_3_5_r1, bcd_3_5_r2, bcd_3_5_r3, bcd_3_5_r4, bcd_3_6_r2, bcd_3_6_r3, bcd_3_6_r4, bcd_4_1_out_5,
       bcd_4_1_out_6, bcd_4_1_out_7, bcd_4_1_out_8, bcd_4_2_out_5, bcd_4_2_out_6, bcd_4_2_out_7,
       bcd_4_2_out_8, bcd_4_3_out_5, bcd_4_3_out_6, bcd_4_3_out_7, bcd_4_3_out_8, bcd_4_4_out_5,
       bcd_4_4_out_6, bcd_4_4_out_7, bcd_4_4_out_8, bcd_4_5_out_5, bcd_4_5_out_6, bcd_4_5_out_7,
       bcd_4_5_out_8, bcd_4_6_out_5, bcd_4_6_out_6, bcd_4_6_out_7, bcd_4_6_out_8, bcd_4_7_out_5,
       bcd_4_7_out_6, bcd_4_7_out_7, bcd_4_7_out_8, bcd_4_8_out_5, bcd_4_8_out_6, bcd_4_8_out_7,
       bcd_4_8_out_8, bcd_4_9_out_5, bcd_4_9_out_6, bcd_4_9_out_7, bcd_4_9_out_8, bcd_4_10_out_5,
       bcd_4_10_out_6, bcd_4_10_out_7, bcd_4_10_out_8, bcd_4_11_out_5, bcd_4_11_out_6, bcd_4_11_out_7,
       bcd_4_11_out_8, bcd_4_12_out_5, bcd_4_12_out_6, bcd_4_12_out_7, bcd_4_12_out_8, bcd_4_13_out_5,
       bcd_4_13_out_6, bcd_4_13_out_7, bcd_4_13_out_8, bcd_4_14_out_5, bcd_4_14_out_6, bcd_4_14_out_7,
       bcd_4_14_out_8, bcd_4_15_out_5, bcd_4_15_out_6, bcd_4_15_out_7, bcd_4_15_out_8, bcd_4_16_out_5,
       bcd_4_16_out_6, bcd_4_16_out_7, bcd_4_16_out_8, bcd_4_17_out_5, bcd_4_17_out_6, bcd_4_17_out_7,
       bcd_4_17_out_8, bcd_4_18_out_5, bcd_4_18_out_6, bcd_4_18_out_7, bcd_4_18_out_8, bcd_4_19_out_5,
       bcd_4_19_out_6, bcd_4_19_out_7, bcd_4_19_out_8, bcd_4_20_out_5, bcd_4_20_out_6, bcd_4_20_out_7,
       bcd_4_20_out_8, bcd_4_21_out_5, bcd_4_21_out_6, bcd_4_21_out_7, bcd_4_21_out_8, bcd_4_22_out_5,
       bcd_4_22_out_6, bcd_4_22_out_7, bcd_4_22_out_8, bcd_4_23_out_5, bcd_4_23_out_6, bcd_4_23_out_7,
       bcd_4_23_out_8, bcd_4_24_out_5, bcd_4_24_out_6, bcd_4_24_out_7, bcd_4_24_out_8, bcd_4_25_out_5,
       bcd_4_25_out_6, bcd_4_25_out_7, bcd_4_25_out_8, bcd_4_26_out_5, bcd_4_26_out_6, bcd_4_26_out_7,
       bcd_4_26_out_8, bcd_4_27_out_5, bcd_4_27_out_6, bcd_4_27_out_7, bcd_4_27_out_8, bcd_4_28_out_5,
       bcd_4_28_out_6, bcd_4_28_out_7, bcd_4_28_out_8, bcd_4_29_out_5, bcd_4_29_out_6, bcd_4_29_out_7,
       bcd_4_29_out_8, bcd_4_30_out_5, bcd_4_30_out_6, bcd_4_30_out_7, bcd_4_30_out_8, bcd_4_31_out_5,
       bcd_4_31_out_6, bcd_4_31_out_7, bcd_4_31_out_8, bcd_4_32_out_5, bcd_4_32_out_6, bcd_4_32_out_7,
       bcd_4_32_out_8, bcd_4_33_out_5, bcd_4_33_out_6, bcd_4_33_out_7, bcd_4_33_out_8, bcd_4_34_out_5,
       bcd_4_34_out_6, bcd_4_34_out_7, bcd_4_34_out_8, bcd_4_35_out_5, bcd_4_35_out_6, bcd_4_35_out_7,
       bcd_4_35_out_8, bcd_4_36_out_5, bcd_4_36_out_6, bcd_4_36_out_7, bcd_4_36_out_8, bcd_4_37_out_5,
       bcd_4_37_out_6, bcd_4_37_out_7, bcd_4_37_out_8, bcd_4_38_out_5, bcd_4_38_out_6, bcd_4_38_out_7,
       bcd_4_38_out_8, bcd_4_39_out_5, bcd_4_39_out_6, bcd_4_39_out_7, bcd_4_39_out_8, bcd_4_40_out_5,
       bcd_4_40_out_6, bcd_4_40_out_7, bcd_4_40_out_8, bcd_4_41_out_5, bcd_4_41_out_6, bcd_4_41_out_7,
       bcd_4_41_out_8, bcd_4_42_out_5, bcd_4_42_out_6, bcd_4_42_out_7, bcd_4_42_out_8, bcd_4_43_out_5,
       bcd_4_43_out_6, bcd_4_43_out_7, bcd_4_43_out_8, bcd_4_44_out_5, bcd_4_44_out_6, bcd_4_44_out_7,
       bcd_4_44_out_8, bcd_4_46_out_5, bcd_4_46_out_6, bcd_4_46_out_7, bcd_4_46_out_8;

  BCD_3 bcd_3_1 (.E1(in_1), .E2(in_2), .E3(in_3), .R1(bcd_3_1_r1), .R2(bcd_3_1_r2), .R3(bcd_3_1_r3), .R4(bcd_3_1_r4));
  BCD_4 bcd_4_1 (
    .E1(bcd_3_1_r2), .E2(bcd_3_1_r3), .E3(bcd_3_1_r4), .E4(in_4), .out_5(bcd_4_1_out_5),
    .out_6(bcd_4_1_out_6), .out_7(bcd_4_1_out_7), .out_8(bcd_4_1_out_8));
  BCD_3 bcd_3_2 (
    .E1(bcd_3_1_r1), .E2(bcd_4_1_out_5), .E3(bcd_4_2_out_5), .R1(bcd_3_2_r1), .R2(bcd_3_2_r2),
    .R3(bcd_3_2_r3), .R4(bcd_3_2_r4));
  BCD_4 bcd_4_2 (
    .E1(bcd_4_1_out_6), .E2(bcd_4_1_out_7), .E3(bcd_4_1_out_8), .E4(in_5), .out_5(bcd_4_2_out_5),
    .out_6(bcd_4_2_out_6), .out_7(bcd_4_2_out_7), .out_8(bcd_4_2_out_8));
  BCD_4 bcd_4_3 (
    .E1(bcd_4_2_out_6), .E2(bcd_4_2_out_7), .E3(bcd_4_2_out_8), .E4(in_6), .out_5(bcd_4_3_out_5),
    .out_6(bcd_4_3_out_6), .out_7(bcd_4_3_out_7), .out_8(bcd_4_3_out_8));
  BCD_4 bcd_4_4 (
    .E1(bcd_3_2_r2), .E2(bcd_3_2_r3), .E3(bcd_3_2_r4), .E4(bcd_4_3_out_5), .out_5(bcd_4_4_out_5),
    .out_6(bcd_4_4_out_6), .out_7(bcd_4_4_out_7), .out_8(bcd_4_4_out_8));
  BCD_4 bcd_4_5 (
    .E1(bcd_4_4_out_6), .E2(bcd_4_4_out_7), .E3(bcd_4_4_out_8), .E4(bcd_4_6_out_5), .out_5(bcd_4_5_out_5),
    .out_6(bcd_4_5_out_6), .out_7(bcd_4_5_out_7), .out_8(bcd_4_5_out_8));
  BCD_4 bcd_4_6 (
    .E1(bcd_4_3_out_6), .E2(bcd_4_3_out_7), .E3(bcd_4_3_out_8), .E4(in_7), .out_5(bcd_4_6_out_5),
    .out_6(bcd_4_6_out_6), .out_7(bcd_4_6_out_7), .out_8(bcd_4_6_out_8));
  BCD_4 bcd_4_7 (
    .E1(bcd_4_6_out_6), .E2(bcd_4_6_out_7), .E3(bcd_4_6_out_8), .E4(in_8), .out_5(bcd_4_7_out_5),
    .out_6(bcd_4_7_out_6), .out_7(bcd_4_7_out_7), .out_8(bcd_4_7_out_8));
  BCD_3 bcd_3_3 (
    .E1(bcd_3_2_r1), .E2(bcd_4_4_out_5), .E3(bcd_4_5_out_5), .R1(bcd_3_3_r1), .R2(bcd_3_3_r2),
    .R3(bcd_3_3_r3), .R4(bcd_3_3_r4));
  BCD_4 bcd_4_8 (
    .E1(bcd_3_3_r2), .E2(bcd_3_3_r3), .E3(bcd_3_3_r4), .E4(bcd_4_9_out_5), .out_5(bcd_4_8_out_5),
    .out_6(bcd_4_8_out_6), .out_7(bcd_4_8_out_7), .out_8(bcd_4_8_out_8));
  BCD_4 bcd_4_9 (
    .E1(bcd_4_5_out_6), .E2(bcd_4_5_out_7), .E3(bcd_4_5_out_8), .E4(bcd_4_7_out_5), .out_5(bcd_4_9_out_5),
    .out_6(bcd_4_9_out_6), .out_7(bcd_4_9_out_7), .out_8(bcd_4_9_out_8));
  BCD_4 bcd_4_10 (
    .E1(bcd_4_9_out_6), .E2(bcd_4_9_out_7), .E3(bcd_4_9_out_8), .E4(bcd_4_11_out_5), .out_5(bcd_4_10_out_5),
    .out_6(bcd_4_10_out_6), .out_7(bcd_4_10_out_7), .out_8(bcd_4_10_out_8));
  BCD_4 bcd_4_11 (
    .E1(bcd_4_7_out_6), .E2(bcd_4_7_out_7), .E3(bcd_4_7_out_8), .E4(in_9), .out_5(bcd_4_11_out_5),
    .out_6(bcd_4_11_out_6), .out_7(bcd_4_11_out_7), .out_8(bcd_4_11_out_8));
  BCD_4 bcd_4_12 (
    .E1(bcd_4_11_out_6), .E2(bcd_4_11_out_7), .E3(bcd_4_11_out_8), .E4(in_10), .out_5(bcd_4_12_out_5),
    .out_6(bcd_4_12_out_6), .out_7(bcd_4_12_out_7), .out_8(bcd_4_12_out_8));
  BCD_3 bcd_3_4 (
    .E1(bcd_3_3_r1), .E2(bcd_4_8_out_5), .E3(bcd_4_13_out_5), .R1(bcd_3_4_r1), .R2(bcd_3_4_r2),
    .R3(bcd_3_4_r3), .R4(bcd_3_4_r4));
  BCD_4 bcd_4_13 (
    .E1(bcd_4_8_out_6), .E2(bcd_4_8_out_7), .E3(bcd_4_8_out_8), .E4(bcd_4_10_out_5), .out_5(bcd_4_13_out_5),
    .out_6(bcd_4_13_out_6), .out_7(bcd_4_13_out_7), .out_8(bcd_4_13_out_8));
  BCD_4 bcd_4_14 (
    .E1(bcd_4_13_out_6), .E2(bcd_4_13_out_7), .E3(bcd_4_13_out_8), .E4(bcd_4_15_out_5),
    .out_5(bcd_4_14_out_5), .out_6(bcd_4_14_out_6), .out_7(bcd_4_14_out_7), .out_8(bcd_4_14_out_8));
  BCD_4 bcd_4_15 (
    .E1(bcd_4_10_out_6), .E2(bcd_4_10_out_7), .E3(bcd_4_10_out_8), .E4(bcd_4_12_out_5),
    .out_5(bcd_4_15_out_5), .out_6(bcd_4_15_out_6), .out_7(bcd_4_15_out_7), .out_8(bcd_4_15_out_8));
  BCD_4 bcd_4_16 (
    .E1(bcd_4_15_out_6), .E2(bcd_4_15_out_7), .E3(bcd_4_15_out_8), .E4(bcd_4_17_out_5),
    .out_5(bcd_4_16_out_5), .out_6(bcd_4_16_out_6), .out_7(bcd_4_16_out_7), .out_8(bcd_4_16_out_8));
  BCD_4 bcd_4_17 (
    .E1(bcd_4_12_out_6), .E2(bcd_4_12_out_7), .E3(bcd_4_12_out_8), .E4(in_11), .out_5(bcd_4_17_out_5),
    .out_6(bcd_4_17_out_6), .out_7(bcd_4_17_out_7), .out_8(bcd_4_17_out_8));
  BCD_4 bcd_4_18 (
    .E1(bcd_4_17_out_6), .E2(bcd_4_17_out_7), .E3(bcd_4_17_out_8), .E4(in_12), .out_5(bcd_4_18_out_5),
    .out_6(bcd_4_18_out_6), .out_7(bcd_4_18_out_7), .out_8(bcd_4_18_out_8));
  BCD_4 bcd_4_19 (
    .E1(bcd_3_4_r2), .E2(bcd_3_4_r3), .E3(bcd_3_4_r4), .E4(bcd_4_14_out_5), .out_5(bcd_4_19_out_5),
    .out_6(bcd_4_19_out_6), .out_7(bcd_4_19_out_7), .out_8(bcd_4_19_out_8));
  BCD_4 bcd_4_20 (
    .E1(bcd_4_19_out_6), .E2(bcd_4_19_out_7), .E3(bcd_4_19_out_8), .E4(bcd_4_21_out_5),
    .out_5(bcd_4_20_out_5), .out_6(bcd_4_20_out_6), .out_7(bcd_4_20_out_7), .out_8(bcd_4_20_out_8));
  BCD_4 bcd_4_21 (
    .E1(bcd_4_14_out_6), .E2(bcd_4_14_out_7), .E3(bcd_4_14_out_8), .E4(bcd_4_16_out_5),
    .out_5(bcd_4_21_out_5), .out_6(bcd_4_21_out_6), .out_7(bcd_4_21_out_7), .out_8(bcd_4_21_out_8));
  BCD_4 bcd_4_22 (
    .E1(bcd_4_21_out_6), .E2(bcd_4_21_out_7), .E3(bcd_4_21_out_8), .E4(bcd_4_23_out_5),
    .out_5(bcd_4_22_out_5), .out_6(bcd_4_22_out_6), .out_7(bcd_4_22_out_7), .out_8(bcd_4_22_out_8));
  BCD_4 bcd_4_23 (
    .E1(bcd_4_16_out_6), .E2(bcd_4_16_out_7), .E3(bcd_4_16_out_8), .E4(bcd_4_18_out_5),
    .out_5(bcd_4_23_out_5), .out_6(bcd_4_23_out_6), .out_7(bcd_4_23_out_7), .out_8(bcd_4_23_out_8));
  BCD_4 bcd_4_24 (
    .E1(bcd_4_23_out_6), .E2(bcd_4_23_out_7), .E3(bcd_4_23_out_8), .E4(bcd_4_25_out_5),
    .out_5(bcd_4_24_out_5), .out_6(bcd_4_24_out_6), .out_7(bcd_4_24_out_7), .out_8(bcd_4_24_out_8));
  BCD_4 bcd_4_25 (
    .E1(bcd_4_18_out_6), .E2(bcd_4_18_out_7), .E3(bcd_4_18_out_8), .E4(in_13), .out_5(bcd_4_25_out_5),
    .out_6(bcd_4_25_out_6), .out_7(bcd_4_25_out_7), .out_8(bcd_4_25_out_8));
  BCD_4 bcd_4_26 (
    .E1(bcd_4_25_out_6), .E2(bcd_4_25_out_7), .E3(bcd_4_25_out_8), .E4(in_14), .out_5(bcd_4_26_out_5),
    .out_6(bcd_4_26_out_6), .out_7(bcd_4_26_out_7), .out_8(bcd_4_26_out_8));
  BCD_3 bcd_3_5 (
    .E1(bcd_3_4_r1), .E2(bcd_4_19_out_5), .E3(bcd_4_20_out_5), .R1(bcd_3_5_r1), .R2(bcd_3_5_r2),
    .R3(bcd_3_5_r3), .R4(bcd_3_5_r4));
  BCD_4 bcd_4_27 (
    .E1(bcd_4_20_out_6), .E2(bcd_4_20_out_7), .E3(bcd_4_20_out_8), .E4(bcd_4_22_out_5),
    .out_5(bcd_4_27_out_5), .out_6(bcd_4_27_out_6), .out_7(bcd_4_27_out_7), .out_8(bcd_4_27_out_8));
  BCD_4 bcd_4_28 (
    .E1(bcd_4_27_out_6), .E2(bcd_4_27_out_7), .E3(bcd_4_27_out_8), .E4(bcd_4_29_out_5),
    .out_5(bcd_4_28_out_5), .out_6(bcd_4_28_out_6), .out_7(bcd_4_28_out_7), .out_8(bcd_4_28_out_8));
  BCD_4 bcd_4_29 (
    .E1(bcd_4_22_out_6), .E2(bcd_4_22_out_7), .E3(bcd_4_22_out_8), .E4(bcd_4_24_out_5),
    .out_5(bcd_4_29_out_5), .out_6(bcd_4_29_out_6), .out_7(bcd_4_29_out_7), .out_8(bcd_4_29_out_8));
  BCD_4 bcd_4_30 (
    .E1(bcd_4_29_out_6), .E2(bcd_4_29_out_7), .E3(bcd_4_29_out_8), .E4(bcd_4_31_out_5),
    .out_5(bcd_4_30_out_5), .out_6(bcd_4_30_out_6), .out_7(bcd_4_30_out_7), .out_8(bcd_4_30_out_8));
  BCD_4 bcd_4_31 (
    .E1(bcd_4_24_out_6), .E2(bcd_4_24_out_7), .E3(bcd_4_24_out_8), .E4(bcd_4_26_out_5),
    .out_5(bcd_4_31_out_5), .out_6(bcd_4_31_out_6), .out_7(bcd_4_31_out_7), .out_8(bcd_4_31_out_8));
  BCD_4 bcd_4_32 (
    .E1(bcd_4_31_out_6), .E2(bcd_4_31_out_7), .E3(bcd_4_31_out_8), .E4(bcd_4_33_out_5),
    .out_5(bcd_4_32_out_5), .out_6(bcd_4_32_out_6), .out_7(bcd_4_32_out_7), .out_8(bcd_4_32_out_8));
  BCD_4 bcd_4_33 (
    .E1(bcd_4_26_out_6), .E2(bcd_4_26_out_7), .E3(bcd_4_26_out_8), .E4(in_15), .out_5(bcd_4_33_out_5),
    .out_6(bcd_4_33_out_6), .out_7(bcd_4_33_out_7), .out_8(bcd_4_33_out_8));
  BCD_4 bcd_4_34 (
    .E1(bcd_4_33_out_6), .E2(bcd_4_33_out_7), .E3(bcd_4_33_out_8), .E4(in_16), .out_5(bcd_4_34_out_5),
    .out_6(bcd_4_34_out_6), .out_7(bcd_4_34_out_7), .out_8(bcd_4_34_out_8));
  BCD_4 bcd_4_35 (
    .E1(bcd_3_5_r2), .E2(bcd_3_5_r3), .E3(bcd_3_5_r4), .E4(bcd_4_27_out_5), .out_5(bcd_4_35_out_5),
    .out_6(bcd_4_35_out_6), .out_7(bcd_4_35_out_7), .out_8(bcd_4_35_out_8));
  BCD_4 bcd_4_36 (
    .E1(bcd_4_35_out_6), .E2(bcd_4_35_out_7), .E3(bcd_4_35_out_8), .E4(bcd_4_28_out_5),
    .out_5(bcd_4_36_out_5), .out_6(bcd_4_36_out_6), .out_7(bcd_4_36_out_7), .out_8(bcd_4_36_out_8));
  BCD_4 bcd_4_37 (
    .E1(bcd_4_28_out_6), .E2(bcd_4_28_out_7), .E3(bcd_4_28_out_8), .E4(bcd_4_30_out_5),
    .out_5(bcd_4_37_out_5), .out_6(bcd_4_37_out_6), .out_7(bcd_4_37_out_7), .out_8(bcd_4_37_out_8));
  BCD_4 bcd_4_38 (
    .E1(bcd_4_37_out_6), .E2(bcd_4_37_out_7), .E3(bcd_4_37_out_8), .E4(bcd_4_39_out_5),
    .out_5(bcd_4_38_out_5), .out_6(bcd_4_38_out_6), .out_7(bcd_4_38_out_7), .out_8(bcd_4_38_out_8));
  BCD_4 bcd_4_39 (
    .E1(bcd_4_30_out_6), .E2(bcd_4_30_out_7), .E3(bcd_4_30_out_8), .E4(bcd_4_32_out_5),
    .out_5(bcd_4_39_out_5), .out_6(bcd_4_39_out_6), .out_7(bcd_4_39_out_7), .out_8(bcd_4_39_out_8));
  BCD_4 bcd_4_40 (
    .E1(bcd_4_39_out_6), .E2(bcd_4_39_out_7), .E3(bcd_4_39_out_8), .E4(bcd_4_41_out_5),
    .out_5(bcd_4_40_out_5), .out_6(bcd_4_40_out_6), .out_7(bcd_4_40_out_7), .out_8(bcd_4_40_out_8));
  BCD_4 bcd_4_41 (
    .E1(bcd_4_32_out_6), .E2(bcd_4_32_out_7), .E3(bcd_4_32_out_8), .E4(bcd_4_34_out_5),
    .out_5(bcd_4_41_out_5), .out_6(bcd_4_41_out_6), .out_7(bcd_4_41_out_7), .out_8(bcd_4_41_out_8));
  BCD_4 bcd_4_42 (
    .E1(bcd_4_41_out_6), .E2(bcd_4_41_out_7), .E3(bcd_4_41_out_8), .E4(bcd_4_43_out_5),
    .out_5(bcd_4_42_out_5), .out_6(bcd_4_42_out_6), .out_7(bcd_4_42_out_7), .out_8(bcd_4_42_out_8));
  BCD_4 bcd_4_43 (
    .E1(bcd_4_34_out_6), .E2(bcd_4_34_out_7), .E3(bcd_4_34_out_8), .E4(in_17), .out_5(bcd_4_43_out_5),
    .out_6(bcd_4_43_out_6), .out_7(bcd_4_43_out_7), .out_8(bcd_4_43_out_8));
  BCD_4 bcd_4_44 (
    .E1(bcd_4_43_out_6), .E2(bcd_4_43_out_7), .E3(bcd_4_43_out_8), .E4(in_18), .out_5(bcd_4_44_out_5),
    .out_6(bcd_4_44_out_6), .out_7(bcd_4_44_out_7), .out_8(bcd_4_44_out_8));
  BCD_3 bcd_3_6 (
    .E1(bcd_3_5_r1), .E2(bcd_4_35_out_5), .E3(bcd_4_36_out_5), .R1(out_21), .R2(bcd_3_6_r2), .R3(bcd_3_6_r3),
    .R4(bcd_3_6_r4));
  BCD_4 bcd_4_45 (
    .E1(bcd_3_6_r2), .E2(bcd_3_6_r3), .E3(bcd_3_6_r4), .E4(bcd_4_46_out_5), .out_5(out_22), .out_6(out_23),
    .out_7(out_24), .out_8(out_25));
  BCD_4 bcd_4_46 (
    .E1(bcd_4_36_out_6), .E2(bcd_4_36_out_7), .E3(bcd_4_36_out_8), .E4(bcd_4_37_out_5),
    .out_5(bcd_4_46_out_5), .out_6(bcd_4_46_out_6), .out_7(bcd_4_46_out_7), .out_8(bcd_4_46_out_8));
  BCD_4 bcd_4_47 (
    .E1(bcd_4_46_out_6), .E2(bcd_4_46_out_7), .E3(bcd_4_46_out_8), .E4(bcd_4_38_out_5), .out_5(out_26),
    .out_6(out_27), .out_7(out_28), .out_8(out_29));
  BCD_4 bcd_4_48 (
    .E1(bcd_4_38_out_6), .E2(bcd_4_38_out_7), .E3(bcd_4_38_out_8), .E4(bcd_4_40_out_5), .out_5(out_30),
    .out_6(out_31), .out_7(out_32), .out_8(out_33));
  BCD_4 bcd_4_49 (
    .E1(bcd_4_40_out_6), .E2(bcd_4_40_out_7), .E3(bcd_4_40_out_8), .E4(bcd_4_42_out_5), .out_5(out_34),
    .out_6(out_35), .out_7(out_36), .out_8(out_37));
  BCD_4 bcd_4_50 (
    .E1(bcd_4_42_out_6), .E2(bcd_4_42_out_7), .E3(bcd_4_42_out_8), .E4(bcd_4_44_out_5), .out_5(out_38),
    .out_6(out_39), .out_7(out_40), .out_8(out_41));
  BCD_4 bcd_4_51 (
    .E1(bcd_4_44_out_6), .E2(bcd_4_44_out_7), .E3(bcd_4_44_out_8), .E4(in_19), .out_5(out_42),
    .out_6(out_43), .out_7(out_44), .out_8(out_45));

  assign out_46 = in_20;
endmodule

module Display_Hexadecimal (
  input  in_1,
  input  in_2,
  input  in_3,
  input  in_4,
  input  in_5,
  input  in_6,
  input  in_7,
  input  in_8,
  input  in_9,
  input  in_10,
  input  in_11,
  input  in_12,
  input  in_13,
  input  in_14,
  input  in_15,
  input  in_16,
  input  in_17,
  input  in_18,
  input  in_19,
  input  in_20,
  input  in_21,
  input  in_22,
  output out_23,
  output out_24,
  output out_25,
  output out_26,
  output out_27,
  output out_28,
  output out_29,
  output out_30,
  output out_31,
  output out_32,
  output out_33,
  output out_34,
  output out_35,
  output out_36,
  output out_37,
  output out_38,
  output out_39,
  output out_40,
  output out_41,
  output out_42,
  output out_43,
  output out_44,
  output out_45,
  output out_46,
  output out_47,
  output out_48,
  output out_49,
  output out_50,
  output out_51,
  output out_52,
  output out_53,
  output out_54,
  output out_55,
  output out_56,
  output out_57,
  output out_58,
  output out_59,
  output out_60,
  output out_61,
  output out_62,
  output out_63,
  output out_64,
  output out_65,
  output out_66,
  output out_67,
  output out_68,
  output out_69,
  output out_70,
  output out_71
);

  wire and_1_out, and_2_out, and_3_out, and_4_out, and_5_out, and_6_out, and_7_out, and_8_out, and_9_out,
       and_10_out, and_11_out, and_12_out, and_13_out, and_14_out, and_15_out, and_16_out, and_17_out,
       and_18_out, and_19_out, and_20_out, display_4_entradas_1_a, display_4_entradas_1_b,
       display_4_entradas_1_c, display_4_entradas_1_d, display_4_entradas_1_e, display_4_entradas_1_f,
       display_4_entradas_1_g, display_4_entradas_2_a, display_4_entradas_2_b, display_4_entradas_2_c,
       display_4_entradas_2_d, display_4_entradas_2_e, display_4_entradas_2_f, display_4_entradas_2_g,
       display_4_entradas_3_a, display_4_entradas_3_b, display_4_entradas_3_c, display_4_entradas_3_d,
       display_4_entradas_3_e, display_4_entradas_3_f, display_4_entradas_3_g, display_4_entradas_4_a,
       display_4_entradas_4_b, display_4_entradas_4_c, display_4_entradas_4_d, display_4_entradas_4_e,
       display_4_entradas_4_f, display_4_entradas_4_g, display_4_entradas_5_a, display_4_entradas_5_b,
       display_4_entradas_5_c, display_4_entradas_5_d, display_4_entradas_5_e, display_4_entradas_5_f,
       display_4_entradas_5_g, not_1_out, not_2_out;

  not not_1 (not_1_out, in_21);
  not not_2 (not_2_out, in_22);
  and and_1 (and_1_out, in_1, not_2_out, not_1_out);
  and and_2 (and_2_out, in_2, not_2_out, not_1_out);
  and and_3 (and_3_out, in_3, not_2_out, not_1_out);
  and and_4 (and_4_out, in_4, not_2_out, not_1_out);
  and and_5 (and_5_out, in_5, not_2_out, not_1_out);
  and and_6 (and_6_out, in_6, not_2_out, not_1_out);
  and and_7 (and_7_out, in_7, not_2_out, not_1_out);
  and and_8 (and_8_out, in_8, not_2_out, not_1_out);
  and and_9 (and_9_out, in_9, not_2_out, not_1_out);
  and and_10 (and_10_out, in_10, not_2_out, not_1_out);
  and and_11 (and_11_out, in_11, not_2_out, not_1_out);
  and and_12 (and_12_out, in_12, not_2_out, not_1_out);
  and and_13 (and_13_out, in_13, not_2_out, not_1_out);
  and and_14 (and_14_out, in_14, not_2_out, not_1_out);
  and and_15 (and_15_out, in_15, not_2_out, not_1_out);
  and and_16 (and_16_out, in_16, not_2_out, not_1_out);
  and and_17 (and_17_out, in_17, not_2_out, not_1_out);
  and and_18 (and_18_out, in_18, not_2_out, not_1_out);
  and and_19 (and_19_out, in_19, not_2_out, not_1_out);
  and and_20 (and_20_out, in_20, not_2_out, not_1_out);
  Display_4_Entradas display_4_entradas_1 (
    .E1(and_1_out), .E2(and_2_out), .E3(and_3_out), .E4(and_4_out), .a(display_4_entradas_1_a),
    .b(display_4_entradas_1_b), .c(display_4_entradas_1_c), .d(display_4_entradas_1_d),
    .e(display_4_entradas_1_e), .f(display_4_entradas_1_f), .g(display_4_entradas_1_g));
  Display_4_Entradas display_4_entradas_2 (
    .E1(and_5_out), .E2(and_6_out), .E3(and_7_out), .E4(and_8_out), .a(display_4_entradas_2_a),
    .b(display_4_entradas_2_b), .c(display_4_entradas_2_c), .d(display_4_entradas_2_d),
    .e(display_4_entradas_2_e), .f(display_4_entradas_2_f), .g(display_4_entradas_2_g));
  Display_4_Entradas display_4_entradas_3 (
    .E1(and_9_out), .E2(and_10_out), .E3(and_11_out), .E4(and_12_out), .a(display_4_entradas_3_a),
    .b(display_4_entradas_3_b), .c(display_4_entradas_3_c), .d(display_4_entradas_3_d),
    .e(display_4_entradas_3_e), .f(display_4_entradas_3_f), .g(display_4_entradas_3_g));
  Display_4_Entradas display_4_entradas_4 (
    .E1(and_13_out), .E2(and_14_out), .E3(and_15_out), .E4(and_16_out), .a(display_4_entradas_4_a),
    .b(display_4_entradas_4_b), .c(display_4_entradas_4_c), .d(display_4_entradas_4_d),
    .e(display_4_entradas_4_e), .f(display_4_entradas_4_f), .g(display_4_entradas_4_g));
  Display_4_Entradas display_4_entradas_5 (
    .E1(and_17_out), .E2(and_18_out), .E3(and_19_out), .E4(and_20_out), .a(display_4_entradas_5_a),
    .b(display_4_entradas_5_b), .c(display_4_entradas_5_c), .d(display_4_entradas_5_d),
    .e(display_4_entradas_5_e), .f(display_4_entradas_5_f), .g(display_4_entradas_5_g));
  and and_21 (out_23, 1'b1, not_2_out, not_1_out);
  and and_22 (out_24, 1'b1, not_2_out, not_1_out);
  and and_23 (out_25, 1'b1, not_2_out, not_1_out);
  and and_24 (out_26, 1'b1, not_2_out, not_1_out);
  and and_25 (out_27, 1'b1, not_2_out, not_1_out);
  and and_26 (out_28, 1'b1, not_2_out, not_1_out);
  and and_27 (out_29, 1'b0, not_2_out, not_1_out);
  and and_28 (out_30, 1'b1, not_2_out, not_1_out);
  and and_29 (out_31, 1'b1, not_2_out, not_1_out);
  and and_30 (out_32, 1'b1, not_2_out, not_1_out);
  and and_31 (out_33, 1'b1, not_2_out, not_1_out);
  and and_32 (out_34, 1'b1, not_2_out, not_1_out);
  and and_33 (out_35, 1'b1, not_2_out, not_1_out);
  and and_34 (out_36, 1'b0, not_2_out, not_1_out);
  and and_35 (out_37, display_4_entradas_1_a, not_2_out, not_1_out);
  and and_36 (out_38, display_4_entradas_1_b, not_2_out, not_1_out);
  and and_37 (out_39, display_4_entradas_1_c, not_2_out, not_1_out);
  and and_38 (out_40, display_4_entradas_1_d, not_2_out, not_1_out);
  and and_39 (out_41, display_4_entradas_1_e, not_2_out, not_1_out);
  and and_40 (out_42, display_4_entradas_1_f, not_2_out, not_1_out);
  and and_41 (out_43, display_4_entradas_1_g, not_2_out, not_1_out);
  and and_42 (out_44, display_4_entradas_2_a, not_2_out, not_1_out);
  and and_43 (out_45, display_4_entradas_2_b, not_2_out, not_1_out);
  and and_44 (out_46, display_4_entradas_2_c, not_2_out, not_1_out);
  and and_45 (out_47, display_4_entradas_2_d, not_2_out, not_1_out);
  and and_46 (out_48, display_4_entradas_2_e, not_2_out, not_1_out);
  and and_47 (out_49, display_4_entradas_2_f, not_2_out, not_1_out);
  and and_48 (out_50, display_4_entradas_2_g, not_2_out, not_1_out);
  and and_49 (out_51, display_4_entradas_3_a, not_2_out, not_1_out);
  and and_50 (out_52, display_4_entradas_3_b, not_2_out, not_1_out);
  and and_51 (out_53, display_4_entradas_3_c, not_2_out, not_1_out);
  and and_52 (out_54, display_4_entradas_3_d, not_2_out, not_1_out);
  and and_53 (out_55, display_4_entradas_3_e, not_2_out, not_1_out);
  and and_54 (out_56, display_4_entradas_3_f, not_2_out, not_1_out);
  and and_55 (out_57, display_4_entradas_3_g, not_2_out, not_1_out);
  and and_56 (out_58, display_4_entradas_4_a, not_2_out, not_1_out);
  and and_57 (out_59, display_4_entradas_4_b, not_2_out, not_1_out);
  and and_58 (out_60, display_4_entradas_4_c, not_2_out, not_1_out);
  and and_59 (out_61, display_4_entradas_4_d, not_2_out, not_1_out);
  and and_60 (out_62, display_4_entradas_4_e, not_2_out, not_1_out);
  and and_61 (out_63, display_4_entradas_4_f, not_2_out, not_1_out);
  and and_62 (out_64, display_4_entradas_4_g, not_2_out, not_1_out);
  and and_63 (out_65, display_4_entradas_5_a, not_2_out, not_1_out);
  and and_64 (out_66, display_4_entradas_5_b, not_2_out, not_1_out);
  and and_65 (out_67, display_4_entradas_5_c, not_2_out, not_1_out);
  and and_66 (out_68, display_4_entradas_5_d, not_2_out, not_1_out);
  and and_67 (out_69, display_4_entradas_5_e, not_2_out, not_1_out);
  and and_68 (out_70, display_4_entradas_5_f, not_2_out, not_1_out);
  and and_69 (out_71, display_4_entradas_5_g, not_2_out, not_1_out);
endmodule

module Display_Decimal (
  input  in_1,
  input  in_2,
  input  in_3,
  input  in_4,
  input  in_5,
  input  in_6,
  input  in_7,
  input  in_8,
  input  in_9,
  input  in_10,
  input  in_11,
  input  in_12,
  input  in_13,
  input  in_14,
  input  in_15,
  input  in_16,
  input  in_17,
  input  in_18,
  input  in_19,
  input  in_20,
  input  in_21,
  input  in_22,
  output out_23,
  output out_24,
  output out_25,
  output out_26,
  output out_27,
  output out_28,
  output out_29,
  output out_30,
  output out_31,
  output out_32,
  output out_33,
  output out_34,
  output out_35,
  output out_36,
  output out_37,
  output out_38,
  output out_39,
  output out_40,
  output out_41,
  output out_42,
  output out_43,
  output out_44,
  output out_45,
  output out_46,
  output out_47,
  output out_48,
  output out_49,
  output out_50,
  output out_51,
  output out_52,
  output out_53,
  output out_54,
  output out_55,
  output out_56,
  output out_57,
  output out_58,
  output out_59,
  output out_60,
  output out_61,
  output out_62,
  output out_63,
  output out_64,
  output out_65,
  output out_66,
  output out_67,
  output out_68,
  output out_69,
  output out_70,
  output out_71
);

  wire and_1_out, and_2_out, and_3_out, and_4_out, and_5_out, and_6_out, and_7_out, and_8_out, and_9_out,
       and_10_out, and_11_out, and_12_out, and_13_out, and_14_out, and_15_out, and_16_out, and_17_out,
       and_18_out, and_19_out, and_20_out, and_21_out, and_22_out, and_23_out, and_24_out, and_25_out,
       and_26_out, binario_a_bcd_1_out_21, binario_a_bcd_1_out_22, binario_a_bcd_1_out_23,
       binario_a_bcd_1_out_24, binario_a_bcd_1_out_25, binario_a_bcd_1_out_26, binario_a_bcd_1_out_27,
       binario_a_bcd_1_out_28, binario_a_bcd_1_out_29, binario_a_bcd_1_out_30, binario_a_bcd_1_out_31,
       binario_a_bcd_1_out_32, binario_a_bcd_1_out_33, binario_a_bcd_1_out_34, binario_a_bcd_1_out_35,
       binario_a_bcd_1_out_36, binario_a_bcd_1_out_37, binario_a_bcd_1_out_38, binario_a_bcd_1_out_39,
       binario_a_bcd_1_out_40, binario_a_bcd_1_out_41, binario_a_bcd_1_out_42, binario_a_bcd_1_out_43,
       binario_a_bcd_1_out_44, binario_a_bcd_1_out_45, binario_a_bcd_1_out_46, display_4_entradas_1_a,
       display_4_entradas_1_b, display_4_entradas_1_c, display_4_entradas_1_d, display_4_entradas_1_e,
       display_4_entradas_1_f, display_4_entradas_1_g, display_4_entradas_2_a, display_4_entradas_2_b,
       display_4_entradas_2_c, display_4_entradas_2_d, display_4_entradas_2_e, display_4_entradas_2_f,
       display_4_entradas_2_g, display_4_entradas_3_a, display_4_entradas_3_b, display_4_entradas_3_c,
       display_4_entradas_3_d, display_4_entradas_3_e, display_4_entradas_3_f, display_4_entradas_3_g,
       display_4_entradas_4_a, display_4_entradas_4_b, display_4_entradas_4_c, display_4_entradas_4_d,
       display_4_entradas_4_e, display_4_entradas_4_f, display_4_entradas_4_g, display_4_entradas_5_a,
       display_4_entradas_5_b, display_4_entradas_5_c, display_4_entradas_5_d, display_4_entradas_5_e,
       display_4_entradas_5_f, display_4_entradas_5_g, display_4_entradas_6_a, display_4_entradas_6_b,
       display_4_entradas_6_c, display_4_entradas_6_d, display_4_entradas_6_e, display_4_entradas_6_f,
       display_4_entradas_6_g, display_4_entradas_7_a, display_4_entradas_7_b, display_4_entradas_7_c,
       display_4_entradas_7_d, display_4_entradas_7_e, display_4_entradas_7_f, display_4_entradas_7_g,
       not_1_out;

  Binario_a_BCD binario_a_bcd_1 (
    .in_1(in_1), .in_2(in_2), .in_3(in_3), .in_4(in_4), .in_5(in_5), .in_6(in_6), .in_7(in_7), .in_8(in_8),
    .in_9(in_9), .in_10(in_10), .in_11(in_11), .in_12(in_12), .in_13(in_13), .in_14(in_14), .in_15(in_15),
    .in_16(in_16), .in_17(in_17), .in_18(in_18), .in_19(in_19), .in_20(in_20),
    .out_21(binario_a_bcd_1_out_21), .out_22(binario_a_bcd_1_out_22), .out_23(binario_a_bcd_1_out_23),
    .out_24(binario_a_bcd_1_out_24), .out_25(binario_a_bcd_1_out_25), .out_26(binario_a_bcd_1_out_26),
    .out_27(binario_a_bcd_1_out_27), .out_28(binario_a_bcd_1_out_28), .out_29(binario_a_bcd_1_out_29),
    .out_30(binario_a_bcd_1_out_30), .out_31(binario_a_bcd_1_out_31), .out_32(binario_a_bcd_1_out_32),
    .out_33(binario_a_bcd_1_out_33), .out_34(binario_a_bcd_1_out_34), .out_35(binario_a_bcd_1_out_35),
    .out_36(binario_a_bcd_1_out_36), .out_37(binario_a_bcd_1_out_37), .out_38(binario_a_bcd_1_out_38),
    .out_39(binario_a_bcd_1_out_39), .out_40(binario_a_bcd_1_out_40), .out_41(binario_a_bcd_1_out_41),
    .out_42(binario_a_bcd_1_out_42), .out_43(binario_a_bcd_1_out_43), .out_44(binario_a_bcd_1_out_44),
    .out_45(binario_a_bcd_1_out_45), .out_46(binario_a_bcd_1_out_46));
  not not_1 (not_1_out, in_22);
  and and_1 (and_1_out, binario_a_bcd_1_out_21, not_1_out, in_21);
  and and_2 (and_2_out, binario_a_bcd_1_out_22, not_1_out, in_21);
  and and_3 (and_3_out, binario_a_bcd_1_out_23, not_1_out, in_21);
  and and_4 (and_4_out, binario_a_bcd_1_out_24, not_1_out, in_21);
  and and_5 (and_5_out, binario_a_bcd_1_out_25, not_1_out, in_21);
  and and_6 (and_6_out, binario_a_bcd_1_out_26, not_1_out, in_21);
  and and_7 (and_7_out, binario_a_bcd_1_out_27, not_1_out, in_21);
  and and_8 (and_8_out, binario_a_bcd_1_out_28, not_1_out, in_21);
  and and_9 (and_9_out, binario_a_bcd_1_out_29, not_1_out, in_21);
  and and_10 (and_10_out, binario_a_bcd_1_out_30, not_1_out, in_21);
  and and_11 (and_11_out, binario_a_bcd_1_out_31, not_1_out, in_21);
  and and_12 (and_12_out, binario_a_bcd_1_out_32, not_1_out, in_21);
  and and_13 (and_13_out, binario_a_bcd_1_out_33, not_1_out, in_21);
  and and_14 (and_14_out, binario_a_bcd_1_out_34, not_1_out, in_21);
  and and_15 (and_15_out, binario_a_bcd_1_out_35, not_1_out, in_21);
  and and_16 (and_16_out, binario_a_bcd_1_out_36, not_1_out, in_21);
  and and_17 (and_17_out, binario_a_bcd_1_out_37, not_1_out, in_21);
  and and_18 (and_18_out, binario_a_bcd_1_out_38, not_1_out, in_21);
  and and_19 (and_19_out, binario_a_bcd_1_out_39, not_1_out, in_21);
  and and_20 (and_20_out, binario_a_bcd_1_out_40, not_1_out, in_21);
  and and_21 (and_21_out, binario_a_bcd_1_out_41, not_1_out, in_21);
  and and_22 (and_22_out, binario_a_bcd_1_out_42, not_1_out, in_21);
  and and_23 (and_23_out, binario_a_bcd_1_out_43, not_1_out, in_21);
  and and_24 (and_24_out, binario_a_bcd_1_out_44, not_1_out, in_21);
  and and_25 (and_25_out, binario_a_bcd_1_out_45, not_1_out, in_21);
  and and_26 (and_26_out, binario_a_bcd_1_out_46, not_1_out, in_21);
  Display_4_Entradas display_4_entradas_1 (
    .E1(and_7_out), .E2(and_8_out), .E3(and_9_out), .E4(and_10_out), .a(display_4_entradas_1_a),
    .b(display_4_entradas_1_b), .c(display_4_entradas_1_c), .d(display_4_entradas_1_d),
    .e(display_4_entradas_1_e), .f(display_4_entradas_1_f), .g(display_4_entradas_1_g));
  Display_4_Entradas display_4_entradas_2 (
    .E1(and_11_out), .E2(and_12_out), .E3(and_13_out), .E4(and_14_out), .a(display_4_entradas_2_a),
    .b(display_4_entradas_2_b), .c(display_4_entradas_2_c), .d(display_4_entradas_2_d),
    .e(display_4_entradas_2_e), .f(display_4_entradas_2_f), .g(display_4_entradas_2_g));
  Display_4_Entradas display_4_entradas_3 (
    .E1(1'b0), .E2(1'b0), .E3(and_1_out), .E4(and_2_out), .a(display_4_entradas_3_a),
    .b(display_4_entradas_3_b), .c(display_4_entradas_3_c), .d(display_4_entradas_3_d),
    .e(display_4_entradas_3_e), .f(display_4_entradas_3_f), .g(display_4_entradas_3_g));
  Display_4_Entradas display_4_entradas_4 (
    .E1(and_3_out), .E2(and_4_out), .E3(and_5_out), .E4(and_6_out), .a(display_4_entradas_4_a),
    .b(display_4_entradas_4_b), .c(display_4_entradas_4_c), .d(display_4_entradas_4_d),
    .e(display_4_entradas_4_e), .f(display_4_entradas_4_f), .g(display_4_entradas_4_g));
  Display_4_Entradas display_4_entradas_5 (
    .E1(and_15_out), .E2(and_16_out), .E3(and_17_out), .E4(and_18_out), .a(display_4_entradas_5_a),
    .b(display_4_entradas_5_b), .c(display_4_entradas_5_c), .d(display_4_entradas_5_d),
    .e(display_4_entradas_5_e), .f(display_4_entradas_5_f), .g(display_4_entradas_5_g));
  Display_4_Entradas display_4_entradas_6 (
    .E1(and_19_out), .E2(and_20_out), .E3(and_21_out), .E4(and_22_out), .a(display_4_entradas_6_a),
    .b(display_4_entradas_6_b), .c(display_4_entradas_6_c), .d(display_4_entradas_6_d),
    .e(display_4_entradas_6_e), .f(display_4_entradas_6_f), .g(display_4_entradas_6_g));
  Display_4_Entradas display_4_entradas_7 (
    .E1(and_23_out), .E2(and_24_out), .E3(and_25_out), .E4(and_26_out), .a(display_4_entradas_7_a),
    .b(display_4_entradas_7_b), .c(display_4_entradas_7_c), .d(display_4_entradas_7_d),
    .e(display_4_entradas_7_e), .f(display_4_entradas_7_f), .g(display_4_entradas_7_g));
  and and_27 (out_23, display_4_entradas_3_a, not_1_out, in_21);
  and and_28 (out_24, display_4_entradas_3_b, not_1_out, in_21);
  and and_29 (out_25, display_4_entradas_3_c, not_1_out, in_21);
  and and_30 (out_26, display_4_entradas_3_d, not_1_out, in_21);
  and and_31 (out_27, display_4_entradas_3_e, not_1_out, in_21);
  and and_32 (out_28, display_4_entradas_3_f, not_1_out, in_21);
  and and_33 (out_29, display_4_entradas_3_g, not_1_out, in_21);
  and and_34 (out_30, display_4_entradas_4_a, not_1_out, in_21);
  and and_35 (out_31, display_4_entradas_4_b, not_1_out, in_21);
  and and_36 (out_32, display_4_entradas_4_c, not_1_out, in_21);
  and and_37 (out_33, display_4_entradas_4_d, not_1_out, in_21);
  and and_38 (out_34, display_4_entradas_4_e, not_1_out, in_21);
  and and_39 (out_35, display_4_entradas_4_f, not_1_out, in_21);
  and and_40 (out_36, display_4_entradas_4_g, not_1_out, in_21);
  and and_41 (out_37, display_4_entradas_1_a, not_1_out, in_21);
  and and_42 (out_38, display_4_entradas_1_b, not_1_out, in_21);
  and and_43 (out_39, display_4_entradas_1_c, not_1_out, in_21);
  and and_44 (out_40, display_4_entradas_1_d, not_1_out, in_21);
  and and_45 (out_41, display_4_entradas_1_e, not_1_out, in_21);
  and and_46 (out_42, display_4_entradas_1_f, not_1_out, in_21);
  and and_47 (out_43, display_4_entradas_1_g, not_1_out, in_21);
  and and_48 (out_44, display_4_entradas_2_a, not_1_out, in_21);
  and and_49 (out_45, display_4_entradas_2_b, not_1_out, in_21);
  and and_50 (out_46, display_4_entradas_2_c, not_1_out, in_21);
  and and_51 (out_47, display_4_entradas_2_d, not_1_out, in_21);
  and and_52 (out_48, display_4_entradas_2_e, not_1_out, in_21);
  and and_53 (out_49, display_4_entradas_2_f, not_1_out, in_21);
  and and_54 (out_50, display_4_entradas_2_g, not_1_out, in_21);
  and and_55 (out_51, display_4_entradas_5_a, not_1_out, in_21);
  and and_56 (out_52, display_4_entradas_5_b, not_1_out, in_21);
  and and_57 (out_53, display_4_entradas_5_c, not_1_out, in_21);
  and and_58 (out_54, display_4_entradas_5_d, not_1_out, in_21);
  and and_59 (out_55, display_4_entradas_5_e, not_1_out, in_21);
  and and_60 (out_56, display_4_entradas_5_f, not_1_out, in_21);
  and and_61 (out_57, display_4_entradas_5_g, not_1_out, in_21);
  and and_62 (out_58, display_4_entradas_6_a, not_1_out, in_21);
  and and_63 (out_59, display_4_entradas_6_b, not_1_out, in_21);
  and and_64 (out_60, display_4_entradas_6_c, not_1_out, in_21);
  and and_65 (out_61, display_4_entradas_6_d, not_1_out, in_21);
  and and_66 (out_62, display_4_entradas_6_e, not_1_out, in_21);
  and and_67 (out_63, display_4_entradas_6_f, not_1_out, in_21);
  and and_68 (out_64, display_4_entradas_6_g, not_1_out, in_21);
  and and_69 (out_65, display_4_entradas_7_a, not_1_out, in_21);
  and and_70 (out_66, display_4_entradas_7_b, not_1_out, in_21);
  and and_71 (out_67, display_4_entradas_7_c, not_1_out, in_21);
  and and_72 (out_68, display_4_entradas_7_d, not_1_out, in_21);
  and and_73 (out_69, display_4_entradas_7_e, not_1_out, in_21);
  and and_74 (out_70, display_4_entradas_7_f, not_1_out, in_21);
  and and_75 (out_71, display_4_entradas_7_g, not_1_out, in_21);
endmodule

module Display_Octal (
  input  in_1,
  input  in_2,
  input  in_3,
  input  in_4,
  input  in_5,
  input  in_6,
  input  in_7,
  input  in_8,
  input  in_9,
  input  in_10,
  input  in_11,
  input  in_12,
  input  in_13,
  input  in_14,
  input  in_15,
  input  in_16,
  input  in_17,
  input  in_18,
  input  in_19,
  input  in_20,
  input  in_21,
  input  in_22,
  output out_23,
  output out_24,
  output out_25,
  output out_26,
  output out_27,
  output out_28,
  output out_29,
  output out_30,
  output out_31,
  output out_32,
  output out_33,
  output out_34,
  output out_35,
  output out_36,
  output out_37,
  output out_38,
  output out_39,
  output out_40,
  output out_41,
  output out_42,
  output out_43,
  output out_44,
  output out_45,
  output out_46,
  output out_47,
  output out_48,
  output out_49,
  output out_50,
  output out_51,
  output out_52,
  output out_53,
  output out_54,
  output out_55,
  output out_56,
  output out_57,
  output out_58,
  output out_59,
  output out_60,
  output out_61,
  output out_62,
  output out_63,
  output out_64,
  output out_65,
  output out_66,
  output out_67,
  output out_68,
  output out_69,
  output out_70,
  output out_71
);

  wire and_1_out, and_2_out, and_3_out, and_4_out, and_5_out, and_6_out, and_7_out, and_8_out, and_9_out,
       and_10_out, and_11_out, and_12_out, and_13_out, and_14_out, and_15_out, and_16_out, and_17_out,
       and_18_out, and_19_out, and_20_out, display_3_entradas_1_a, display_3_entradas_1_b,
       display_3_entradas_1_c, display_3_entradas_1_d, display_3_entradas_1_e, display_3_entradas_1_f,
       display_3_entradas_1_g, display_3_entradas_2_a, display_3_entradas_2_b, display_3_entradas_2_c,
       display_3_entradas_2_d, display_3_entradas_2_e, display_3_entradas_2_f, display_3_entradas_2_g,
       display_3_entradas_3_a, display_3_entradas_3_b, display_3_entradas_3_c, display_3_entradas_3_d,
       display_3_entradas_3_e, display_3_entradas_3_f, display_3_entradas_3_g, display_3_entradas_4_a,
       display_3_entradas_4_b, display_3_entradas_4_c, display_3_entradas_4_d, display_3_entradas_4_e,
       display_3_entradas_4_f, display_3_entradas_4_g, display_3_entradas_5_a, display_3_entradas_5_b,
       display_3_entradas_5_c, display_3_entradas_5_d, display_3_entradas_5_e, display_3_entradas_5_f,
       display_3_entradas_5_g, display_3_entradas_6_a, display_3_entradas_6_b, display_3_entradas_6_c,
       display_3_entradas_6_d, display_3_entradas_6_e, display_3_entradas_6_f, display_3_entradas_6_g,
       display_3_entradas_7_a, display_3_entradas_7_b, display_3_entradas_7_c, display_3_entradas_7_d,
       display_3_entradas_7_e, display_3_entradas_7_f, display_3_entradas_7_g;

  and and_1 (and_1_out, in_1, in_22, in_21);
  and and_2 (and_2_out, in_2, in_22, in_21);
  and and_3 (and_3_out, in_3, in_22, in_21);
  and and_4 (and_4_out, in_4, in_22, in_21);
  and and_5 (and_5_out, in_5, in_22, in_21);
  and and_6 (and_6_out, in_6, in_22, in_21);
  and and_7 (and_7_out, in_7, in_22, in_21);
  and and_8 (and_8_out, in_8, in_22, in_21);
  and and_9 (and_9_out, in_9, in_22, in_21);
  and and_10 (and_10_out, in_10, in_22, in_21);
  and and_11 (and_11_out, in_11, in_22, in_21);
  and and_12 (and_12_out, in_12, in_22, in_21);
  and and_13 (and_13_out, in_13, in_22, in_21);
  and and_14 (and_14_out, in_14, in_22, in_21);
  and and_15 (and_15_out, in_15, in_22, in_21);
  and and_16 (and_16_out, in_16, in_22, in_21);
  and and_17 (and_17_out, in_17, in_22, in_21);
  and and_18 (and_18_out, in_18, in_22, in_21);
  and and_19 (and_19_out, in_19, in_22, in_21);
  and and_20 (and_20_out, in_20, in_22, in_21);
  Display_3_Entradas display_3_entradas_1 (
    .E1(1'b0), .E2(and_1_out), .E3(and_2_out), .a(display_3_entradas_1_a), .b(display_3_entradas_1_b),
    .c(display_3_entradas_1_c), .d(display_3_entradas_1_d), .e(display_3_entradas_1_e),
    .f(display_3_entradas_1_f), .g(display_3_entradas_1_g));
  Display_3_Entradas display_3_entradas_2 (
    .E1(and_3_out), .E2(and_4_out), .E3(and_5_out), .a(display_3_entradas_2_a), .b(display_3_entradas_2_b),
    .c(display_3_entradas_2_c), .d(display_3_entradas_2_d), .e(display_3_entradas_2_e),
    .f(display_3_entradas_2_f), .g(display_3_entradas_2_g));
  Display_3_Entradas display_3_entradas_3 (
    .E1(and_6_out), .E2(and_7_out), .E3(and_8_out), .a(display_3_entradas_3_a), .b(display_3_entradas_3_b),
    .c(display_3_entradas_3_c), .d(display_3_entradas_3_d), .e(display_3_entradas_3_e),
    .f(display_3_entradas_3_f), .g(display_3_entradas_3_g));
  Display_3_Entradas display_3_entradas_4 (
    .E1(and_9_out), .E2(and_10_out), .E3(and_11_out), .a(display_3_entradas_4_a), .b(display_3_entradas_4_b),
    .c(display_3_entradas_4_c), .d(display_3_entradas_4_d), .e(display_3_entradas_4_e),
    .f(display_3_entradas_4_f), .g(display_3_entradas_4_g));
  Display_3_Entradas display_3_entradas_5 (
    .E1(and_12_out), .E2(and_13_out), .E3(and_14_out), .a(display_3_entradas_5_a),
    .b(display_3_entradas_5_b), .c(display_3_entradas_5_c), .d(display_3_entradas_5_d),
    .e(display_3_entradas_5_e), .f(display_3_entradas_5_f), .g(display_3_entradas_5_g));
  Display_3_Entradas display_3_entradas_6 (
    .E1(and_15_out), .E2(and_16_out), .E3(and_17_out), .a(display_3_entradas_6_a),
    .b(display_3_entradas_6_b), .c(display_3_entradas_6_c), .d(display_3_entradas_6_d),
    .e(display_3_entradas_6_e), .f(display_3_entradas_6_f), .g(display_3_entradas_6_g));
  Display_3_Entradas display_3_entradas_7 (
    .E1(and_18_out), .E2(and_19_out), .E3(and_20_out), .a(display_3_entradas_7_a),
    .b(display_3_entradas_7_b), .c(display_3_entradas_7_c), .d(display_3_entradas_7_d),
    .e(display_3_entradas_7_e), .f(display_3_entradas_7_f), .g(display_3_entradas_7_g));
  and and_21 (out_23, display_3_entradas_1_a, in_22, in_21);
  and and_22 (out_24, display_3_entradas_1_b, in_22, in_21);
  and and_23 (out_25, display_3_entradas_1_c, in_22, in_21);
  and and_24 (out_26, display_3_entradas_1_d, in_22, in_21);
  and and_25 (out_27, display_3_entradas_1_e, in_22, in_21);
  and and_26 (out_28, display_3_entradas_1_f, in_22, in_21);
  and and_27 (out_29, display_3_entradas_1_g, in_22, in_21);
  and and_28 (out_30, display_3_entradas_2_a, in_22, in_21);
  and and_29 (out_31, display_3_entradas_2_b, in_22, in_21);
  and and_30 (out_32, display_3_entradas_2_c, in_22, in_21);
  and and_31 (out_33, display_3_entradas_2_d, in_22, in_21);
  and and_32 (out_34, display_3_entradas_2_e, in_22, in_21);
  and and_33 (out_35, display_3_entradas_2_f, in_22, in_21);
  and and_34 (out_36, display_3_entradas_2_g, in_22, in_21);
  and and_35 (out_37, display_3_entradas_3_a, in_22, in_21);
  and and_36 (out_38, display_3_entradas_3_b, in_22, in_21);
  and and_37 (out_39, display_3_entradas_3_c, in_22, in_21);
  and and_38 (out_40, display_3_entradas_3_d, in_22, in_21);
  and and_39 (out_41, display_3_entradas_3_e, in_22, in_21);
  and and_40 (out_42, display_3_entradas_3_f, in_22, in_21);
  and and_41 (out_43, display_3_entradas_3_g, in_22, in_21);
  and and_42 (out_44, display_3_entradas_4_a, in_22, in_21);
  and and_43 (out_45, display_3_entradas_4_b, in_22, in_21);
  and and_44 (out_46, display_3_entradas_4_c, in_22, in_21);
  and and_45 (out_47, display_3_entradas_4_d, in_22, in_21);
  and and_46 (out_48, display_3_entradas_4_e, in_22, in_21);
  and and_47 (out_49, display_3_entradas_4_f, in_22, in_21);
  and and_48 (out_50, display_3_entradas_4_g, in_22, in_21);
  and and_49 (out_51, display_3_entradas_5_a, in_22, in_21);
  and and_50 (out_52, display_3_entradas_5_b, in_22, in_21);
  and and_51 (out_53, display_3_entradas_5_c, in_22, in_21);
  and and_52 (out_54, display_3_entradas_5_d, in_22, in_21);
  and and_53 (out_55, display_3_entradas_5_e, in_22, in_21);
  and and_54 (out_56, display_3_entradas_5_f, in_22, in_21);
  and and_55 (out_57, display_3_entradas_5_g, in_22, in_21);
  and and_56 (out_58, display_3_entradas_6_a, in_22, in_21);
  and and_57 (out_59, display_3_entradas_6_b, in_22, in_21);
  and and_58 (out_60, display_3_entradas_6_c, in_22, in_21);
  and and_59 (out_61, display_3_entradas_6_d, in_22, in_21);
  and and_60 (out_62, display_3_entradas_6_e, in_22, in_21);
  and and_61 (out_63, display_3_entradas_6_f, in_22, in_21);
  and and_62 (out_64, display_3_entradas_6_g, in_22, in_21);
  and and_63 (out_65, display_3_entradas_7_a, in_22, in_21);
  and and_64 (out_66, display_3_entradas_7_b, in_22, in_21);
  and and_65 (out_67, display_3_entradas_7_c, in_22, in_21);
  and and_66 (out_68, display_3_entradas_7_d, in_22, in_21);
  and and_67 (out_69, display_3_entradas_7_e, in_22, in_21);
  and and_68 (out_70, display_3_entradas_7_f, in_22, in_21);
  and and_69 (out_71, display_3_entradas_7_g, in_22, in_21);
endmodule
